// Digital circuit 4位寄存器.dig as structural Verilog
module \_4位寄存器  (
  input  [3:0] Din,
  input  clock,
  input  WE,
  input  OE,
  output [3:0] data,
  output [3:0] Output
);

  Register #(.Bits(4)) register_1 (.D(Din), .C(clock), .en(WE), .Q(data));
  assign Output = OE ? data : 4'bz;  // Driver driver_1
endmodule
