// Digital circuit 8位加法器.dig as structural Verilog
module \_8位加法器  (
  input  [7:0] A,
  input  [7:0] B,
  input  OE,
  input  C,
  output [7:0] Sum,
  output [7:0] data,
  output carray
);

  Add #(.Bits(8)) add_1 (.a(A), .b(B), .c_i(C), .s(data), .c_o(carray));
  assign Sum = OE ? data : 8'bz;  // Driver driver_1
endmodule
