// Digital circuit 8位寄存器.dig as structural Verilog
module \_8位寄存器  (
  input  [7:0] Din,
  input  clock,
  input  WE,
  input  OE,
  output [7:0] data,
  output [7:0] Output
);

  Register #(.Bits(8)) register_1 (.D(Din), .C(clock), .en(WE), .Q(data));
  assign Output = OE ? data : 8'bz;  // Driver driver_1
endmodule
