// Digital circuit Instruction-decoder.dig as structural Verilog
module Instruction_decoder (
  input  [31:0] PC_In,
  output [7:0] mechie_op,
  output [4:0] rd,
  output [4:0] rs1,
  output [4:0] rs2,
  output [6:0] imm_2531,
  output [19:0] imm_1231,
  output [11:0] imm_2032,
  output invalid,
  output [5:0] csr_op,
  output [8:0] jmp_op,
  output [9:0] salu_op,
  output [11:0] alu_op,
  output [9:0] SL_op
);

  wire _3bit_decoder_3__0, _3bit_decoder_3__5, _3bit_decoder_6__5, _3bit_decoder_7__0, and_1_out, and_2_out,
       decoder_1_out_1, decoder_1_out_2, decoder_1_out_3, decoder_1_out_5, decoder_1_out_7, decoder_1_out_8,
       decoder_1_out_11, nor_1_out, not_1_out, not_2_out, not_3_out, not_4_out;
  wire [3:0] lookuptable_1_out;

  LookUpTable #(.Bits(4)) lookuptable_1 (
    .in0(PC_In[0]), .in1(PC_In[1]), .in2(PC_In[2]), .in3(PC_In[3]), .in4(PC_In[4]), .in5(PC_In[5]),
    .in6(PC_In[6]), .out(lookuptable_1_out));
  Decoder #(.Selector_Bits(4)) decoder_1 (
    .sel(lookuptable_1_out), .out_0(invalid), .out_1(decoder_1_out_1), .out_2(decoder_1_out_2),
    .out_3(decoder_1_out_3), .out_4(jmp_op[1]), .out_5(decoder_1_out_5), .out_6(jmp_op[0]),
    .out_7(decoder_1_out_7), .out_8(decoder_1_out_8), .out_9(jmp_op[8]), .out_10(SL_op[0]),
    .out_11(decoder_1_out_11));  // open: out_12, out_13, out_14, out_15
  _3bit_decoder _3bit_decoder_1 (
    .EN(decoder_1_out_11), .Din(PC_In[14:12]), ._0(mechie_op[6]), ._1(mechie_op[7]), ._2(invalid),
    ._3(invalid), ._4(invalid), ._5(invalid), ._6(invalid), ._7(invalid));
  _3bit_decoder _3bit_decoder_2 (
    .EN(decoder_1_out_8), .Din(PC_In[14:12]), ._0(SL_op[7]), ._1(SL_op[8]), ._2(SL_op[9]), ._3(invalid),
    ._4(invalid), ._5(invalid), ._6(invalid), ._7(invalid));
  not not_1 (not_1_out, PC_In[30]);
  _3bit_decoder _3bit_decoder_3 (
    .EN(decoder_1_out_7), .Din(PC_In[14:12]), ._0(_3bit_decoder_3__0), ._1(alu_op[2]), ._2(alu_op[3]),
    ._3(alu_op[4]), ._4(alu_op[9]), ._5(_3bit_decoder_3__5), ._6(alu_op[10]), ._7(alu_op[11]));
  _3bit_decoder _3bit_decoder_4 (
    .EN(decoder_1_out_5), .Din(PC_In[14:12]), ._0(SL_op[1]), ._1(SL_op[2]), ._2(SL_op[3]), ._3(SL_op[4]),
    ._4(SL_op[5]), ._5(SL_op[6]), ._6(invalid), ._7(invalid));
  _3bit_decoder _3bit_decoder_5 (
    .EN(decoder_1_out_1), .Din(PC_In[14:12]), ._0(jmp_op[2]), ._1(jmp_op[3]), ._2(invalid), ._3(invalid),
    ._4(jmp_op[4]), ._5(jmp_op[5]), ._6(jmp_op[6]), ._7(jmp_op[7]));
  _3bit_decoder _3bit_decoder_6 (
    .EN(decoder_1_out_2), .Din(PC_In[14:12]), ._0(alu_op[5]), ._1(salu_op[5]), ._2(salu_op[6]),
    ._3(salu_op[7]), ._4(alu_op[6]), ._5(_3bit_decoder_6__5), ._6(alu_op[7]), ._7(alu_op[8]));
  _3bit_decoder _3bit_decoder_7 (
    .EN(decoder_1_out_3), .Din(PC_In[14:12]), ._0(_3bit_decoder_7__0), ._1(csr_op[0]), ._2(csr_op[1]),
    ._3(csr_op[2]), ._4(invalid), ._5(csr_op[3]), ._6(csr_op[4]), ._7(csr_op[5]));
  nor nor_1 (nor_1_out, PC_In[25], PC_In[26], PC_In[27], PC_In[28], PC_In[29], PC_In[30], PC_In[31], PC_In[21], PC_In[22], PC_In[23], PC_In[24]);
  not not_2 (not_2_out, PC_In[20]);
  and and_1 (and_1_out, nor_1_out, PC_In[20]);
  and and_2 (and_2_out, nor_1_out, not_2_out);
  assign alu_op[0] = _3bit_decoder_3__0 ? not_1_out : 1'bz;  // Driver driver_1
  assign alu_op[1] = _3bit_decoder_3__0 ? PC_In[30] : 1'bz;  // Driver driver_2
  PullDown pulldown_1 (.out(_3bit_decoder_3__0));
  PullDown pulldown_2 (.out(_3bit_decoder_3__5));
  PullDown pulldown_3 (.out(_3bit_decoder_6__5));
  assign mechie_op[0] = _3bit_decoder_7__0 ? and_1_out : 1'bz;  // Driver driver_3
  assign mechie_op[1] = _3bit_decoder_7__0 ? and_2_out : 1'bz;  // Driver driver_4
  not not_3 (not_3_out, PC_In[30]);
  not not_4 (not_4_out, PC_In[30]);
  PullDown pulldown_4 (.out(_3bit_decoder_7__0));
  PullDown #(.Bits(10)) pulldown_5 (.out(SL_op));
  assign salu_op[8] = _3bit_decoder_6__5 ? not_4_out : 1'bz;  // Driver driver_5
  assign salu_op[9] = _3bit_decoder_6__5 ? PC_In[30] : 1'bz;  // Driver driver_6
  PullDown #(.Bits(12)) pulldown_6 (.out(alu_op));
  assign salu_op[3] = _3bit_decoder_3__5 ? PC_In[30] : 1'bz;  // Driver driver_7
  assign salu_op[4] = _3bit_decoder_3__5 ? not_3_out : 1'bz;  // Driver driver_8
  PullDown #(.Bits(9)) pulldown_7 (.out(jmp_op));
  PullDown #(.Bits(10)) pulldown_8 (.out({salu_op[9:3], alu_op[4:2]}));
  PullDown #(.Bits(6)) pulldown_9 (.out(csr_op));
  PullDown #(.Bits(8)) pulldown_10 (.out(mechie_op));

  assign imm_1231 = PC_In[31:12];
  assign imm_2032 = PC_In[31:20];
  assign imm_2531 = PC_In[31:25];
  assign rd = PC_In[11:7];
  assign rs1 = PC_In[19:15];
  assign rs2 = PC_In[24:20];
  assign salu_op[2:0] = alu_op[4:2];

  // Other names for the same wires on the sheet: add = alu_op[0]; addi = alu_op[5]; and = alu_op[11];
  //   andi = alu_op[8]; auipc = jmp_op[8]; beq = jmp_op[2]; bge = jmp_op[5]; bgeu = jmp_op[7]; blt = jmp_op[4];
  //   bltu = jmp_op[6]; bne = jmp_op[3]; csrrc = csr_op[2]; csrrci = csr_op[5]; csrrs = csr_op[1]; csrrsi = csr_op[4];
  //   csrrw = csr_op[0]; csrrwi = csr_op[3]; ebreak = mechie_op[0]; ecall = mechie_op[1]; fence = mechie_op[6];
  //   fence_i = mechie_op[7]; invlid_op = invalid; jal = jmp_op[0]; jalr = jmp_op[1]; lb = SL_op[1]; lbu = SL_op[5];
  //   ld = SL_op[4]; lh = SL_op[2]; lhu = SL_op[6]; lui = SL_op[0]; lw = SL_op[3]; mret = mechie_op[2];
  //   or = alu_op[10]; ori = alu_op[7]; funct3[2:0] = PC_In[14:12]; imm_12_31[19:0] = PC_In[31:12];
  //   imm_20_31[11:0] = PC_In[31:20]; imm_25_31[6:0] = PC_In[31:25]; _30 = PC_In[30]; sb = SL_op[7];
  //   sfence_vma = mechie_op[3]; sh = SL_op[8]; sll = alu_op[2]; slli = salu_op[5]; slt = alu_op[3];
  //   slti = salu_op[6]; sltiu = salu_op[7]; sltu = alu_op[4]; sra = salu_op[3]; srai = salu_op[9];
  //   sret = mechie_op[4]; srl = salu_op[4]; srli = salu_op[8]; sub = alu_op[1]; sw = SL_op[9]; wfi = mechie_op[5];
  //   xor = alu_op[9]; xori = alu_op[6]

  // Notes on the sheet:
  //   contents of lookuptable_1 (hex, n*v repeats v):
  //   0,0,0,5,11*0,b,0,0,0,2,0,0,0,9,11*0,8,15*0,7,0,0,0,a,43*0,1,0,0,0
  //   ,4,7*0,6,0,0,0,3
  //   U
  //   R
  //   I
  //   B
  //   S
endmodule
