// Digital circuit Program-Counter.dig as structural Verilog
module Program_Counter (
  input  En,
  input  Clock,
  input  [31:0] Addr_set,
  input  [31:0] Addr_jmp,
  input  En_jmp,
  output [31:0] PC_next
);

  wire and_1_out, and_2_out, not_1_out;
  wire [31:0] add_1_s, out;

  not not_1 (not_1_out, En_jmp);
  Add #(.Bits(32)) add_1 (.a(Addr_set), .b(32'h4), .c_i(1'b0), .s(add_1_s));  // open: c_o
  and and_1 (and_1_out, En, En_jmp);
  Register #(.Bits(32)) register_1 (.D(out), .C(~Clock), .en(En), .Q(PC_next));
  and and_2 (and_2_out, En, not_1_out);
  assign out = and_2_out ? add_1_s : 32'bz;  // Driver driver_1
  assign out = and_1_out ? Addr_jmp : 32'bz;  // Driver driver_2

  // Other names for the same wires on the sheet: addr_cur[31:0] = Addr_set; addr_next[31:0] = PC_next; C = Clock
endmodule
