// Digital circuit 11.dig as structural Verilog
module _11 (
  input  clk,
  input  in_2,
  input  in_3,
  input  in_15,
  output out_4,
  output [7:0] out_5,
  output [7:0] out_6,
  output out_7,
  output [1:0] out_8,
  output out_9,
  output [7:0] out_10,
  output out_11,
  output [1:0] out_12,
  output [2:0] out_13,
  output out_14,
  output out_16
);

  wire counter_2_out, i2c_master_1_scl, i2c_master_1_sda;

  i2c_master i2c_master_1 (
    .Dev_addr(7'b0000001), .mem_addr(8'h3), .RW(in_2), .on_off(in_3), .SDA_in(i2c_master_1_sda),
    .Data_in(8'hf), .Clock(clk), .SCL(i2c_master_1_scl), .SDA(i2c_master_1_sda), .Data_out(out_10),
    .status(out_11), .NACK(out_9), .stat(out_12));
  Counter #(.Bits(3)) counter_1 (.en(1'b1), .C(clk), .clr(1'b0), .out(out_13));  // open: ovf
  // ScopeTrigger scopetrigger_1: pin names not known; wires that end beside it: i2c_master_1_sda
  i2c_slave i2c_slave_1 (
    .SCL(i2c_master_1_scl), .SDA(i2c_master_1_sda), .Address(7'b0000001), .Data_in(8'h1),
    .SDA_out(i2c_master_1_sda), .Out_en(out_4), .Data_out(out_5), .Addr_out(out_6), .invalidaddr(out_7),
    .stat(out_8));
  Counter counter_2 (.en(1'b1), .C(clk), .clr(1'b0), .out(counter_2_out));  // open: ovf
  PullUp pullup_1 (.out(i2c_master_1_sda));
  RS_FF_AS rs_ff_as_1 (.S(in_15), .R(counter_2_out), .Q(out_14), .nQ(out_16));

  // Notes on the sheet:
  //   clk: Hz: 2
endmodule
