// Digital circuit 32-bit-register.dig as structural Verilog
module _32_bit_register (
  input  [31:0] Din,
  input  clock,
  input  WE,
  input  OE1,
  input  OE2,
  input  OE3,
  output [31:0] data,
  output [31:0] Output1,
  output [31:0] Output2,
  output [31:0] Output3
);

  Register #(.Bits(32)) register_1 (.D(Din), .C(clock), .en(WE), .Q(data));
  assign Output1 = OE1 ? data : 32'bz;  // Driver driver_1
  assign Output2 = OE2 ? data : 32'bz;  // Driver driver_2
  assign Output3 = OE3 ? data : 32'bz;  // Driver driver_3
endmodule
