// Digital circuit 4-status-mechine.dig as structural Verilog
module _4_status_mechine (
  input  Clock,
  input  nexten_0,
  input  nexten_1,
  input  nexten_2,
  input  nexten_3,
  output [1:0] Status_cur
);

  wire and_5_out, CUR0, CUR1, CUR2, CUR3, S0, S1, S2, S3;
  wire [1:0] next;

  Decoder #(.Selector_Bits(2)) decoder_1 (.sel(Status_cur), .out_0(CUR0), .out_1(CUR1), .out_2(CUR2), .out_3(CUR3));
  and and_1 (S0, nexten_0, CUR0);
  and and_2 (S1, nexten_1, CUR1);
  and and_3 (S2, nexten_2, CUR2);
  and and_4 (S3, nexten_3, CUR3);
  assign next = S1 ? 2'b10 : 2'bz;  // Driver driver_1
  assign next = S2 ? 2'b11 : 2'bz;  // Driver driver_2
  assign next = S3 ? 2'b00 : 2'bz;  // Driver driver_3
  assign next = S0 ? 2'b01 : 2'bz;  // Driver driver_4
  and and_5 (and_5_out, ~S0, ~S1, ~S2, ~S3);  // And
  PullDown #(.Bits(2)) pulldown_1 (.out(next));
  D_FF #(.Bits(2)) d_ff_1 (.D(next), .C(Clock), .Q(Status_cur));  // open: nQ
  assign next = and_5_out ? Status_cur : 2'bz;  // Driver driver_5

  // Other names for the same wires on the sheet: cur[1:0] = Status_cur
endmodule
