// Digital circuit PLIC.dig as structural Verilog
module PLIC (
  input  Clock,
  input  TimerClock,
  input  [31:0] Addr_w,
  input  [31:0] Addr_r1,
  input  [31:0] Addr_r2,
  input  [31:0] Data_in,
  input  [31:0] mip_in,
  output [63:0] out_4,
  output [31:0] mip_set,
  output mip_seten
);

  wire [31:0] mc_en;
  wire [63:0] mc_in, mc_out, mtime_in;

  Add #(.Bits(64)) add_1 (.a(out_4), .b(64'h1), .c_i(TimerClock), .s(mtime_in));  // open: c_o
  Register #(.Bits(64)) mtime (.D(mtime_in), .C(TimerClock), .en(1'b1), .Q(out_4));
  assign mc_en = ~(Addr_w ^ 32'hb0000000);  // XNOr xnor_1, 32 bits wide
  assign mc_en = ~(Addr_w ^ 32'hb0000004);  // XNOr xnor_2, 32 bits wide
  Register #(.Bits(64)) mtimecmp (.D(mc_in), .C(Clock), .en(mc_en[0]), .Q(mc_out));
  assign mc_in[0] = mc_en[0] ? Data_in[0] : 1'bz;  // Driver driver_1
  assign mc_in[0] = mc_en[0] ? mc_out[0] : 1'bz;  // Driver driver_2
  RegisterFile #(.AddrBits(24), .Bits(32)) registerfile_1 (
    .Din(Data_in), .we(Addr_w[0]), .Rw(Addr_w[29:6]), .C(Clock), .Ra(Addr_r1[29:6]), .Rb(Addr_r2[29:6]));  // open: Da, Db
  PullDown pulldown_1 (.out(mip_seten));
  // Pins of 1 and 32 bits meet at mc_en
  // Pins of 1 and 64 bits meet at mc_in
  // Pins of 1 and 64 bits meet at {mc_out[63:32], Data_in}
  // Pins of 1 and 64 bits meet at {Data_in, mc_out[31:0]}

  // Other names for the same wires on the sheet: ra = Addr_r1[0]; Addr_ra[23:0] = Addr_r1[29:6]; rb = Addr_r2[0];
  //   Addr_rb[23:0] = Addr_r2[29:6]; we = Addr_w[0]; Addr_rw[23:0] = Addr_w[29:6]; C = Clock; mip_out[31:0] = mip_set;
  //   mtime_out[63:0] = out_4; TC = TimerClock
endmodule
