// Digital circuit alu.dig as structural Verilog
module alu (
  input  [18:0] Alu_in,
  input  [31:0] rs1_in,
  input  [31:0] rs2_in,
  input  [11:0] Imm12_in,
  input  Clock,
  output [31:0] rd_out,
  output EN_out,
  output [31:0] InvlidOP_out
);

  wire comparator_1_eq, comparator_1_gt, comparator_1_lt, comparator_2_eq, comparator_2_gt, comparator_2_lt,
       comparator_3_eq, comparator_3_gt, comparator_3_lt, comparator_4_eq, comparator_4_gt, comparator_4_lt,
       invalidop, not_1_out, not_2_out, not_3_out, or_3_out, or_5_out, or_6_out, or_7_out;
  wire [5:0] driver_6_out, driver_10_out, driver_22_out;
  wire [31:0] add_1_s, add_2_s, and_1_out, and_2_out, barrelshifter_1_out, barrelshifter_2_out,
       barrelshifter_3_out, barrelshifter_4_out, barrelshifter_5_out, barrelshifter_6_out, bitextender_1_out,
       bitextender_2_out, bitextender_3_out, bitextender_4_out, bitextender_5_out, driver_15_out,
       driver_24_out, driver_26_out, driver_32_out, or_2_out, or_4_out, sub_1_s, xor_1_out, xor_2_out;

  or or_1 (EN_out, Alu_in[0], Alu_in[1], Alu_in[2], Alu_in[3], Alu_in[4], Alu_in[10], Alu_in[16], Alu_in[14], Alu_in[17], Alu_in[18], Alu_in[5], Alu_in[8], Alu_in[9], Alu_in[6], Alu_in[7], Alu_in[11], Alu_in[12], Alu_in[13], Alu_in[15]);
  assign InvlidOP_out = invalidop ? 32'h2 : 32'bz;  // Driver driver_1
  PullDown pulldown_1 (.out(invalidop));
  BitExtender #(.inputBits(12), .outputBits(32)) bitextender_1 (.in(Imm12_in), .out(bitextender_1_out));
  not not_1 (not_1_out, Imm12_in[5]);
  assign invalidop = Alu_in[11] ? Imm12_in[5] : 1'bz;  // Driver driver_2
  assign and_1_out = rs1_in & rs2_in;  // And and_1, 32 bits wide
  assign and_2_out = rs1_in & bitextender_1_out;  // And and_2, 32 bits wide
  not not_2 (not_2_out, Imm12_in[5]);
  assign invalidop = Alu_in[16] ? Imm12_in[5] : 1'bz;  // Driver driver_3
  Add #(.Bits(32)) add_1 (.a(rs1_in), .b(rs2_in), .c_i(1'b0), .s(add_1_s));  // open: c_o
  BarrelShifter #(.Bits(32)) barrelshifter_1 (.in(rs1_in), .shift({1'b0, rs2_in[4:0]}), .out(barrelshifter_1_out));
  BarrelShifter #(.Bits(32), .barrelShifterMode("arithmetic"), .direction("right")) barrelshifter_2 (
    .in(rs1_in), .shift({1'b0, rs2_in[4:0]}), .out(barrelshifter_2_out));
  assign rd_out = Alu_in[0] ? add_1_s : 32'bz;  // Driver driver_4
  assign rd_out = Alu_in[2] ? barrelshifter_1_out : 32'bz;  // Driver driver_5
  BarrelShifter #(.Bits(32)) barrelshifter_3 (.in(rs1_in), .shift(driver_6_out), .out(barrelshifter_3_out));
  assign driver_6_out = not_1_out ? {1'b0, Imm12_in[4:0]} : 6'bz;  // Driver driver_6
  assign rd_out = Alu_in[9] ? and_1_out : 32'bz;  // Driver driver_7
  assign rd_out = Alu_in[18] ? and_2_out : 32'bz;  // Driver driver_8
  assign rd_out = Alu_in[6] ? barrelshifter_2_out : 32'bz;  // Driver driver_9
  BarrelShifter #(.Bits(32), .barrelShifterMode("arithmetic"), .direction("right")) barrelshifter_4 (
    .in(rs1_in), .shift(driver_10_out), .out(barrelshifter_4_out));
  assign driver_10_out = not_2_out ? {1'b0, Imm12_in[4:0]} : 6'bz;  // Driver driver_10
  assign rd_out = Alu_in[11] ? barrelshifter_3_out : 32'bz;  // Driver driver_11
  assign rd_out = Alu_in[16] ? barrelshifter_4_out : 32'bz;  // Driver driver_12
  Sub #(.Bits(32)) sub_1 (.a(rs1_in), .b(rs2_in), .c_i(1'b0), .s(sub_1_s));  // open: c_o
  Comparator #(.Signed("true"), .Bits(32)) comparator_1 (
    .a(rs1_in), .b(rs2_in), .gt(comparator_1_gt), .eq(comparator_1_eq), .lt(comparator_1_lt));
  assign or_2_out = rs1_in | rs2_in;  // Or or_2, 32 bits wide
  BitExtender #(.inputBits(12), .outputBits(32)) bitextender_2 (.in(Imm12_in), .out(bitextender_2_out));
  assign rd_out = Alu_in[1] ? sub_1_s : 32'bz;  // Driver driver_13
  or or_3 (or_3_out, comparator_1_gt, comparator_1_eq);
  assign rd_out = Alu_in[8] ? or_2_out : 32'bz;  // Driver driver_14
  assign or_4_out = rs1_in | bitextender_2_out;  // Or or_4, 32 bits wide
  BarrelShifter #(.Bits(32), .direction("right")) barrelshifter_5 (
    .in(rs1_in), .shift({1'b0, rs2_in[4:0]}), .out(barrelshifter_5_out));
  assign driver_15_out = or_3_out ? {32{1'b0}} : 32'bz;  // Driver driver_15
  assign driver_15_out = comparator_1_lt ? 32'h1 : 32'bz;  // Driver driver_16
  assign rd_out = Alu_in[7] ? barrelshifter_5_out : 32'bz;  // Driver driver_17
  assign rd_out = Alu_in[3] ? driver_15_out : 32'bz;  // Driver driver_18
  BitExtender #(.inputBits(12), .outputBits(32)) bitextender_3 (.in(Imm12_in), .out(bitextender_3_out));
  assign rd_out = Alu_in[17] ? or_4_out : 32'bz;  // Driver driver_19
  BitExtender #(.inputBits(12), .outputBits(32)) bitextender_4 (.in(Imm12_in), .out(bitextender_4_out));
  Comparator #(.Signed("true"), .Bits(32)) comparator_2 (
    .a(rs1_in), .b(bitextender_3_out), .gt(comparator_2_gt), .eq(comparator_2_eq), .lt(comparator_2_lt));
  assign xor_1_out = rs1_in ^ rs2_in;  // XOr xor_1, 32 bits wide
  not not_3 (not_3_out, Imm12_in[5]);
  assign invalidop = Alu_in[15] ? Imm12_in[5] : 1'bz;  // Driver driver_20
  Add #(.Bits(32)) add_2 (.a(rs1_in), .b(bitextender_4_out), .c_i(1'b0), .s(add_2_s));  // open: c_o
  Comparator #(.Bits(32)) comparator_3 (
    .a(rs1_in), .b(rs2_in), .gt(comparator_3_gt), .eq(comparator_3_eq), .lt(comparator_3_lt));
  or or_5 (or_5_out, comparator_2_gt, comparator_2_eq);
  assign rd_out = Alu_in[5] ? xor_1_out : 32'bz;  // Driver driver_21
  BitExtender #(.inputBits(12), .outputBits(32)) bitextender_5 (.in(Imm12_in), .out(bitextender_5_out));
  BarrelShifter #(.Bits(32), .direction("right")) barrelshifter_6 (
    .in(rs1_in), .shift(driver_22_out), .out(barrelshifter_6_out));
  assign driver_22_out = not_3_out ? {1'b0, Imm12_in[4:0]} : 6'bz;  // Driver driver_22
  assign rd_out = Alu_in[10] ? add_2_s : 32'bz;  // Driver driver_23
  or or_6 (or_6_out, comparator_3_gt, comparator_3_eq);
  assign driver_24_out = or_5_out ? {32{1'b0}} : 32'bz;  // Driver driver_24
  assign driver_24_out = comparator_2_lt ? 32'h1 : 32'bz;  // Driver driver_25
  assign xor_2_out = rs1_in ^ bitextender_5_out;  // XOr xor_2, 32 bits wide
  assign driver_26_out = or_6_out ? {32{1'b0}} : 32'bz;  // Driver driver_26
  assign driver_26_out = comparator_3_lt ? 32'h1 : 32'bz;  // Driver driver_27
  assign rd_out = Alu_in[12] ? driver_24_out : 32'bz;  // Driver driver_28
  assign rd_out = Alu_in[15] ? barrelshifter_6_out : 32'bz;  // Driver driver_29
  assign rd_out = Alu_in[4] ? driver_26_out : 32'bz;  // Driver driver_30
  assign rd_out = Alu_in[14] ? xor_2_out : 32'bz;  // Driver driver_31
  Comparator #(.Bits(32)) comparator_4 (
    .a(rs1_in), .b({{20{1'b0}}, Imm12_in}), .gt(comparator_4_gt), .eq(comparator_4_eq), .lt(comparator_4_lt));
  or or_7 (or_7_out, comparator_4_gt, comparator_4_eq);
  assign driver_32_out = or_7_out ? {32{1'b0}} : 32'bz;  // Driver driver_32
  assign driver_32_out = comparator_4_lt ? 32'h1 : 32'bz;  // Driver driver_33
  assign rd_out = Alu_in[13] ? driver_32_out : 32'bz;  // Driver driver_34

  // Other names for the same wires on the sheet: add = Alu_in[0]; sub = Alu_in[1]; sll = Alu_in[2]; slt = Alu_in[3];
  //   sltu = Alu_in[4]; xor = Alu_in[5]; sra = Alu_in[6]; srl = Alu_in[7]; or = Alu_in[8]; and = Alu_in[9];
  //   addi = Alu_in[10]; slli = Alu_in[11]; slti = Alu_in[12]; sltiu = Alu_in[13]; xori = Alu_in[14];
  //   srli = Alu_in[15]; srai = Alu_in[16]; ori = Alu_in[17]; andi = Alu_in[18]; c = Clock; rd[31:0] = rd_out;
  //   rs1[31:0] = rs1_in; rs2[31:0] = rs2_in
endmodule
