// Digital circuit base.dig as structural Verilog
module base (
  input  in_2,
  input  in_3,
  input  in_5,
  input  in_6,
  input  in_7,
  input  in_8,
  input  S,
  input  R,
  input  EN,
  input  D,
  input  in_19,
  input  in_20,
  input  in_22,
  input  in_23,
  input  in_25,
  input  in_26,
  input  in_28,
  input  in_29,
  input  clk,
  output out_1,
  output out_4,
  output out_9,
  output Q,
  output Q_2,
  output Q_3,
  output Q_4,
  output out_18,
  output out_21,
  output out_24,
  output [1:0] out_27,
  output out_31,
  output out_32
);

  wire and_1_out, and_2_out, and_3_out, and_4_out, nfet_1_s, not_1_out, relay_1_p4, relay_3_p4;

  // Relay relay_1: pin names not known; wires that end beside it: in_2, 1'b1, 1'b0, relay_1_p4
  // Relay relay_2: pin names not known; wires that end beside it: in_5, 1'b1, 1'b0, out_4
  PFET pfet_1 (.G(in_19), .S(1'b1), .D(out_18));
  PullDown pulldown_1 (.out(out_18));
  NFET nfet_1 (.G(in_20), .D(1'b1), .S(nfet_1_s));
  NFET nfet_2 (.G(in_23), .D(1'b1), .S(out_24));
  // Relay relay_3: pin names not known; wires that end beside it: in_26, 1'b1, 1'b0, relay_3_p4
  NFET nfet_3 (.G(in_22), .D(nfet_1_s), .S(out_21));
  NFET nfet_4 (.G(in_25), .D(1'b1), .S(out_24));
  // Relay relay_4: pin names not known; wires that end beside it: in_3, relay_1_p4, 1'b0, out_1
  // Relay relay_5: pin names not known; wires that end beside it: in_6, 1'b1, 1'b0, out_4
  LED led_1 (.in(relay_3_p4));
  PullDown pulldown_2 (.out(out_21));
  PullDown pulldown_3 (.out(out_24));
  PullDown pulldown_4 (.out(out_1));
  PullDown pulldown_5 (.out(out_4));
  LookUpTable #(.Bits(2)) lookuptable_1 (.in0(in_28), .in1(in_29), .out(out_27));
  Button button_1 (.out(out_32));
  and and_1 (and_1_out, in_7, ~in_8);  // And
  and and_2 (and_2_out, ~in_7, in_8);  // And
  nor nor_1 (Q, S, Q_2);
  nor nor_2 (Q_2, Q, R);
  or or_1 (out_9, and_1_out, and_2_out);
  not not_1 (not_1_out, D);
  and and_3 (and_3_out, EN, not_1_out);
  and and_4 (and_4_out, EN, D);
  nor nor_3 (Q_3, and_3_out, Q_4);
  nor nor_4 (Q_4, Q_3, and_4_out);

  assign out_31 = clk;

  // Notes on the sheet:
  //   非门
  //   与门
  //   或门
  //   或门 MOS管
  //   与门 MOS管
  //   contents of lookuptable_1 (hex, n*v repeats v):
  //   0,1,2,3
  //   异或门
  //   SR锁存器
  //   D触发器
endmodule
