// Digital circuit boot-rom.dig as structural Verilog
module boot_rom (
  input  [23:0] Addr,
  input  En,
  output [31:0] Out_code
);

  wire [23:0] barrelshifter_1_out;

  BarrelShifter #(.Bits(24), .direction("right")) barrelshifter_1 (
    .in(Addr), .shift(5'b00010), .out(barrelshifter_1_out));
  ROM #(.AddrBits(24), .Bits(8)) rom_1 (.A(barrelshifter_1_out), .sel(En), .D(Out_code[7:0]));
  ROM #(.AddrBits(24), .Bits(8)) rom_2 (.A(barrelshifter_1_out), .sel(En), .D(Out_code[15:8]));
  ROM #(.AddrBits(24), .Bits(8)) rom_3 (.A(barrelshifter_1_out), .sel(En), .D(Out_code[23:16]));
  ROM #(.AddrBits(24), .Bits(8)) rom_4 (.A(barrelshifter_1_out), .sel(En), .D(Out_code[31:24]));

  // Notes on the sheet:
  //   contents of rom_1 (hex, n*v repeats v):
  //   7f,f3,13,b7,23,37,13,83,93,37,23,97,93,93,f3,37,13,f3,37,13,f3
  //   ,13,6f,48*13,6f,13,13,13,37,13,83,93,63,13,23,73,93,63,93,3,93
  //   ,63,13,6f,13,23,37,83,93,23,73
  //   contents of rom_2 (hex, n*v repeats v):
  //   0,12,3,5,a0,e,e,2e,8e,e,20,7,87,87,93,2e,e,13,1e,e,13,4,53*0,f,f
  //   ,29,f9,84,4,22,0,72,92,84,a3,f2,96,63,0,73,a2,e,2e,8e,20
  //   contents of rom_3 (hex, n*v repeats v):
  //   0,0,f0,0,65,0,8e,e,e,0,de,0,47,17,57,0,8e,e,0,8e,4e,55*0,4f,f
  //   ,9,9,14,f,20,14,2,14,45,14,2,f3,80,3,65,0,8e,8e,de,20
  //   contents of rom_4 (hex, n*v repeats v):
  //   80,30,7,a0,0,b0,0,0,7d,b0,1,0,d,0,30,0,80,30,0,88,30,50*0,3,0,0,0
  //   ,a0,0,0,20,0,0,0,30,0,2,4*0,7,0,38,0,b0,0,2e,1,30
endmodule
