// Digital circuit csr.dig as structural Verilog
module csr (
  input  [5:0] CSRCode_in,
  input  [31:0] Data_in,
  input  [11:0] Csr_Addr,
  input  [4:0] Imm5_in,
  input  Clock,
  output [31:0] ddata,
  output [31:0] Out_rd,
  output En_rd
);

  wire and_4_out, and_5_out, not_1_out, not_3_out, re, we;
  wire [31:0] data_temp, data_w, driver_2_out, driver_6_out, not_2_out, not_4_out, or_2_out, or_3_out,
       out_temp_q;

  not not_1 (not_1_out, En_rd);
  or or_1 (En_rd, CSRCode_in[0], CSRCode_in[1], CSRCode_in[2], CSRCode_in[3], CSRCode_in[4], CSRCode_in[5]);
  Counter RW_EN (.en(En_rd), .C(Clock), .clr(not_1_out), .out(we));  // open: ovf
  assign data_w = CSRCode_in[0] ? Data_in : 32'bz;  // Driver driver_1
  assign or_2_out = Data_in | Out_rd;  // Or or_2, 32 bits wide
  assign not_2_out = ~Data_in;  // Not not_2, 32 bits wide
  not not_3 (not_3_out, we);
  and and_1 (re, not_3_out, En_rd);
  assign driver_2_out = CSRCode_in[2] ? not_2_out : 32'bz;  // Driver driver_2
  assign data_w = CSRCode_in[1] ? or_2_out : 32'bz;  // Driver driver_3
  assign data_w = driver_2_out & Out_rd;  // And and_2, 32 bits wide
  assign data_w = CSRCode_in[3] ? {{27{1'b0}}, Imm5_in} : 32'bz;  // Driver driver_4
  assign or_3_out = {{27{1'b0}}, Imm5_in} | Out_rd;  // Or or_3, 32 bits wide
  assign not_4_out = ~{{27{1'b0}}, Imm5_in};  // Not not_4, 32 bits wide
  assign data_w = CSRCode_in[4] ? or_3_out : 32'bz;  // Driver driver_5
  assign driver_6_out = CSRCode_in[5] ? not_4_out : 32'bz;  // Driver driver_6
  assign data_w = driver_6_out & Out_rd;  // And and_3, 32 bits wide
  and and_4 (and_4_out, we, En_rd);
  and and_5 (and_5_out, re, En_rd);
  RegisterFile #(.AddrBits(12), .Bits(32)) CSR_Registers (
    .Din(data_w), .we(and_4_out), .Rw(Csr_Addr), .C(Clock), .Ra(Csr_Addr), .Rb(Csr_Addr), .Da(data_temp),
    .Db(ddata));
  Register #(.Bits(32)) out_temp (.D(data_temp), .C(Clock), .en(and_5_out), .Q(out_temp_q));
  PullDown pulldown_1 (.out(En_rd));
  assign Out_rd = En_rd ? out_temp_q : 32'bz;  // Driver driver_7
  PullDown #(.Bits(32)) pulldown_2 (.out(Out_rd));

  // Other names for the same wires on the sheet: addr[11:0] = Csr_Addr; c = Clock; csr_en = En_rd;
  //   csrrw = CSRCode_in[0]; csrrs = CSRCode_in[1]; csrrc = CSRCode_in[2]; csrrwi = CSRCode_in[3];
  //   csrrsi = CSRCode_in[4]; csrrci = CSRCode_in[5]; data_out[31:0] = Out_rd; imm_in[4:0] = Imm5_in
endmodule
