// Digital circuit gpio.dig as structural Verilog
module gpio (
  input  Clock,
  input  [31:0] Addr_w,
  input  [31:0] Data_in,
  input  we,
  input  [31:0] Addr_rd,
  input  int_gate,
  input  GPIO1_in,
  input  GPIO2_in,
  input  GPIO3_in,
  input  GPIO4_in,
  input  GPIO5_in,
  input  GPIO6_in,
  input  GPIO7_in,
  input  GPIO8_in,
  input  GPIO9_in,
  input  GPIO10_in,
  output [31:0] Out_rd,
  output Out_en,
  output [31:0] perint_code,
  output GPIO1_out,
  output GPIO2_out,
  output GPIO3_out,
  output GPIO4_out,
  output GPIO5_out,
  output GPIO6_out,
  output GPIO7_out,
  output GPIO8_out,
  output GPIO9_out,
  output GPIO10_out
);

  wire addr_compare_1_eq_out, addr_compare_2_eq_out, addr_compare_3_eq_out, addr_compare_4_eq_out,
       addr_compare_5_eq_out, addr_compare_6_eq_out, addr_compare_7_eq_out, addr_compare_8_eq_out,
       addr_compare_9_eq_out, and_8_out, and_9_out, code_en, gpio_datawe, gpio_setwe, not_1_out, not_2_out;
  wire [9:0] and_1_out, and_2_out, and_5_out, and_6_out, gpio_datain, gpio_value1, or_2_out;
  wire [31:0] cur_gpioset, cur_gpiovalue, gpio_setin, int_code, int_codein;

  Register #(.Bits(32)) gpio_set_reg (.D(gpio_setin), .C(Clock), .en(gpio_setwe), .Q(cur_gpioset));
  addr_compare addr_compare_1 (.Addr_in1(Addr_w), .Addr_in2(32'ha0000000), .Eq_out(addr_compare_1_eq_out));
  addr_compare addr_compare_2 (.Addr_in1(Addr_w), .Addr_in2(32'ha0000004), .Eq_out(addr_compare_2_eq_out));
  addr_compare addr_compare_3 (
    .Addr_in1({{22{1'b0}}, gpio_value1}), .Addr_in2({{22{1'b0}}, cur_gpiovalue[9:0]}),
    .Eq_out(addr_compare_3_eq_out));
  assign and_1_out = {GPIO10_in, GPIO9_in, GPIO8_in, GPIO7_in, GPIO6_in, GPIO5_in, GPIO4_in, GPIO3_in, GPIO2_in, GPIO1_in} & ~cur_gpioset[9:0];  // And and_1, 10 bits wide
  assign and_2_out = cur_gpioset[9:0] & cur_gpiovalue[9:0];  // And and_2, 10 bits wide
  assign gpio_value1 = and_1_out | and_2_out;  // Or or_1, 10 bits wide
  and and_3 (gpio_setwe, we, addr_compare_1_eq_out);
  assign gpio_setin = addr_compare_1_eq_out ? Data_in : 32'bz;  // Driver driver_1
  and and_4 (gpio_datawe, we, addr_compare_2_eq_out);
  assign and_5_out = Data_in[9:0] & cur_gpioset[9:0];  // And and_5, 10 bits wide
  assign and_6_out = gpio_value1 & ~cur_gpioset[9:0];  // And and_6, 10 bits wide
  not not_1 (not_1_out, addr_compare_3_eq_out);
  assign {GPIO10_out, GPIO9_out, GPIO8_out, GPIO7_out, GPIO6_out, GPIO5_out, GPIO4_out, GPIO3_out, GPIO2_out, GPIO1_out} = cur_gpiovalue[9:0] & cur_gpioset[9:0];  // And and_7, 10 bits wide
  Register #(.Bits(32)) gpio_value_reg (.D({{22{1'b0}}, gpio_datain}), .C(Clock), .en(1'b1), .Q(cur_gpiovalue));
  assign or_2_out = and_5_out | and_6_out;  // Or or_2, 10 bits wide
  and and_8 (and_8_out, ~int_gate, not_1_out);  // And
  assign int_codein = and_8_out ? 32'h1 : 32'bz;  // Driver driver_2
  not not_2 (not_2_out, gpio_datawe);
  assign gpio_datain = gpio_datawe ? or_2_out : 10'bz;  // Driver driver_3
  assign code_en = and_8_out ? 1'b1 : 1'bz;  // Driver driver_4
  assign gpio_datain = not_2_out ? gpio_value1 : 10'bz;  // Driver driver_5
  addr_compare addr_compare_4 (.Addr_in1(int_code), .Addr_in2({32{1'b0}}), .Eq_out(addr_compare_4_eq_out));
  addr_compare addr_compare_5 (.Addr_in1(Addr_w), .Addr_in2(32'ha0000008), .Eq_out(addr_compare_5_eq_out));
  PullDown pulldown_1 (.out(code_en));
  addr_compare addr_compare_6 (.Addr_in1(Addr_rd), .Addr_in2(32'ha0000000), .Eq_out(addr_compare_6_eq_out));
  addr_compare addr_compare_7 (.Addr_in1(Addr_rd), .Addr_in2(32'ha0000004), .Eq_out(addr_compare_7_eq_out));
  addr_compare addr_compare_8 (.Addr_in1(Addr_rd), .Addr_in2(32'ha0000008), .Eq_out(addr_compare_8_eq_out));
  Register #(.Bits(32)) register_1 (.D(int_codein), .C(Clock), .en(code_en), .Q(int_code));
  and and_9 (and_9_out, ~addr_compare_4_eq_out, we, addr_compare_5_eq_out);  // And
  assign Out_rd = addr_compare_6_eq_out ? cur_gpioset : 32'bz;  // Driver driver_6
  assign Out_rd = addr_compare_7_eq_out ? cur_gpiovalue : 32'bz;  // Driver driver_7
  assign Out_rd = addr_compare_8_eq_out ? int_code : 32'bz;  // Driver driver_8
  assign int_codein = and_9_out ? Data_in : 32'bz;  // Driver driver_9
  assign code_en = and_9_out ? 1'b1 : 1'bz;  // Driver driver_10
  assign Out_en = addr_compare_6_eq_out ? 1'b1 : 1'bz;  // Driver driver_11
  assign Out_en = addr_compare_7_eq_out ? 1'b1 : 1'bz;  // Driver driver_12
  assign Out_en = addr_compare_8_eq_out ? 1'b1 : 1'bz;  // Driver driver_13
  addr_compare addr_compare_9 (.Addr_in1(int_code), .Addr_in2({32{1'b0}}), .Eq_out(addr_compare_9_eq_out));
  PullDown pulldown_2 (.out(Out_en));
  assign perint_code = ~addr_compare_9_eq_out ? int_code : 32'bz;  // DriverInvSel driverinvsel_1

  // Other names for the same wires on the sheet: GPIOOUT_1 = GPIO1_out; GPIOOUT_2 = GPIO2_out; GPIOOUT_3 = GPIO3_out;
  //   GPIOOUT_4 = GPIO4_out; GPIOOUT_5 = GPIO5_out; GPIOOUT_6 = GPIO6_out; GPIOOUT_7 = GPIO7_out;
  //   GPIOOUT_8 = GPIO8_out; GPIOOUT_9 = GPIO9_out; GPIOOUT_10 = GPIO10_out; C = Clock;
  //   gpio_settmp[9:0] = cur_gpioset[9:0]; cur_gpiovaluetemp[9:0] = cur_gpiovalue[9:0];
  //   gpio_valuein[9:0] = gpio_datain;
  //   gpio_inputtemp[9:0] = {GPIO10_in, GPIO9_in, GPIO8_in, GPIO7_in, GPIO6_in, GPIO5_in, GPIO4_in, GPIO3_in, GPIO2_in, GPIO1_in};
  //   GPIOIN_1 = GPIO1_in; GPIOIN_2 = GPIO2_in; GPIOIN_3 = GPIO3_in; GPIOIN_4 = GPIO4_in; GPIOIN_5 = GPIO5_in;
  //   GPIOIN_6 = GPIO6_in; GPIOIN_7 = GPIO7_in; GPIOIN_8 = GPIO8_in; GPIOIN_9 = GPIO9_in; GPIOIN_10 = GPIO10_in
endmodule
