// Digital circuit i2c-controller.dig as structural Verilog
module i2c_controller (
  input  IICClock,
  input  SDA,
  input  [31:0] Addr_w,
  input  [31:0] Data_in,
  input  we,
  input  [31:0] Addr_rd,
  input  int_gate,
  input  Clock,
  output SDA_out,
  output SCL,
  output [31:0] Out_rd,
  output Out_en,
  output [31:0] perint_code
);

  wire addr_compare_1_eq_out, addr_compare_2_eq_out, and_2_out, and_3_out, and_4_out, ic_s0, ic_s1, ic_s2,
       ic_s3, not_1_out, option_on, or_1_out, out_en_t, res_status, to_s3;
  wire [1:0] iic_c_status;
  wire [6:0] Dev_addr;
  wire [7:0] Data_out, Data_res, data_send;
  wire [31:0] iic_buffer, iic_operate, iic_read;

  addr_compare addr_compare_1 (.Addr_in1(Addr_w), .Addr_in2(32'ha0000200), .Eq_out(addr_compare_1_eq_out));
  assign iic_buffer = option_on ? 32'h1 : 32'bz;  // Driver driver_1
  D_FF #(.Bits(8)) d_ff_1 (.D(Data_out), .C(out_en_t), .Q(Data_res));  // open: nQ
  and and_1 (option_on, addr_compare_1_eq_out, we);
  or or_1 (or_1_out, ic_s3, option_on);
  i2c_master i2c_master_1 (
    .Dev_addr(Dev_addr), .mem_addr(iic_operate[15:8]), .RW(iic_operate[0]), .on_off(ic_s1), .SDA_in(SDA),
    .Data_in(data_send), .Clock(IICClock), .SCL(SCL), .SDA(SDA_out), .Out_en(out_en_t), .Data_out(Data_out),
    .status(res_status));  // open: NACK, stat
  Register #(.Bits(32)) IIC_OPTION (
    .D(Data_in), .C(Clock), .en(option_on),
    .Q({iic_operate[31:24], data_send, iic_operate[15:8], Dev_addr, iic_operate[0]}));
  Register #(.Bits(32)) IIC_READBUFFER (.D(iic_buffer), .C(Clock), .en(or_1_out), .Q(iic_read));
  assign iic_buffer = ic_s3 ? {iic_read[31:16], Data_res, iic_read[7:1], 1'b0} : 32'bz;  // Driver driver_2
  and and_2 (and_2_out, ic_s3, ~int_gate);  // And
  addr_compare addr_compare_2 (.Addr_in1(Addr_rd), .Addr_in2(32'ha0000204), .Eq_out(addr_compare_2_eq_out));
  and and_3 (and_3_out, out_en_t, iic_operate[0]);
  and and_4 (and_4_out, res_status, ~iic_operate[0]);  // And
  not not_1 (not_1_out, res_status);
  assign perint_code = and_2_out ? 32'h3 : 32'bz;  // Driver driver_3
  assign Out_rd = addr_compare_2_eq_out ? iic_read : 32'bz;  // Driver driver_4
  _4_status_mechine _4_status_mechine_1 (
    .Clock(Clock), .nexten_0(option_on), .nexten_1(not_1_out), .nexten_2(to_s3), .nexten_3(res_status),
    .direct_statusen(1'b0), .direct_status(2'b00), .falling_edge_status(4'b0000), .Status_cur(iic_c_status));
  or or_2 (to_s3, and_3_out, and_4_out);
  assign Out_en = addr_compare_2_eq_out ? 1'b1 : 1'bz;  // Driver driver_5
  Decoder #(.Selector_Bits(2)) decoder_1 (
    .sel(iic_c_status), .out_0(ic_s0), .out_1(ic_s1), .out_2(ic_s2), .out_3(ic_s3));
  PullDown pulldown_1 (.out(Out_en));

  // Other names for the same wires on the sheet: C = Clock; iic_clock = IICClock; rw = iic_operate[0];
  //   iic_operate (some bits) = {data_send, Dev_addr}; mem_addr[7:0] = iic_operate[15:8]; op_status = iic_read[0];
  //   iic_reserved1[6:0] = iic_read[7:1]; iic_reserved2[15:0] = iic_read[31:16]; int_code[31:0] = perint_code;
  //   sda_in = SDA

  // Notes on the sheet:
  //   IICClock: Hz: 5
  //   Clock: Hz: 500
endmodule
