// Digital circuit i2c-master-startandaddr.dig as structural Verilog
module i2c_master_startandaddr (
  input  Clock,
  input  start,
  input  RW,
  input  [6:0] Dev_addr,
  input  SDA_in,
  input  Clock_Src,
  output SDA,
  output ack,
  output status
);

  wire and_1_out, d_statusen, driverinvsel_1_out, master_s0, master_s1, master_s2, rs_ff_as_1_q,
       start_status, t_ff_1_q, tos3;
  wire [1:0] m_status;

  _4_status_mechine _4_status_mechine_1 (
    .Clock(Clock), .nexten_0(start), .nexten_1(1'b1), .nexten_2(tos3), .nexten_3(1'b1),
    .direct_statusen(1'b0), .direct_status(2'b01), .falling_edge_status(4'b0000), .Status_cur(m_status));
  and and_1 (and_1_out, master_s1, Clock);
  T_FF t_ff_1 (.T(1'b1), .C(Clock_Src), .Q(t_ff_1_q));  // open: nQ
  Decoder #(.Selector_Bits(2)) decoder_1 (
    .sel(m_status), .out_0(master_s0), .out_1(master_s1), .out_2(master_s2), .out_3(d_statusen));
  assign driverinvsel_1_out = ~t_ff_1_q ? and_1_out : 1'bz;  // DriverInvSel driverinvsel_1
  RS_FF_AS rs_ff_as_1 (.S(driverinvsel_1_out), .R(~master_s1), .Q(rs_ff_as_1_q));  // open: nQ
  assign SDA = rs_ff_as_1_q ? 1'b0 : 1'bz;  // Driver driver_1
  i2c_master_senddata i2c_master_senddata_1 (
    .Data_in({Dev_addr, RW}), .en(master_s1), .Clock(Clock), .SDA_in(SDA_in), .SDA(SDA),
    .status(start_status), .ack(ack));
  and and_2 (tos3, start_status, master_s2);
  and and_3 (status, start_status, ~master_s1);  // And

  // Other names for the same wires on the sheet: c = Clock_Src; send_byte[7:0] = {Dev_addr, RW};
  //   master_s3 = d_statusen; on_off = start; scl = Clock

  // Notes on the sheet:
  //   Clock_Src: Hz: 2
  //   s0: wait start
  //   s1: send start 
  //   s2: send dev address
endmodule
