// Digital circuit i2c-master.dig as structural Verilog
module i2c_master (
  input  [6:0] Dev_addr,
  input  [7:0] mem_addr,
  input  RW,
  input  on_off,
  input  SDA_in,
  input  [7:0] Data_in,
  input  Clock,
  output SCL,
  output SDA,
  output [7:0] Data_out,
  output status,
  output NACK,
  output [1:0] stat
);

  wire ack_1, ack_2, and_1_out, and_2_out, and_3_out, and_4_out, and_5_out, and_6_out, and_9_out, dstatus_en,
       or_2_out, or_3_out, or_4_out, out_en, send_complate, senddata_en, slave_s1, slave_s2, slave_s3, to_s2,
       to_s3;
  wire [1:0] dstatus;
  wire [7:0] data_send;

  Counter counter_1 (.en(1'b1), .C(Clock), .clr(1'b0), .ovf(SCL));  // open: out
  _4_status_mechine _4_status_mechine_1 (
    .Clock(SCL), .nexten_0(on_off), .nexten_1(to_s2), .nexten_2(to_s3), .nexten_3(to_s3),
    .direct_statusen(dstatus_en), .direct_status(dstatus), .falling_edge_status(4'b0000), .Status_cur(stat));
  and and_1 (and_1_out, status, on_off);
  and and_2 (and_2_out, ~ack_1, send_complate, slave_s2);  // And
  and and_3 (and_3_out, RW, out_en);
  and and_4 (and_4_out, to_s3, slave_s3);
  Decoder #(.Selector_Bits(2)) decoder_1 (
    .sel(stat), .out_0(status), .out_1(slave_s1), .out_2(slave_s2), .out_3(slave_s3));
  i2c_master_startandaddr i2c_master_startandaddr_1 (
    .Clock(SCL), .start(and_1_out), .RW(RW), .Dev_addr(Dev_addr), .SDA_in(SDA_in), .Clock_Src(Clock),
    .SDA(SDA), .ack(ack_1), .status(to_s2));
  or or_1 (dstatus_en, and_2_out, and_3_out, and_4_out);
  assign dstatus = dstatus_en ? 2'b00 : 2'bz;  // Driver driver_1
  and and_5 (and_5_out, slave_s2, RW);
  i2c_master_readdata i2c_master_readdata_1 (
    .en(and_5_out), .Clock(SCL), .SDA_in(SDA_in), .SDA(SDA), .status(out_en), .Data_out(Data_out));
  assign SDA = dstatus_en ? 1'b0 : 1'bz;  // Driver driver_2
  or or_2 (or_2_out, to_s2, to_s3);
  and and_6 (and_6_out, slave_s2, ~to_s3);  // And
  i2c_master_senddata i2c_master_senddata_1 (
    .Data_in(data_send), .en(senddata_en), .Clock(SCL), .SDA_in(SDA_in), .SDA(SDA), .status(send_complate),
    .ack(ack_2));
  or or_3 (or_3_out, and_6_out, to_s2);
  and and_7 (senddata_en, or_2_out, ~RW);  // And
  and and_8 (to_s3, send_complate, ~RW, slave_s2);  // And
  assign data_send = or_3_out ? mem_addr : 8'bz;  // Driver driver_3
  and and_9 (and_9_out, to_s3, slave_s2);
  or or_4 (or_4_out, slave_s3, and_9_out);
  not not_1 (NACK, ack_1);
  assign data_send = or_4_out ? Data_in : 8'bz;  // Driver driver_4

  // Other names for the same wires on the sheet: c = Clock; I2C_status[1:0] = stat; slave_s0 = status

  // Notes on the sheet:
  //   Clock: Hz: 2
  //   s0: wait start
  //   s1: send dev address
  //   s2: send write mem address or read data
  //   s3: send write data
endmodule
