// Digital circuit i2c-slave.dig as structural Verilog
module i2c_slave (
  input  SCL,
  input  SDA,
  input  [6:0] Address,
  input  [7:0] Data_in,
  output SDA_out,
  output Out_en,
  output [7:0] Data_out,
  output [7:0] Addr_out,
  output invalidaddr,
  output [1:0] stat
);

  wire and_1_out, and_5_out, and_7_out, and_8_out, and_12_out, bit0, bit1, bit2, bit3, bit4, bit5, bit6,
       bit7, bitselector_1_out, comparator_1_eq, control_sig, d_ff_6_q, data_bit, dstatus_en, in_data,
       or_2_out, or_3_out, or_5_out, recv_data, rw, s1_end, s2_end, s_ack, s_acktmp, s_end, send_data,
       slave_s0, slave_s1, slave_s2, slave_s3, start_sig, stop_sig, stop_sigtmp, xor_1_out;
  wire [1:0] dstatus;
  wire [2:0] bit_pos, sub_1_s;
  wire [3:0] counter_2_out;
  wire [7:0] byte_in, byte_out;

  and and_1 (and_1_out, control_sig, SDA);
  xor xor_1 (xor_1_out, SDA, data_bit);
  and and_2 (start_sig, control_sig, ~SDA);  // And
  and and_3 (control_sig, xor_1_out, SCL);
  D_FF d_ff_1 (.D(stop_sigtmp), .C(~SCL), .Q(stop_sig));  // open: nQ
  and and_4 (recv_data, ~slave_s0, ~s_ack);  // And
  or or_1 (stop_sigtmp, and_1_out, invalidaddr);
  Decoder #(.Selector_Bits(3)) decoder_1 (
    .sel(bit_pos), .out_0(bit7), .out_1(bit6), .out_2(bit5), .out_3(bit4), .out_4(bit3), .out_5(bit2),
    .out_6(bit1), .out_7(bit0));
  _4_status_mechine _4_status_mechine_1 (
    .Clock(SCL), .nexten_0(start_sig), .nexten_1(s1_end), .nexten_2(s2_end), .nexten_3(stop_sig),
    .direct_statusen(dstatus_en), .direct_status(dstatus), .falling_edge_status(4'b0001), .Status_cur(stat));
  or or_2 (or_2_out, ~recv_data, s_end);  // Or
  D_FF d_ff_2 (.D(SDA), .C(SCL), .Q(data_bit));  // open: nQ
  Counter #(.Bits(3)) counter_1 (.en(1'b1), .C(SCL), .clr(or_2_out), .out(bit_pos));  // open: ovf
  Multiplexer multiplexer_1 (.sel(bit0), .in_0(byte_out[0]), .in_1(data_bit), .out(byte_in[0]));
  Multiplexer multiplexer_2 (.sel(bit1), .in_0(byte_out[1]), .in_1(data_bit), .out(byte_in[1]));
  Multiplexer multiplexer_3 (.sel(bit2), .in_0(byte_out[2]), .in_1(data_bit), .out(byte_in[2]));
  Multiplexer multiplexer_4 (.sel(bit3), .in_0(byte_out[3]), .in_1(data_bit), .out(byte_in[3]));
  Multiplexer multiplexer_5 (.sel(bit4), .in_0(byte_out[4]), .in_1(data_bit), .out(byte_in[4]));
  Multiplexer multiplexer_6 (.sel(bit5), .in_0(byte_out[5]), .in_1(data_bit), .out(byte_in[5]));
  Multiplexer multiplexer_7 (.sel(bit6), .in_0(byte_out[6]), .in_1(data_bit), .out(byte_in[6]));
  Multiplexer multiplexer_8 (.sel(bit7), .in_0(byte_out[7]), .in_1(data_bit), .out(byte_in[7]));
  Decoder #(.Selector_Bits(2)) decoder_2 (
    .sel(stat), .out_0(slave_s0), .out_1(slave_s1), .out_2(slave_s2), .out_3(slave_s3));
  Register #(.Bits(8)) register_1 (.D(byte_in), .C(SCL), .en(recv_data), .Q(byte_out));
  D_FF d_ff_3 (.D(data_bit), .C(s1_end), .Q(rw));  // open: nQ
  or or_3 (or_3_out, ~rw, slave_s1);  // Or
  D_FF d_ff_4 (.D(s_acktmp), .C(~SCL), .Q(s_ack));  // open: nQ
  and and_5 (and_5_out, or_3_out, SCL, s_ack);
  and and_6 (s1_end, s_end, slave_s1);
  Comparator #(.Bits(7)) comparator_1 (.a(byte_out[7:1]), .b(Address), .eq(comparator_1_eq));  // open: gt, lt
  and and_7 (and_7_out, s_end, slave_s2);
  assign SDA_out = and_5_out ? 1'b0 : 1'bz;  // Driver driver_1
  and and_8 (and_8_out, slave_s2, s_end);
  and and_9 (s_acktmp, bit0, ~invalidaddr);  // And
  and and_10 (invalidaddr, ~comparator_1_eq, s1_end);  // And
  or or_4 (s2_end, and_7_out, stop_sig);
  and and_11 (Out_en, ~rw, s_ack, slave_s3);  // And
  D_FF d_ff_5 (.D(bit0), .C(SCL), .nQ(in_data));  // open: Q
  Register #(.Bits(8)) register_2 (.D(byte_out), .C(SCL), .en(and_8_out), .Q(Addr_out));
  and and_12 (and_12_out, start_sig, ~slave_s1);  // And
  Sub #(.Bits(3)) sub_1 (.a(3'b111), .b(bit_pos), .c_i(1'b0), .s(sub_1_s));  // open: c_o
  or or_5 (or_5_out, and_12_out, stop_sig);
  assign Data_out = ~rw ? byte_out : 8'bz;  // DriverInvSel driverinvsel_1
  Counter #(.Bits(4)) counter_2 (.en(1'b1), .C(SCL), .clr(s_ack), .out(counter_2_out));  // open: ovf
  and and_13 (send_data, rw, slave_s2, in_data);
  BitSelector #(.Selector_Bits(3)) bitselector_1 (.in(Data_in), .sel(sub_1_s), .out(bitselector_1_out));
  Comparator #(.Bits(4)) comparator_2 (.a(counter_2_out), .b(4'b0000), .eq(s_end));  // open: gt, lt
  D_FF d_ff_6 (.D(bitselector_1_out), .C(~SCL), .Q(d_ff_6_q));  // open: nQ
  and and_14 (dstatus_en, or_5_out, ~slave_s0);  // And
  assign SDA_out = send_data ? d_ff_6_q : 1'bz;  // Driver driver_2
  assign dstatus = dstatus_en ? 2'b00 : 2'bz;  // Driver driver_3

  // Other names for the same wires on the sheet: Addr_invalid = invalidaddr; Addr_self[6:0] = Address;
  //   dev_addr[6:0] = byte_out[7:1]; I2C_status[1:0] = stat; scl_in = SCL; sda_in = SDA

  // Notes on the sheet:
  //   s0: wait start
  //   s1: read dev address
  //   s2: read write mem address or send data
  //   s3: read write data
endmodule
