// Digital circuit instuction-jump-unit.dig as structural Verilog
module instuction_jump_unit (
  input  [8:0] jmp_op,
  input  [31:0] PC_cur,
  input  [31:0] PC_next,
  input  [31:0] rs1_in,
  input  [31:0] rs2_in,
  input  [11:0] Imm12_in,
  input  [19:0] Imm20_in,
  input  [6:0] Imm7_in,
  input  [4:0] offset_5,
  output [31:0] Addr_jmp,
  output [31:0] rd_out,
  output EN_out,
  output En_jmp
);

  wire add_pc, and_1_out, and_2_out, and_3_out, and_4_out, and_5_out, and_6_out, comparator_1_eq,
       comparator_1_gt, comparator_1_lt, comparator_2_eq, comparator_2_gt, comparator_2_lt, En_jmpc,
       En_jmpc1, en_out1, en_out_t, not_1_out, not_2_out, or_2_out, or_3_out, or_4_out, or_5_out, or_11_out,
       save_rd;
  wire [31:0] add_1_s, add_2_s, Addr_offset, barrelshifter_1_out, bitextender_1_out, bitextender_2_out,
       bitextender_3_out, bitextender_4_out;

  or or_1 (EN_out, en_out1, en_out_t);
  PullDown pulldown_1 (.out(en_out1));
  Add #(.Bits(32)) add_1 (.a(Addr_offset), .b(rs1_in), .c_i(1'b0), .s(add_1_s));  // open: c_o
  PullDown pulldown_2 (.out(en_out_t));
  assign Addr_jmp = jmp_op[1] ? add_1_s : 32'bz;  // Driver driver_1
  or or_2 (or_2_out, jmp_op[2], jmp_op[3], jmp_op[5], jmp_op[4]);
  or or_3 (or_3_out, jmp_op[6], jmp_op[7]);
  BitExtender #(.inputBits(21), .outputBits(32)) bitextender_1 (
    .in({Imm20_in[19], Imm20_in[7:0], Imm20_in[8], Imm20_in[18:9], 1'b0}), .out(bitextender_1_out));
  BitExtender #(.inputBits(13), .outputBits(32)) bitextender_2 (
    .in({Imm7_in[6], offset_5[0], Imm7_in[5:0], offset_5[4:1], 1'b0}), .out(bitextender_2_out));
  Add #(.Bits(32)) add_2 (.a(Addr_offset), .b(PC_cur), .c_i(1'b0), .s(add_2_s));  // open: c_o
  assign Addr_offset = or_2_out ? bitextender_2_out : 32'bz;  // Driver driver_2
  assign Addr_offset = or_3_out ? {{19{1'b0}}, Imm7_in[6], offset_5[0], Imm7_in[5:0], offset_5[4:1], 1'b0} : 32'bz;  // Driver driver_3
  assign Addr_jmp = add_pc ? add_2_s : 32'bz;  // Driver driver_4
  assign Addr_offset = jmp_op[0] ? bitextender_1_out : 32'bz;  // Driver driver_5
  Comparator #(.Signed("true"), .Bits(32)) comparator_1 (
    .a(rs1_in), .b(rs2_in), .gt(comparator_1_gt), .eq(comparator_1_eq), .lt(comparator_1_lt));
  Comparator #(.Bits(32)) comparator_2 (
    .a(rs1_in), .b(rs2_in), .gt(comparator_2_gt), .eq(comparator_2_eq), .lt(comparator_2_lt));
  or or_4 (or_4_out, comparator_2_gt, comparator_2_eq);
  assign rd_out = save_rd ? PC_next : 32'bz;  // Driver driver_6
  BitExtender #(.inputBits(12), .outputBits(32)) bitextender_3 (.in(Imm12_in), .out(bitextender_3_out));
  or or_5 (or_5_out, comparator_1_gt, comparator_1_eq);
  and and_1 (and_1_out, comparator_1_eq, jmp_op[2]);
  and and_2 (and_2_out, comparator_1_lt, jmp_op[4]);
  not not_1 (not_1_out, comparator_2_eq);
  and and_3 (and_3_out, comparator_2_lt, jmp_op[6]);
  and and_4 (and_4_out, or_5_out, jmp_op[5]);
  and and_5 (and_5_out, or_4_out, jmp_op[7]);
  and and_6 (and_6_out, not_1_out, jmp_op[3]);
  or or_6 (En_jmp, En_jmpc1, En_jmpc);
  assign Addr_offset = jmp_op[1] ? bitextender_3_out : 32'bz;  // Driver driver_7
  PullDown pulldown_3 (.out(En_jmp));
  PullDown #(.Bits(32)) pulldown_4 (.out(Addr_jmp));
  or or_7 (En_jmpc1, and_4_out, and_1_out, and_2_out, and_5_out, and_6_out, and_3_out);
  or or_8 (en_out_t, jmp_op[0], jmp_op[1]);
  or or_9 (save_rd, jmp_op[0], jmp_op[1]);
  or or_10 (En_jmpc, jmp_op[0], jmp_op[1]);
  not not_2 (not_2_out, jmp_op[1]);
  or or_11 (or_11_out, jmp_op[0], jmp_op[2], jmp_op[3], jmp_op[4], jmp_op[5], jmp_op[6], jmp_op[7], jmp_op[8]);
  BitExtender #(.inputBits(20), .outputBits(32)) bitextender_4 (.in(Imm20_in), .out(bitextender_4_out));
  assign En_jmpc = jmp_op[8] ? 1'b0 : 1'bz;  // Driver driver_8
  BarrelShifter #(.Bits(32)) barrelshifter_1 (.in(bitextender_4_out), .shift(6'b001100), .out(barrelshifter_1_out));
  and and_7 (add_pc, not_2_out, or_11_out);
  assign save_rd = jmp_op[8] ? 1'b0 : 1'bz;  // Driver driver_9
  assign Addr_offset = jmp_op[8] ? barrelshifter_1_out : 32'bz;  // Driver driver_10
  assign rd_out = jmp_op[8] ? Addr_jmp : 32'bz;  // Driver driver_11
  assign en_out1 = jmp_op[8] ? 1'b1 : 1'bz;  // Driver driver_12

  // Other names for the same wires on the sheet: jal = jmp_op[0]; jalr = jmp_op[1]; beq = jmp_op[2]; bne = jmp_op[3];
  //   blt = jmp_op[4]; bge = jmp_op[5]; bltu = jmp_op[6]; bgeu = jmp_op[7]; auipc = jmp_op[8]; rd[31:0] = rd_out;
  //   rs1[31:0] = rs1_in; rs2[31:0] = rs2_in
endmodule
