// Digital circuit int-bus.dig as structural Verilog
module int_bus (
  input  Clock,
  input  int_gate,
  input  [31:0] int_uart,
  input  [31:0] int_gpio,
  input  [31:0] int_iic,
  output int_gateout,
  output [31:0] int_code
);

  wire and_1_out, and_2_out, and_3_out, comparator_1_gt, comparator_2_gt, comparator_3_gt, comparator_5_eq,
       comparator_6_eq, comparator_7_eq, en_gpio, en_iic, en_noint, en_uart;
  wire [1:0] en_select;
  wire [31:0] code_cur;

  PullDown #(.Bits(32)) pulldown_1 (.out(int_uart));
  PullDown #(.Bits(32)) pulldown_2 (.out(int_gpio));
  PullDown #(.Bits(32)) pulldown_3 (.out(int_iic));
  PriorityEncoder #(.Selector_Bits(2)) priorityencoder_1 (
    .in0(en_gpio), .in1(en_uart), .in2(en_iic), .in3(1'b0), .num(en_select));  // open: any
  Multiplexer #(.Selector_Bits(2), .Bits(32)) multiplexer_1 (
    .sel(en_select), .in_0(int_gpio), .in_1(int_uart), .in_2(int_iic), .in_3({32{1'b0}}), .out(code_cur));
  Comparator #(.Bits(32)) comparator_1 (.a(int_uart), .b({32{1'b0}}), .gt(comparator_1_gt));  // open: eq, lt
  Comparator #(.Bits(32)) comparator_2 (.a(int_gpio), .b({32{1'b0}}), .gt(comparator_2_gt));  // open: eq, lt
  Comparator #(.Bits(32)) comparator_3 (.a(int_iic), .b({32{1'b0}}), .gt(comparator_3_gt));  // open: eq, lt
  Comparator #(.Bits(32)) comparator_4 (.a(int_code), .b({32{1'b0}}), .eq(en_noint));  // open: gt, lt
  and and_1 (and_1_out, comparator_1_gt, ~int_gate, en_noint);  // And
  Comparator #(.Bits(32)) comparator_5 (.a(int_code), .b(int_uart), .eq(comparator_5_eq));  // open: gt, lt
  and and_2 (and_2_out, comparator_2_gt, ~int_gate, en_noint);  // And
  Comparator #(.Bits(32)) comparator_6 (.a(int_code), .b(int_gpio), .eq(comparator_6_eq));  // open: gt, lt
  and and_3 (and_3_out, comparator_3_gt, ~int_gate, en_noint);  // And
  Comparator #(.Bits(32)) comparator_7 (.a(int_code), .b(int_iic), .eq(comparator_7_eq));  // open: gt, lt
  or or_1 (en_uart, and_1_out, comparator_5_eq);
  or or_2 (en_gpio, and_2_out, comparator_6_eq);
  or or_3 (en_iic, and_3_out, comparator_7_eq);
  PullDown #(.Bits(32)) pulldown_4 (.out(code_cur));
  D_FF #(.Bits(32)) d_ff_1 (.D(code_cur), .C(Clock), .Q(int_code));  // open: nQ
  or or_4 (int_gateout, int_gate, ~en_noint);  // Or

  // Other names for the same wires on the sheet: C = Clock
endmodule
