// Digital circuit int-except-unit.dig as structural Verilog
module int_except_unit (
  input  [31:0] Data_csr,
  input  WE_CSR,
  input  [11:0] Addr_csrw,
  input  Clock,
  input  [11:0] Addr_csr1,
  input  [11:0] Addr_csr2,
  input  [31:0] Exception_code,
  input  [31:0] PC_Addr,
  input  [31:0] PC_ip,
  input  [31:0] PC_next,
  input  mret,
  input  [31:0] mip_in,
  input  mip_en,
  output [31:0] Out_csr1,
  output [31:0] Out_csr2,
  output En_jmp,
  output [31:0] Addr_jmp,
  output [31:0] mip_out,
  output [31:0] mie_out,
  output [31:0] ecode_out,
  output timer_en,
  output [31:0] mepc_out
);

  wire and_1_out, and_6_out, and_7_out, and_8_out, and_10_out, and_11_out, and_12_out, and_13_out,
       and_14_out, and_15_out, Do_intperipheral, Do_intsoft, Do_inttimer, EN_excep, EN_ie, EN_int,
       enter_excep, int_peripheral, int_soft, int_timer, mcause_en, mepc_en, mie_en, mip_en_t, mstatus_en,
       mtval, mtvec_en, not_2_out, or_2_out, or_3_out, or_4_out, raen0, raen1, raen2, raen3, raen4, raen5,
       raen6, raen7, rben0, rben1, rben2, rben3, rben4, rben5, rben6, rben7, WE_common, wen0, wen1, wen2,
       wen3, wen4, wen5, wen6, wen7;
  wire [11:0] Addr_cw;
  wire [30:0] int_code;
  wire [31:0] add_2_s, and_3_out, Data_common, mcause_data, mcause_in, mcause_out, mepc_data, mepc_in,
       mepc_out_t, mie_in, mip_in_t, mstatus_in, mstatus_out, mtval_in, mtval_out, mtvec_in, mtvec_out,
       offset_jmp, Out_cc1, Out_cc2, PC_Addrtmp, PC_nexttmp, vec_offset;

  and and_1 (and_1_out, EN_int, EN_ie);
  not not_1 (EN_excep, Exception_code[0]);
  Register #(.Bits(32)) pcnext_reg (.D(PC_next), .C(Clock), .en(1'b1), .Q(PC_nexttmp));
  Register #(.Bits(32)) pc_reg (.D(PC_Addr), .C(Clock), .en(1'b1), .Q(PC_Addrtmp));
  or or_1 (EN_int, int_soft, int_timer, int_peripheral);
  or or_2 (or_2_out, EN_excep, and_1_out);
  PullUp #(.Bits(32)) pullup_1 (.out(Exception_code));
  and and_2 (enter_excep, or_2_out, ~mret);  // And
  csr_addr_spliter csr_addr_spliter_1 (
    .Addr_csr(Addr_csr1), .Out_0(raen0), .Out_1(raen1), .Out_2(raen2), .Out_3(raen3), .Out_4(raen4),
    .Out_5(raen5), .Out_6(raen6), .Out_7(raen7));
  csr_addr_spliter csr_addr_spliter_2 (
    .Addr_csr(Addr_csrw), .Out_0(wen0), .Out_1(wen1), .Out_2(wen2), .Out_3(wen3), .Out_4(wen4), .Out_5(wen5),
    .Out_6(wen6), .Out_7(wen7));
  assign {and_3_out[31:12], int_peripheral, and_3_out[10:8], int_timer, and_3_out[6:4], int_soft, and_3_out[2:0]} = mie_out & mip_out;  // And and_3, 32 bits wide
  Register #(.Bits(32)) mstatus (
    .D(mstatus_in), .C(Clock), .en(mstatus_en), .Q({mstatus_out[31:4], EN_ie, mstatus_out[2:0]}));
  PullDown pulldown_1 (.out(mstatus_en));
  and and_4 (Do_intperipheral, ~EN_excep, EN_ie, int_peripheral);  // And
  assign mstatus_in = enter_excep ? {mstatus_out[31:8], EN_ie, mstatus_out[6:4], 1'b0, mstatus_out[2:0]} : 32'bz;  // Driver driver_1
  assign mtval_in = enter_excep ? PC_ip : 32'bz;  // Driver driver_2
  assign mstatus_in = mret ? {mstatus_out[31:8], 1'b1, mstatus_out[6:4], mstatus_out[7], mstatus_out[2:0]} : 32'bz;  // Driver driver_3
  assign Out_csr1 = raen0 ? Out_cc1 : 32'bz;  // Driver driver_4
  assign Out_csr1 = raen2 ? mie_out : 32'bz;  // Driver driver_5
  assign Out_csr1 = raen4 ? mepc_out_t : 32'bz;  // Driver driver_6
  assign Out_csr1 = raen6 ? mtval_out : 32'bz;  // Driver driver_7
  assign Data_common = wen0 ? Data_csr : 32'bz;  // Driver driver_8
  assign mstatus_in = wen1 ? Data_csr : 32'bz;  // Driver driver_9
  assign mtvec_in = wen3 ? Data_csr : 32'bz;  // Driver driver_10
  assign mcause_in = wen5 ? Data_csr : 32'bz;  // Driver driver_11
  Register #(.Bits(32)) mie (.D(mie_in), .C(Clock), .en(mie_en), .Q(mie_out));
  PullDown pulldown_2 (.out(mie_en));
  assign mstatus_en = enter_excep ? 1'b1 : 1'bz;  // Driver driver_12
  assign mtval = enter_excep ? 1'b1 : 1'bz;  // Driver driver_13
  assign mstatus_en = mret ? 1'b1 : 1'bz;  // Driver driver_14
  assign Out_csr1 = raen1 ? {mstatus_out[31:4], EN_ie, mstatus_out[2:0]} : 32'bz;  // Driver driver_15
  assign Out_csr1 = raen3 ? mtvec_out : 32'bz;  // Driver driver_16
  assign Out_csr1 = raen5 ? mcause_out : 32'bz;  // Driver driver_17
  assign Out_csr1 = raen7 ? mip_out : 32'bz;  // Driver driver_18
  Register #(.Bits(32)) mtvec (.D(mtvec_in), .C(Clock), .en(mtvec_en), .Q(mtvec_out));
  PullDown pulldown_3 (.out(mtvec_en));
  LookUpTable #(.Bits(31)) lookuptable_1 (.in0(int_soft), .in1(int_timer), .in2(int_peripheral), .out(int_code));
  and and_5 (Do_intsoft, ~EN_excep, ~Do_intperipheral, EN_ie, int_soft);  // And
  and and_6 (and_6_out, ~mtvec_out[0], enter_excep);  // And
  assign mcause_in = enter_excep ? mcause_data : 32'bz;  // Driver driver_19
  assign WE_common = wen0 ? WE_CSR : 1'bz;  // Driver driver_20
  assign mstatus_en = wen1 ? WE_CSR : 1'bz;  // Driver driver_21
  assign mtvec_en = wen3 ? WE_CSR : 1'bz;  // Driver driver_22
  assign mcause_en = wen5 ? WE_CSR : 1'bz;  // Driver driver_23
  assign mepc_in = enter_excep ? mepc_data : 32'bz;  // Driver driver_24
  Register #(.Bits(32)) mepc (.D(mepc_in), .C(Clock), .en(mepc_en), .Q(mepc_out_t));
  PullDown pulldown_4 (.out(mepc_en));
  or or_3 (or_3_out, EN_excep, and_6_out);
  assign mcause_en = enter_excep ? 1'b1 : 1'bz;  // Driver driver_25
  assign Addr_jmp = mret ? mepc_out_t : 32'bz;  // Driver driver_26
  assign Addr_cw = wen0 ? Addr_csrw : 12'bz;  // Driver driver_27
  and and_7 (and_7_out, EN_excep, enter_excep);
  and and_8 (and_8_out, or_3_out, ~mret);  // And
  assign mepc_en = enter_excep ? 1'b1 : 1'bz;  // Driver driver_28
  csr_addr_spliter csr_addr_spliter_3 (
    .Addr_csr(Addr_csr2), .Out_0(rben0), .Out_1(rben1), .Out_2(rben2), .Out_3(rben3), .Out_4(rben4),
    .Out_5(rben5), .Out_6(rben6), .Out_7(rben7));
  assign mie_in = wen2 ? Data_csr : 32'bz;  // Driver driver_29
  assign mepc_in = wen4 ? Data_csr : 32'bz;  // Driver driver_30
  assign mtval_in = wen6 ? Data_csr : 32'bz;  // Driver driver_31
  Register #(.Bits(32)) mcause (.D(mcause_in), .C(Clock), .en(mcause_en), .Q(mcause_out));
  PullDown pulldown_5 (.out(mcause_en));
  assign mcause_data = and_7_out ? {1'b0, Exception_code[31:1]} : 32'bz;  // Driver driver_32
  and and_9 (Do_inttimer, ~EN_excep, ~Do_intsoft, ~Do_intperipheral, EN_ie, int_timer);  // And
  assign Addr_jmp = and_8_out ? {mtvec_out[31:2], 2'b00} : 32'bz;  // Driver driver_33
  and and_10 (and_10_out, EN_excep, enter_excep);
  Add #(.Bits(32)) add_1 (.a({mtvec_out[31:2], 2'b00}), .b(offset_jmp), .c_i(1'b0), .s(vec_offset));  // open: c_o
  assign mie_en = wen2 ? WE_CSR : 1'bz;  // Driver driver_34
  assign mepc_en = wen4 ? WE_CSR : 1'bz;  // Driver driver_35
  assign mtval = wen6 ? WE_CSR : 1'bz;  // Driver driver_36
  Register #(.Bits(32)) u_mtval (.D(mtval_in), .C(Clock), .en(mtval), .Q(mtval_out));
  PullDown pulldown_6 (.out(mtval));
  assign mip_in_t = mip_en ? mip_in : 32'bz;  // Driver driver_37
  assign Out_csr2 = rben6 ? mtval_out : 32'bz;  // Driver driver_38
  assign mepc_data = and_10_out ? PC_Addrtmp : 32'bz;  // Driver driver_39
  and and_11 (and_11_out, Do_intperipheral, mtvec_out[0], ~mret);  // And
  and and_12 (and_12_out, Do_inttimer, mtvec_out[0], ~mret);  // And
  assign mip_en_t = mip_en ? 1'b1 : 1'bz;  // Driver driver_40
  assign Out_csr2 = rben0 ? Out_cc2 : 32'bz;  // Driver driver_41
  assign Out_csr2 = rben2 ? mie_out : 32'bz;  // Driver driver_42
  assign Out_csr2 = rben4 ? mepc_out_t : 32'bz;  // Driver driver_43
  Register #(.Bits(32)) mip (.D(mip_in_t), .C(Clock), .en(mip_en_t), .Q(mip_out));
  PullDown pulldown_7 (.out(mip_en_t));
  not not_2 (not_2_out, EN_excep);
  assign Addr_jmp = and_11_out ? vec_offset : 32'bz;  // Driver driver_44
  and and_13 (and_13_out, Do_intsoft, mtvec_out[0], ~mret);  // And
  and and_14 (and_14_out, not_2_out, enter_excep);
  assign Addr_jmp = and_13_out ? vec_offset : 32'bz;  // Driver driver_45
  assign Addr_jmp = and_12_out ? vec_offset : 32'bz;  // Driver driver_46
  assign Out_csr2 = rben1 ? {mstatus_out[31:4], EN_ie, mstatus_out[2:0]} : 32'bz;  // Driver driver_47
  assign Out_csr2 = rben3 ? mtvec_out : 32'bz;  // Driver driver_48
  assign Out_csr2 = rben5 ? mcause_out : 32'bz;  // Driver driver_49
  assign Out_csr2 = rben7 ? mip_out : 32'bz;  // Driver driver_50
  assign mcause_data = and_14_out ? {1'b1, int_code} : 32'bz;  // Driver driver_51
  assign offset_jmp = and_11_out ? 32'h2c : 32'bz;  // Driver driver_52
  RegisterFile #(.AddrBits(12), .Bits(32)) CSR_Registers (
    .Din(Data_common), .we(WE_common), .Rw(Addr_cw), .C(Clock), .Ra(Addr_csr1), .Rb(Addr_csr2), .Da(Out_cc1),
    .Db(Out_cc2));
  and and_15 (and_15_out, not_2_out, enter_excep);
  assign offset_jmp = and_13_out ? 32'hc : 32'bz;  // Driver driver_53
  assign offset_jmp = and_12_out ? 32'h1c : 32'bz;  // Driver driver_54
  assign mepc_data = and_15_out ? PC_nexttmp : 32'bz;  // Driver driver_55
  or or_4 (or_4_out, enter_excep, mret);
  Add #(.Bits(32)) add_2 (.a(mepc_out), .b(32'h1), .c_i(1'b0), .s(add_2_s));  // open: c_o
  and and_16 (En_jmp, or_4_out, 1'b1);
  PullDown #(.Bits(32)) pulldown_8 (.out(Addr_jmp));
  Register #(.Bits(32)) register_1 (.D(add_2_s), .C(Clock), .en(enter_excep), .Q(mepc_out));

  assign ecode_out = Exception_code;
  assign timer_en = mret;

  // Other names for the same wires on the sheet: c = Clock; excep_code[30:0] = Exception_code[31:1];
  //   mip_set[31:0] = mip_in; mip_seten = mip_en; mstatus_out[3] = EN_ie; vec_mode = mtvec_out[0];
  //   vec_base[31:2] = mtvec_out[31:2]

  // Notes on the sheet:
  //   contents of lookuptable_1 (hex, n*v repeats v):
  //   0,3,7,0,b
endmodule
