// Digital circuit mechine-op-unit.dig as structural Verilog
module mechine_op_unit (
  input  [7:0] mechine_op,
  output mret
);


  assign mret = mechine_op[2];

  // Other names for the same wires on the sheet: ebreak = mechine_op[0]; ecall = mechine_op[1];
  //   sfence_vma = mechine_op[3]; sret = mechine_op[4]; wfi = mechine_op[5]; fence = mechine_op[6];
  //   fence_i = mechine_op[7]
endmodule
