// Digital circuit memory-operation-unit.dig as structural Verilog
module memory_operation_unit (
  input  [8:0] MemOp_in,
  input  [31:0] Data_in,
  input  [31:0] rs1,
  input  [31:0] rs2,
  input  [11:0] Offset_12,
  input  [6:0] Offset_7,
  input  [4:0] Offset_5,
  input  [19:0] imm_20,
  output we_out,
  output [31:0] Addr_out,
  output [31:0] Mem_out,
  output [3:0] StoreByteSize_out,
  output oe_out,
  output RegWE_out,
  output [31:0] rd_out
);

  wire not_1_out, or_1_out;
  wire [31:0] add_1_s, and_2_out, barrelshifter_1_out, bitextender_1_out, bitextender_2_out,
       bitextender_3_out, bitextender_4_out, bitextender_5_out, bitextender_6_out, bitextender_7_out,
       bitextender_8_out, bitextender_9_out, offset;

  PullDown pulldown_1 (.out(we_out));
  assign we_out = MemOp_in[1] ? 1'b0 : 1'bz;  // Driver driver_1
  assign we_out = MemOp_in[4] ? 1'b0 : 1'bz;  // Driver driver_2
  assign we_out = MemOp_in[2] ? 1'b0 : 1'bz;  // Driver driver_3
  assign we_out = MemOp_in[5] ? 1'b0 : 1'bz;  // Driver driver_4
  assign we_out = MemOp_in[3] ? 1'b0 : 1'bz;  // Driver driver_5
  or or_1 (or_1_out, MemOp_in[0], MemOp_in[1], MemOp_in[2], MemOp_in[3], MemOp_in[4], MemOp_in[5]);
  PullDown pulldown_2 (.out(we_out));
  BitExtender #(.inputBits(12), .outputBits(32)) bitextender_1 (.in(Offset_12), .out(bitextender_1_out));
  BitExtender #(.inputBits(12), .outputBits(32)) bitextender_2 (.in(Offset_12), .out(bitextender_2_out));
  BitExtender #(.inputBits(12), .outputBits(32)) bitextender_3 (.in(Offset_12), .out(bitextender_3_out));
  not not_1 (not_1_out, we_out);
  assign offset = MemOp_in[1] ? bitextender_1_out : 32'bz;  // Driver driver_6
  assign offset = MemOp_in[4] ? {{20{1'b0}}, Offset_12} : 32'bz;  // Driver driver_7
  assign offset = MemOp_in[2] ? bitextender_2_out : 32'bz;  // Driver driver_8
  assign offset = MemOp_in[5] ? {{20{1'b0}}, Offset_12} : 32'bz;  // Driver driver_9
  assign offset = MemOp_in[3] ? bitextender_3_out : 32'bz;  // Driver driver_10
  and and_1 (oe_out, or_1_out, not_1_out);
  assign StoreByteSize_out = MemOp_in[1] ? 4'b0001 : 4'bz;  // Driver driver_11
  assign StoreByteSize_out = MemOp_in[4] ? 4'b0001 : 4'bz;  // Driver driver_12
  assign StoreByteSize_out = MemOp_in[2] ? 4'b0011 : 4'bz;  // Driver driver_13
  assign StoreByteSize_out = MemOp_in[5] ? 4'b0011 : 4'bz;  // Driver driver_14
  assign StoreByteSize_out = MemOp_in[3] ? 4'b1111 : 4'bz;  // Driver driver_15
  assign rd_out = MemOp_in[3] ? Data_in : 32'bz;  // Driver driver_16
  BitExtender #(.outputBits(32)) bitextender_4 (.in(Data_in[7:0]), .out(bitextender_4_out));
  BitExtender #(.inputBits(16), .outputBits(32)) bitextender_5 (.in(Data_in[15:0]), .out(bitextender_5_out));
  assign rd_out = MemOp_in[1] ? bitextender_4_out : 32'bz;  // Driver driver_17
  assign rd_out = MemOp_in[4] ? {{24{1'b0}}, Data_in[7:0]} : 32'bz;  // Driver driver_18
  assign rd_out = MemOp_in[2] ? bitextender_5_out : 32'bz;  // Driver driver_19
  assign rd_out = MemOp_in[5] ? {{16{1'b0}}, Data_in[15:0]} : 32'bz;  // Driver driver_20
  assign we_out = MemOp_in[0] ? 1'b0 : 1'bz;  // Driver driver_21
  BitExtender #(.inputBits(20), .outputBits(32)) bitextender_6 (.in(imm_20), .out(bitextender_6_out));
  assign we_out = MemOp_in[6] ? 1'b1 : 1'bz;  // Driver driver_22
  assign we_out = MemOp_in[7] ? 1'b1 : 1'bz;  // Driver driver_23
  assign we_out = MemOp_in[8] ? 1'b1 : 1'bz;  // Driver driver_24
  Add #(.Bits(32)) add_1 (.a(rs1), .b(offset), .c_i(1'b0), .s(add_1_s));  // open: c_o
  BarrelShifter #(.Bits(32)) barrelshifter_1 (.in(bitextender_6_out), .shift(6'b001100), .out(barrelshifter_1_out));
  assign and_2_out = barrelshifter_1_out & 32'hfffff00;  // And and_2, 32 bits wide
  Add #(.Bits(32)) add_2 (.a(rs1), .b(offset), .c_i(1'b0), .s(Addr_out));  // open: c_o
  BitExtender #(.inputBits(12), .outputBits(32)) bitextender_7 (.in({Offset_7, Offset_5}), .out(bitextender_7_out));
  BitExtender #(.inputBits(12), .outputBits(32)) bitextender_8 (.in({Offset_7, Offset_5}), .out(bitextender_8_out));
  BitExtender #(.inputBits(12), .outputBits(32)) bitextender_9 (.in({Offset_7, Offset_5}), .out(bitextender_9_out));
  assign rd_out = MemOp_in[0] ? add_1_s : 32'bz;  // Driver driver_25
  assign offset = MemOp_in[6] ? bitextender_7_out : 32'bz;  // Driver driver_26
  assign offset = MemOp_in[7] ? bitextender_8_out : 32'bz;  // Driver driver_27
  assign offset = MemOp_in[8] ? bitextender_9_out : 32'bz;  // Driver driver_28
  assign offset = MemOp_in[0] ? and_2_out : 32'bz;  // Driver driver_29
  assign StoreByteSize_out = MemOp_in[6] ? 4'b0001 : 4'bz;  // Driver driver_30
  assign StoreByteSize_out = MemOp_in[7] ? 4'b0011 : 4'bz;  // Driver driver_31
  assign StoreByteSize_out = MemOp_in[8] ? 4'b1111 : 4'bz;  // Driver driver_32
  assign StoreByteSize_out = MemOp_in[0] ? 4'b0000 : 4'bz;  // Driver driver_33

  assign Mem_out = rs2;
  assign RegWE_out = oe_out;

  // Other names for the same wires on the sheet: Addr[31:0] = Addr_out; bytesize[3:0] = StoreByteSize_out;
  //   b[7:0] = Data_in[7:0]; h[15:0] = Data_in[15:0]; w[31:0] = Data_in; dataout[31:0] = rd_out; lui = MemOp_in[0];
  //   lb = MemOp_in[1]; lh = MemOp_in[2]; lw = MemOp_in[3]; lbu = MemOp_in[4]; lhu = MemOp_in[5]; sb = MemOp_in[6];
  //   sh = MemOp_in[7]; sw = MemOp_in[8]; oe = oe_out; we = we_out
endmodule
