// Digital circuit memory.dig as structural Verilog
module memory (
  input  [31:0] Addr,
  input  [31:0] Data_in,
  input  WE,
  input  OE,
  input  [3:0] ByteSize_in,
  input  Clock,
  input  [31:0] Addr_PC,
  input  OE_PC,
  output [31:0] Data_out,
  output [31:0] DataPC_out
);

  wire and_1_out, and_2_out, and_3_out, and_4_out, and_5_out, and_6_out, and_7_out, and_8_out, and_9_out,
       and_10_out, and_11_out, and_12_out, and_13_out, and_14_out, and_15_out, and_16_out, cs0, cs0_pc, cs1,
       cs1_pc, cs2, cs2_pc, cs3, cs3_pc, we0, we1, we2, we3;
  wire [7:0] byte0, byte0_pc, byte1, byte1_pc, byte2, byte2_pc, byte3, byte3_pc, data0, data0_pc, data1,
       data1_pc, data2, data2_pc, data3, data3_pc;

  assign {byte3, byte2, byte1, byte0} = WE ? Data_in : 32'bz;  // Driver driver_1
  PullDown pulldown_1 (.out(WE));
  assign Data_out = OE ? {byte3, byte2, byte1, byte0} : 32'bz;  // Driver driver_2
  Decoder #(.Selector_Bits(2)) decoder_1 (.sel(Addr[1:0]), .out_0(cs0), .out_1(cs1), .out_2(cs2), .out_3(cs3));
  and and_1 (and_1_out, WE, cs0);
  and and_2 (and_2_out, OE, cs0);
  and and_3 (and_3_out, WE, cs0);
  PullDown pulldown_2 (.out(we0));
  RAMDualAccess #(.AddrBits(24), .Bits(8)) ramdualaccess_1 (
    .str(we0), .C(Clock), .ld(OE), .A1(Addr[25:2]), .Din1(data0), .A2(Addr_PC[25:2]), .D1(data0),
    .D2(data0_pc));
  assign data0 = and_1_out ? byte0 : 8'bz;  // Driver driver_3
  assign data1 = and_1_out ? byte1 : 8'bz;  // Driver driver_4
  assign data2 = and_1_out ? byte2 : 8'bz;  // Driver driver_5
  assign data3 = and_1_out ? byte3 : 8'bz;  // Driver driver_6
  assign byte0 = and_2_out ? data0 : 8'bz;  // Driver driver_7
  assign byte1 = and_2_out ? data1 : 8'bz;  // Driver driver_8
  assign byte2 = and_2_out ? data2 : 8'bz;  // Driver driver_9
  assign byte3 = and_2_out ? data3 : 8'bz;  // Driver driver_10
  assign we0 = and_3_out ? ByteSize_in[0] : 1'bz;  // Driver driver_11
  assign we1 = and_3_out ? ByteSize_in[1] : 1'bz;  // Driver driver_12
  assign we2 = and_3_out ? ByteSize_in[2] : 1'bz;  // Driver driver_13
  assign we3 = and_3_out ? ByteSize_in[3] : 1'bz;  // Driver driver_14
  PullDown pulldown_3 (.out(we1));
  RAMDualAccess #(.AddrBits(24), .Bits(8)) ramdualaccess_2 (
    .str(we1), .C(Clock), .ld(OE), .A1(Addr[25:2]), .Din1(data1), .A2(Addr_PC[25:2]), .D1(data1),
    .D2(data1_pc));
  and and_4 (and_4_out, WE, cs1);
  and and_5 (and_5_out, OE, cs1);
  and and_6 (and_6_out, WE, cs1);
  assign data1 = and_4_out ? byte0 : 8'bz;  // Driver driver_15
  assign data2 = and_4_out ? byte1 : 8'bz;  // Driver driver_16
  assign data3 = and_4_out ? byte2 : 8'bz;  // Driver driver_17
  assign data0 = and_4_out ? byte3 : 8'bz;  // Driver driver_18
  assign byte0 = and_5_out ? data1 : 8'bz;  // Driver driver_19
  assign byte1 = and_5_out ? data2 : 8'bz;  // Driver driver_20
  assign byte2 = and_5_out ? data3 : 8'bz;  // Driver driver_21
  assign byte3 = and_5_out ? data0 : 8'bz;  // Driver driver_22
  assign we1 = and_6_out ? ByteSize_in[0] : 1'bz;  // Driver driver_23
  assign we2 = and_6_out ? ByteSize_in[1] : 1'bz;  // Driver driver_24
  assign we3 = and_6_out ? ByteSize_in[2] : 1'bz;  // Driver driver_25
  assign we0 = and_6_out ? ByteSize_in[3] : 1'bz;  // Driver driver_26
  PullDown pulldown_4 (.out(we2));
  RAMDualAccess #(.AddrBits(24), .Bits(8)) ramdualaccess_3 (
    .str(we2), .C(Clock), .ld(OE), .A1(Addr[25:2]), .Din1(data2), .A2(Addr_PC[25:2]), .D1(data2),
    .D2(data2_pc));
  and and_7 (and_7_out, WE, cs2);
  and and_8 (and_8_out, OE, cs2);
  and and_9 (and_9_out, WE, cs2);
  assign data2 = and_7_out ? byte0 : 8'bz;  // Driver driver_27
  assign data3 = and_7_out ? byte1 : 8'bz;  // Driver driver_28
  assign data0 = and_7_out ? byte2 : 8'bz;  // Driver driver_29
  assign data1 = and_7_out ? byte3 : 8'bz;  // Driver driver_30
  assign byte0 = and_8_out ? data2 : 8'bz;  // Driver driver_31
  assign byte1 = and_8_out ? data3 : 8'bz;  // Driver driver_32
  assign byte2 = and_8_out ? data0 : 8'bz;  // Driver driver_33
  assign byte3 = and_8_out ? data1 : 8'bz;  // Driver driver_34
  assign we2 = and_9_out ? ByteSize_in[0] : 1'bz;  // Driver driver_35
  assign we3 = and_9_out ? ByteSize_in[1] : 1'bz;  // Driver driver_36
  assign we0 = and_9_out ? ByteSize_in[2] : 1'bz;  // Driver driver_37
  assign we1 = and_9_out ? ByteSize_in[3] : 1'bz;  // Driver driver_38
  PullDown pulldown_5 (.out(we3));
  RAMDualAccess #(.AddrBits(24), .Bits(8)) ramdualaccess_4 (
    .str(we3), .C(Clock), .ld(OE), .A1(Addr[25:2]), .Din1(data3), .A2(Addr_PC[25:2]), .D1(data3),
    .D2(data3_pc));
  and and_10 (and_10_out, WE, cs3);
  and and_11 (and_11_out, OE, cs3);
  and and_12 (and_12_out, WE, cs3);
  assign data3 = and_10_out ? byte0 : 8'bz;  // Driver driver_39
  assign data0 = and_10_out ? byte1 : 8'bz;  // Driver driver_40
  assign data1 = and_10_out ? byte2 : 8'bz;  // Driver driver_41
  assign data2 = and_10_out ? byte3 : 8'bz;  // Driver driver_42
  assign byte0 = and_11_out ? data3 : 8'bz;  // Driver driver_43
  assign byte1 = and_11_out ? data0 : 8'bz;  // Driver driver_44
  assign byte2 = and_11_out ? data1 : 8'bz;  // Driver driver_45
  assign byte3 = and_11_out ? data2 : 8'bz;  // Driver driver_46
  assign we3 = and_12_out ? ByteSize_in[0] : 1'bz;  // Driver driver_47
  assign we0 = and_12_out ? ByteSize_in[1] : 1'bz;  // Driver driver_48
  assign we1 = and_12_out ? ByteSize_in[2] : 1'bz;  // Driver driver_49
  assign we2 = and_12_out ? ByteSize_in[3] : 1'bz;  // Driver driver_50
  and and_13 (and_13_out, OE_PC, cs0_pc);
  assign byte0_pc = and_13_out ? data0_pc : 8'bz;  // Driver driver_51
  assign byte1_pc = and_13_out ? data1_pc : 8'bz;  // Driver driver_52
  assign byte2_pc = and_13_out ? data2_pc : 8'bz;  // Driver driver_53
  assign byte3_pc = and_13_out ? data3_pc : 8'bz;  // Driver driver_54
  Decoder #(.Selector_Bits(2)) decoder_2 (
    .sel(Addr_PC[1:0]), .out_0(cs0_pc), .out_1(cs1_pc), .out_2(cs2_pc), .out_3(cs3_pc));
  and and_14 (and_14_out, OE_PC, cs1_pc);
  assign byte0_pc = and_14_out ? data1_pc : 8'bz;  // Driver driver_55
  assign byte1_pc = and_14_out ? data2_pc : 8'bz;  // Driver driver_56
  assign byte2_pc = and_14_out ? data3_pc : 8'bz;  // Driver driver_57
  assign byte3_pc = and_14_out ? data0_pc : 8'bz;  // Driver driver_58
  and and_15 (and_15_out, OE_PC, cs2_pc);
  assign byte0_pc = and_15_out ? data2_pc : 8'bz;  // Driver driver_59
  assign byte1_pc = and_15_out ? data3_pc : 8'bz;  // Driver driver_60
  assign byte2_pc = and_15_out ? data0_pc : 8'bz;  // Driver driver_61
  assign byte3_pc = and_15_out ? data1_pc : 8'bz;  // Driver driver_62
  assign DataPC_out = OE_PC ? {byte3_pc, byte2_pc, byte1_pc, byte0_pc} : 32'bz;  // Driver driver_63
  and and_16 (and_16_out, OE_PC, cs3_pc);
  assign byte0_pc = and_16_out ? data3_pc : 8'bz;  // Driver driver_64
  assign byte1_pc = and_16_out ? data0_pc : 8'bz;  // Driver driver_65
  assign byte2_pc = and_16_out ? data1_pc : 8'bz;  // Driver driver_66
  assign byte3_pc = and_16_out ? data2_pc : 8'bz;  // Driver driver_67

  // Other names for the same wires on the sheet: addr_sub[23:0] = Addr[25:2]; addr_sub_pc[23:0] = Addr_PC[25:2];
  //   _1byte = ByteSize_in[0]; _2byte = ByteSize_in[1]; _3byte = ByteSize_in[2]; _4byte = ByteSize_in[3]; c = Clock;
  //   data[31:0] = Data_out; data_pc[31:0] = DataPC_out
endmodule
