// Digital circuit risc-v-mcu.dig as structural Verilog
module risc_v_mcu (
  input  Clock,
  input  TimerClock,
  input  UartClock,
  input  IICClock,
  input  GPIO_in1,
  input  GPIO_in2,
  input  GPIO_in3,
  input  GPIO_in4,
  input  GPIO_in5,
  input  GPIO_in6,
  input  GPIO_in7,
  input  GPIO_in8,
  input  GPIO_in9,
  input  GPIO_in10,
  input  RX,
  input  SDA_in,
  input  [7:0] ssd_bytein,
  output GPIO_1,
  output GPIO_2,
  output GPIO_3,
  output GPIO_4,
  output GPIO_5,
  output GPIO_6,
  output GPIO_7,
  output GPIO_8,
  output GPIO_9,
  output GPIO_10,
  output TX,
  output SDA_out,
  output SCL,
  output [23:0] Addr_ssd,
  output ssd_en,
  output [31:0] ddd
);

  wire addrflag_boot, addrflag_mem, addrflag_memtmp, addrflag_peripheral, addrflag_ssd, and_4_out, ard_en,
       comparator_1_eq, crd_en, Cust_op, int_gatesrc, int_peripheral, int_timer, jrd_en, lrd_en, memgpio_en,
       memiic_en, memplic_en, memuart_en, mip_seten, mret, nor_1_out, not_1_out, Oe_dma, Oe_mem, Oe_memop,
       or_3_out, PC_except, PC_inited, PC_jmp, PC_jmpen, rd_en, We_dma, We_mem;
  wire [3:0] storebytes_size;
  wire [4:0] driver_17_out, rd, rs1, rs2;
  wire [5:0] csr_op;
  wire [6:0] imm_7;
  wire [7:0] mechine_op;
  wire [8:0] jmp_op, mem_op;
  wire [11:0] Addr_csr1, imm_12;
  wire [18:0] alu_op;
  wire [19:0] imm_20;
  wire [23:0] addr_real;
  wire [29:24] mem_addr;
  wire [30:24] PC_exec;
  wire [31:0] Addr_except, Addr_jmp, Addr_jmpto, ard_out, crd_out, Data_csr, data_dma, data_mem,
       data_memgpio, data_memiic, data_memplic, data_memrd, data_memrdin, data_memuart, dma_addr,
       instruction_code, int_gpiocode, int_iiccode, int_peripheralcode, int_uartcode, Invalid_op, IR_q,
       jrd_out, lrd_out, mip_cur, mip_set, Out_csr1, Out_csr2, PC_next, PC_pc_next, rd_out, rs1_data,
       rs2_data;

  nor nor_1 (nor_1_out, addrflag_peripheral, addrflag_ssd);
  and and_1 (ssd_en, addrflag_ssd, ~Oe_dma, Oe_memop);  // And
  and and_2 (Oe_mem, nor_1_out, Oe_memop);
  and and_3 (Oe_dma, addrflag_ssd, addrflag_peripheral, Oe_memop);
  or or_1 (PC_jmpen, PC_jmp, PC_except);
  and and_4 (and_4_out, PC_jmp, ~PC_except);  // And
  or or_2 (rd_en, jrd_en, ard_en, crd_en, lrd_en);
  assign data_memrdin = memplic_en ? data_memplic : 32'bz;  // Driver driver_1
  assign data_memrdin = memgpio_en ? data_memgpio : 32'bz;  // Driver driver_2
  assign Addr_jmpto = and_4_out ? Addr_jmp : 32'bz;  // Driver driver_3
  assign data_memrdin = memuart_en ? data_memuart : 32'bz;  // Driver driver_4
  not not_1 (not_1_out, PC_inited);
  assign data_memrdin = ssd_en ? {{24{1'b0}}, ssd_bytein} : 32'bz;  // Driver driver_5
  assign data_memrdin = or_3_out ? data_memrd : 32'bz;  // Driver driver_6
  assign {addrflag_boot, PC_exec[30:26], addrflag_memtmp, PC_exec[24], addr_real} = not_1_out ? 32'h80000000 : 32'bz;  // Driver driver_7
  assign Addr_jmpto = PC_except ? Addr_except : 32'bz;  // Driver driver_8
  assign rd_out = jrd_en ? jrd_out : 32'bz;  // Driver driver_9
  assign rd_out = ard_en ? ard_out : 32'bz;  // Driver driver_10
  assign rd_out = crd_en ? crd_out : 32'bz;  // Driver driver_11
  assign rd_out = lrd_en ? lrd_out : 32'bz;  // Driver driver_12
  assign data_memrdin = memiic_en ? data_memiic : 32'bz;  // Driver driver_13
  or or_3 (or_3_out, Oe_dma, Oe_mem);
  assign PC_next = not_1_out ? 32'h80000004 : 32'bz;  // Driver driver_14
  program_counter PC (
    .En(1'b1), .Clock(Clock),
    .Addr_set({addrflag_boot, PC_exec[30:26], addrflag_memtmp, PC_exec[24], addr_real}),
    .Addr_jmp(Addr_jmpto), .En_jmp(PC_jmpen), .PC_next(PC_pc_next));
  assign PC_next = PC_inited ? PC_pc_next : 32'bz;  // Driver driver_15
  mechine_op_unit mechine_op_unit_1 (.mechine_op(mechine_op), .mret(mret));
  cust_ctrl cust_ctrl_1 (.op_code(instruction_code), .cust_code(Cust_op), .Clock(Clock), .PC_init(PC_inited));
  csr csr_1 (
    .CSRCode_in(csr_op), .Data_in(rs1_data), .Csr_Addr(imm_12), .Imm5_in(rs1), .Clock(Clock),
    .Data_temp(Out_csr1), .En(crd_en), .Addr_csr(Addr_csr1), .Out_rd(crd_out), .Out_csr(Data_csr));
  Register #(.Bits(32)) IR (.D(PC_next), .C(Clock), .en(1'b1), .Q(IR_q));
  assign {addrflag_boot, PC_exec[30:26], addrflag_memtmp, PC_exec[24], addr_real} = PC_inited ? IR_q : 32'bz;  // Driver driver_16
  instuction_jump_unit instuction_jump_unit_1 (
    .jmp_op(jmp_op), .PC_cur({addrflag_boot, PC_exec[30:26], addrflag_memtmp, PC_exec[24], addr_real}),
    .PC_next(PC_next), .rs1_in(rs1_data), .rs2_in(rs2_data), .Imm12_in(imm_12), .Imm20_in(imm_20),
    .Imm7_in(imm_7), .offset_5(rd), .Addr_jmp(Addr_jmp), .rd_out(jrd_out), .EN_out(jrd_en), .En_jmp(PC_jmp));
  memory_operation_unit memory_operation_unit_1 (
    .MemOp_in(mem_op), .Data_in(data_memrdin), .rs1(rs1_data), .rs2(rs2_data), .Offset_12(imm_12),
    .Offset_7(imm_7), .Offset_5(rd), .imm_20(imm_20), .we_out(We_mem),
    .Addr_out({addrflag_peripheral, addrflag_ssd, mem_addr, Addr_ssd}), .Mem_out(data_mem),
    .StoreByteSize_out(storebytes_size), .oe_out(Oe_memop), .RegWE_out(lrd_en), .rd_out(lrd_out));
  alu alu_1 (
    .Alu_in(alu_op), .rs1_in(rs1_data), .rs2_in(rs2_data), .Imm12_in(imm_12), .Clock(Clock),
    .rd_out(ard_out), .EN_out(ard_en), .InvlidOP_out(Invalid_op));
  instruction_decoder instruction_decoder_1 (
    .Instruction_In(instruction_code), .EN(1'b1), .mechie_op(mechine_op), .rd(rd), .rs1(rs1), .rs2(rs2),
    .imm_2531(imm_7), .imm_1231(imm_20), .imm_2032(imm_12), .invalid(Invalid_op), .csr_op(csr_op),
    .jmp_op(jmp_op), .alu_op(alu_op), .SL_op(mem_op), .Cust_op(Cust_op));
  and and_5 (addrflag_mem, addrflag_memtmp, ~addrflag_boot);  // And
  PLIC plic_1 (
    .Clock(Clock), .TimerClock(TimerClock), .Addr_w({addrflag_peripheral, addrflag_ssd, mem_addr, Addr_ssd}),
    .Data_in(data_mem), .WE(We_mem), .Addr_r1({addrflag_peripheral, addrflag_ssd, mem_addr, Addr_ssd}),
    .mip_in(mip_cur), .perint_code(int_peripheralcode), .Out_ra(data_memplic), .Out_en(memplic_en),
    .mip_set(mip_set), .mip_seten(mip_seten), .int_timer(int_timer), .gate_peripheral(int_gatesrc));  // open: mtimcmp, mtime
  assign driver_17_out = rd_en ? rd : 5'bz;  // Driver driver_17
  risc_v_registers Common_Regs (
    .OE_P1(rs1), .Din(rd_out), .Clock(Clock), .WE(driver_17_out), .OE_P2(rs2), .OE_P3({5{1'b0}}),
    .Output_P1(rs1_data), .Output_P2(rs2_data));  // open: Output_P3
  boot_rom Boot_Rom (.Addr(addr_real), .En(addrflag_boot), .Out_code(instruction_code));
  memory Momery (
    .Addr(dma_addr), .Data_in(data_dma), .WE(We_dma), .OE(1'b0), .ByteSize_in(4'b0001), .Clock(Clock),
    .Addr_PC({addrflag_peripheral, addrflag_ssd, mem_addr, Addr_ssd}), .OE_PC(Oe_dma), .DataPC_out(data_memrd));  // open: Data_out
  int_except_unit int_except_unit_1 (
    .Data_csr(Data_csr), .WE_CSR(crd_en), .Addr_csrw(Addr_csr1), .Clock(Clock), .Addr_csr1(Addr_csr1),
    .Addr_csr2({12{1'b0}}), .Exception_code(Invalid_op),
    .PC_Addr({addrflag_boot, PC_exec[30:26], addrflag_memtmp, PC_exec[24], addr_real}),
    .PC_ip(instruction_code), .PC_next(PC_next), .mret(mret), .mip_in(mip_set), .mip_en(mip_seten),
    .Out_csr1(Out_csr1), .Out_csr2(Out_csr2), .En_jmp(PC_except), .Addr_jmp(Addr_except), .mip_out(mip_cur));  // open: mie_out, ecode_out, timer_en, mepc_out
  i2c_controller i2c_controller_1 (
    .IICClock(IICClock), .SDA(SDA_in), .Addr_w({addrflag_peripheral, addrflag_ssd, mem_addr, Addr_ssd}),
    .Data_in(data_mem), .we(We_mem), .Addr_rd({addrflag_peripheral, addrflag_ssd, mem_addr, Addr_ssd}),
    .int_gate(int_peripheral), .Clock(Clock), .SDA_out(SDA_out), .SCL(SCL), .Out_rd(data_memiic),
    .Out_en(memiic_en), .perint_code(int_iiccode));
  memory Momery_2 (
    .Addr({addrflag_peripheral, addrflag_ssd, mem_addr, Addr_ssd}), .Data_in(data_mem), .WE(We_mem),
    .OE(Oe_mem), .ByteSize_in(storebytes_size), .Clock(Clock),
    .Addr_PC({addrflag_boot, PC_exec[30:26], addrflag_memtmp, PC_exec[24], addr_real}), .OE_PC(addrflag_mem),
    .Data_out(data_memrd), .DataPC_out(instruction_code));
  int_bus int_bus_1 (
    .Clock(Clock), .int_gate(int_gatesrc), .int_uart(int_uartcode), .int_gpio(int_gpiocode),
    .int_iic(int_iiccode), .int_gateout(int_peripheral), .int_code(int_peripheralcode));
  gpio u_gpio_1 (
    .Clock(Clock), .Addr_w({addrflag_peripheral, addrflag_ssd, mem_addr, Addr_ssd}), .Data_in(data_mem),
    .we(We_mem), .Addr_rd({addrflag_peripheral, addrflag_ssd, mem_addr, Addr_ssd}),
    .int_gate(int_peripheral), .GPIO1_in(GPIO_in1), .GPIO2_in(GPIO_in2), .GPIO3_in(GPIO_in3),
    .GPIO4_in(GPIO_in4), .GPIO5_in(GPIO_in5), .GPIO6_in(GPIO_in6), .GPIO7_in(GPIO_in7), .GPIO8_in(GPIO_in8),
    .GPIO9_in(GPIO_in9), .GPIO10_in(GPIO_in10), .Out_rd(data_memgpio), .Out_en(memgpio_en),
    .perint_code(int_gpiocode), .GPIO1_out(GPIO_1), .GPIO2_out(GPIO_2), .GPIO3_out(GPIO_3),
    .GPIO4_out(GPIO_4), .GPIO5_out(GPIO_5), .GPIO6_out(GPIO_6), .GPIO7_out(GPIO_7), .GPIO8_out(GPIO_8),
    .GPIO9_out(GPIO_9), .GPIO10_out(GPIO_10));
  uart uart_1 (
    .Addr_w({addrflag_peripheral, addrflag_ssd, mem_addr, Addr_ssd}), .Data_in(data_mem), .we(We_mem),
    .Addr_rd({addrflag_peripheral, addrflag_ssd, mem_addr, Addr_ssd}), .int_gate(int_peripheral), .RX(RX),
    .Clock(Clock), .UartClock(UartClock), .TX(TX), .Out_rd(data_memuart), .Out_en(memuart_en),
    .perint_code(int_uartcode), .Data_dma(data_dma), .Addr_dma(dma_addr), .we_dma(We_dma));
  Comparator #(.Bits(32)) comparator_1 (
    .a({addrflag_peripheral, addrflag_ssd, mem_addr, Addr_ssd}), .b(32'hc0000000), .eq(comparator_1_eq));  // open: gt, lt
  // And and_6 has open pins: In_1=comparator_1_eq, In_2=Oe_dma, out=open
  Register #(.Bits(32)) register_1 (.D(data_dma), .C(Clock), .en(We_dma), .Q(ddd));

  // Other names for the same wires on the sheet: Addr_csrw[11:0] = Addr_csr1; c = Clock; gpio_out1 = GPIO_1;
  //   gpio_out2 = GPIO_2; gpio_out3 = GPIO_3; gpio_out4 = GPIO_4; gpio_out5 = GPIO_5; gpio_out6 = GPIO_6;
  //   gpio_out7 = GPIO_7; gpio_out8 = GPIO_8; gpio_out9 = GPIO_9; gpio_out10 = GPIO_10; iic_clock = IICClock;
  //   addr_iop[23:0] = Addr_ssd; mem_addr (some bits) = {addrflag_peripheral, addrflag_ssd, Addr_ssd};
  //   Oe_ssd = ssd_en; PC_exec (some bits) = {addrflag_boot, addrflag_memtmp, addr_real};
  //   data_memssd[7:0] = ssd_bytein; Timer_clock = TimerClock; uart_clock = UartClock

  // Notes on the sheet:
  //   Clock: Hz: 50000
  //   TimerClock: Hz: 100
  //   UartClock: Hz: 50000
  //   IICClock: Hz: 50000
  //   Reg Bus
  //   Memory Bus
  //   Instruction Execution Unit
  //   Instruction Program Counter Bus
  //   Instruction Decoder
  //   Exception  Interrupt Unit
  //   Peripheral IIC
  //   DMA Controller
  //   Storage
  //   Peripheral GPIO
  //   Peripheral UART
endmodule
