// Digital circuit test_op.dig as structural Verilog
module test_op (
  input  [31:0] instruction_code,
  input  PC_EN,
  output [4:0] rd,
  output [4:0] rs1,
  output [4:0] rs2,
  output [6:0] imm_2531,
  output [19:0] imm_1231,
  output [11:0] imm_2031,
  output [31:0] invalid_op,
  output [7:0] mechine_op,
  output [5:0] csr_op,
  output [8:0] jmp_op,
  output [18:0] alu_op,
  output [8:0] mem_op,
  output cust_op,
  output [31:0] wrong_op,
  output wrong_en
);

  wire and_1_out, comparator_1_eq, comparator_2_eq, comparator_3_eq, comparator_4_eq, comparator_5_eq,
       comparator_6_eq, cust_op_old;
  wire [4:0] rd_old, rs1_old, rs2_old;
  wire [5:0] csr_op_old;
  wire [6:0] imm_2531_old;
  wire [7:0] mechie_op_old;
  wire [8:0] jmp_op_old, mem_op_old;
  wire [11:0] imm_2031_old;
  wire [18:0] alu_op_old;
  wire [19:0] imm_1231_old;
  wire [31:0] invalid_op_old;

  inst_decoder_verilog inst_decoder_verilog_1 (
    .instruction_code(instruction_code), .PC_EN(PC_EN), .rd(rd), .rs1(rs1), .rs2(rs2), .imm_2531(imm_2531),
    .imm_1231(imm_1231), .imm_2031(imm_2031), .invalid_op(invalid_op), .mechine_op(mechine_op),
    .csr_op(csr_op), .jmp_op(jmp_op), .alu_op(alu_op), .mem_op(mem_op), .cust_op(cust_op));
  instruction_decoder instruction_decoder_1 (
    .Instruction_In(instruction_code), .EN(PC_EN), .rd(rd_old), .rs1(rs1_old), .rs2(rs2_old),
    .imm_2531(imm_2531_old), .imm_1231(imm_1231_old), .imm_2032(imm_2031_old), .invalid(invalid_op_old),
    .mechie_op(mechie_op_old), .csr_op(csr_op_old), .jmp_op(jmp_op_old), .alu_op(alu_op_old),
    .mem_op(mem_op_old), .cust_op(cust_op_old));
  Comparator #(.Bits(8)) comparator_1 (.a(mechie_op_old), .b(mechine_op), .eq(comparator_1_eq));  // open: gt, lt
  Comparator #(.Bits(6)) comparator_2 (.a(csr_op), .b(csr_op_old), .eq(comparator_2_eq));  // open: gt, lt
  Comparator #(.Bits(9)) comparator_3 (.a(jmp_op), .b(jmp_op_old), .eq(comparator_3_eq));  // open: gt, lt
  Comparator #(.Bits(19)) comparator_4 (.a(alu_op), .b(alu_op_old), .eq(comparator_4_eq));  // open: gt, lt
  Comparator #(.Bits(9)) comparator_5 (.a(mem_op), .b(mem_op_old), .eq(comparator_5_eq));  // open: gt, lt
  Comparator comparator_6 (.a(cust_op_old), .b(cust_op), .eq(comparator_6_eq));  // open: gt, lt
  and and_1 (and_1_out, comparator_1_eq, comparator_2_eq, comparator_3_eq, comparator_4_eq, comparator_5_eq, comparator_6_eq);
  not not_1 (wrong_en, and_1_out);
  assign wrong_op = wrong_en ? instruction_code : 32'bz;  // Driver driver_1

  // Other names for the same wires on the sheet: mechie_op[7:0] = mechine_op; wrong_op_t = wrong_en
endmodule
