// Digital circuit uart-term.dig as structural Verilog
module uart_term (
  input  RX,
  input  UartClock
);

  wire read_en, read_ready, tx, writeable;
  wire [7:0] read_byte;

  Terminal terminal_1 (.D(read_byte), .C(UartClock), .en(read_ready));
  assign read_en = UartClock ? read_ready : 1'bz;  // Driver driver_1
  PullUp pullup_1 (.out(read_en));
  uart_ttl uart_ttl_1 (
    .InnerClock(UartClock), .Clock(UartClock), .read_en(read_en), .Data_in(8'h31), .write_en(1'b0), .RX(RX),
    .TX(tx), .Read_out(read_byte), .Read_ready(read_ready), .Writeable(writeable));

  // Other names for the same wires on the sheet: read_bit = RX; uart_clock = UartClock

  // Notes on the sheet:
  //   UartClock: Hz: 50
endmodule
