// Digital circuit uart.dig as structural Verilog
module uart (
  input  [31:0] Addr_w,
  input  [31:0] Data_in,
  input  we,
  input  [31:0] Addr_rd,
  input  int_gate,
  input  RX,
  input  Clock,
  input  UartClock,
  output TX,
  output [31:0] Out_rd,
  output Out_en,
  output [31:0] perint_code,
  output [31:0] Data_dma,
  output [31:0] Addr_dma,
  output we_dma
);

  wire addr_compare_1_eq_out, addr_compare_2_eq_out, addr_compare_4_eq_out, addr_compare_5_eq_out,
       addr_compare_6_eq_out, addr_compare_7_eq_out, and_1_out, and_2_out, and_4_out, and_5_out,
       comparator_1_gt, comparator_2_eq, comparator_2_gt, d_ff_1_q, or_1_out, or_2_out, or_3_out, pos_init,
       read_en, read_ready, save_dma, update_read, w_begin, write_able, xor_1_out;
  wire [31:0] add_1_s, buf_write_pos, d_ff_2_q, uart_config;

  or or_1 (or_1_out, we_dma, pos_init);
  and and_1 (and_1_out, ~save_dma, read_ready);  // And
  PullDown pulldown_1 (.out(save_dma));
  Register #(.Bits(32)) dma_write_address (.D(buf_write_pos), .C(Clock), .en(or_1_out), .Q(Addr_dma));
  assign read_en = and_1_out ? 1'b0 : 1'bz;  // Driver driver_1
  addr_compare addr_compare_1 (.Addr_in1(Addr_w), .Addr_in2(32'ha0000100), .Eq_out(addr_compare_1_eq_out));
  PullUp pullup_1 (.out(read_en));
  addr_compare addr_compare_2 (.Addr_in1(Addr_w), .Addr_in2(32'ha0000104), .Eq_out(addr_compare_2_eq_out));
  addr_compare addr_compare_3 (.Addr_in1(Addr_w), .Addr_in2(32'ha0000108), .Eq_out(update_read));
  uart_ttl uart_ttl_1 (
    .InnerClock(UartClock), .Clock(Clock), .read_en(read_en), .Data_in(Data_in[7:0]), .write_en(w_begin),
    .RX(RX), .TX(TX), .Read_out(Data_dma[7:0]), .Read_ready(read_ready), .Writeable(write_able));
  and and_2 (and_2_out, addr_compare_1_eq_out, we);
  and and_3 (w_begin, addr_compare_2_eq_out, we);
  Register #(.Bits(32)) u_uart_config (.D(Data_in), .C(Clock), .en(and_2_out), .Q(uart_config));
  RS_FF rs_ff_1 (.S(1'b1), .C(Clock), .R(read_ready), .nQ(save_dma));  // open: Q
  Comparator #(.Bits(32)) comparator_1 (.a(Addr_dma), .b(32'hc0000000), .gt(comparator_1_gt));  // open: eq, lt
  Comparator #(.Bits(32)) comparator_2 (
    .a(Data_in), .b(Addr_dma), .gt(comparator_2_gt), .eq(comparator_2_eq));  // open: lt
  addr_compare addr_compare_4 (.Addr_in1(Addr_rd), .Addr_in2(32'ha0000100), .Eq_out(addr_compare_4_eq_out));
  addr_compare addr_compare_5 (.Addr_in1(Addr_rd), .Addr_in2(32'ha000010c), .Eq_out(addr_compare_5_eq_out));
  addr_compare addr_compare_6 (.Addr_in1(Addr_rd), .Addr_in2(32'ha0000110), .Eq_out(addr_compare_6_eq_out));
  PullDown #(.Bits(32)) pulldown_2 (.out(Addr_dma));
  and and_4 (and_4_out, comparator_1_gt, ~int_gate);  // And
  or or_2 (or_2_out, comparator_2_gt, comparator_2_eq);
  addr_compare addr_compare_7 (.Addr_in1({32{1'b0}}), .Addr_in2(Addr_dma), .Eq_out(addr_compare_7_eq_out));
  assign perint_code = and_4_out ? 32'h2 : 32'bz;  // Driver driver_2
  assign Out_rd = addr_compare_4_eq_out ? uart_config : 32'bz;  // Driver driver_3
  assign Out_rd = addr_compare_5_eq_out ? Addr_dma : 32'bz;  // Driver driver_4
  assign Out_rd = addr_compare_6_eq_out ? {{31{1'b0}}, write_able} : 32'bz;  // Driver driver_5
  and and_5 (and_5_out, update_read, or_2_out);
  assign Out_en = addr_compare_5_eq_out ? 1'b1 : 1'bz;  // Driver driver_6
  assign Out_en = addr_compare_6_eq_out ? 1'b1 : 1'bz;  // Driver driver_7
  D_FF d_ff_1 (.D(read_ready), .C(Clock), .Q(d_ff_1_q));  // open: nQ
  assign Out_en = addr_compare_4_eq_out ? 1'b1 : 1'bz;  // Driver driver_8
  or or_3 (or_3_out, and_5_out, addr_compare_7_eq_out);
  xor xor_1 (xor_1_out, read_ready, d_ff_1_q);
  Add #(.Bits(32)) add_1 (.a(Addr_dma), .b(32'h1), .c_i(1'b0), .s(add_1_s));  // open: c_o
  and and_6 (pos_init, ~read_ready, or_3_out);  // And
  assign buf_write_pos = pos_init ? 32'hc0000000 : 32'bz;  // Driver driver_9
  and and_7 (we_dma, read_ready, xor_1_out);
  D_FF #(.Bits(32)) d_ff_2 (.D(add_1_s), .C(we_dma), .Q(d_ff_2_q));  // open: nQ
  PullDown pulldown_3 (.out(Out_en));
  PullUp pullup_2 (.out(TX));
  assign buf_write_pos = we_dma ? d_ff_2_q : 32'bz;  // Driver driver_10

  assign Data_dma[31:8] = {24{1'b0}};

  // Other names for the same wires on the sheet: buf_wpos[31:0] = Addr_dma; C = Clock; data_w[7:0] = Data_in[7:0];
  //   int_code[31:0] = perint_code; pos_add = we_dma; read_bit = RX; read_byte[7:0] = Data_dma[7:0]; send_bit = TX;
  //   uart_clock = UartClock

  // Notes on the sheet:
  //   Clock: Hz: 100
  //   UartClock: Hz: 50
  //   31	30   ...	6 	5 	4-1 	0
  //   writeable  readable           stop  verify  bit-size   start
endmodule
