// Digital circuit digital_soc.dig as structural Verilog
module digital_soc (
  input  C,
  input  timeclk
);

  wire rst, u_riscvmcu_digital_flash_read_en, u_riscvmcu_digital_flash_write_en,
       u_riscvmcu_digital_mem_read_en, u_riscvmcu_digital_mem_write_en;
  wire [7:0] flash_data, u_riscvmcu_digital_flash_wdata;
  wire [31:0] mem_data, u_riscvmcu_digital_flash_addr, u_riscvmcu_digital_mem_addr,
       u_riscvmcu_digital_mem_wdata, u_riscvmcu_gpio_values;

  Reset reset_1 (.out(rst));
  riscvmcu #(.applicationType("IVERILOG")) u_riscvmcu (
    .clk(C), .rst(rst), .clk_timer(timeclk), .digital_mem_data(mem_data), .digital_flash_data(flash_data),
    .digital_flash_addr(u_riscvmcu_digital_flash_addr),
    .digital_flash_write_en(u_riscvmcu_digital_flash_write_en),
    .digital_flash_read_en(u_riscvmcu_digital_flash_read_en),
    .digital_flash_wdata(u_riscvmcu_digital_flash_wdata), .digital_mem_addr(u_riscvmcu_digital_mem_addr),
    .digital_mem_write_en(u_riscvmcu_digital_mem_write_en),
    .digital_mem_read_en(u_riscvmcu_digital_mem_read_en), .digital_mem_wdata(u_riscvmcu_digital_mem_wdata),
    .gpio_values(u_riscvmcu_gpio_values));  // open: digital_flash_byte_size, digital_mem_byte_size
  EEPROMDualPort #(.AddrBits(24), .Bits(8)) eepromdualport_1 (
    .A(u_riscvmcu_digital_flash_addr[23:0]), .Din(u_riscvmcu_digital_flash_wdata),
    .str(u_riscvmcu_digital_flash_write_en), .C(C), .ld(u_riscvmcu_digital_flash_read_en), .D(flash_data));
  RAMDualPort #(.AddrBits(24), .Bits(32)) ramdualport_1 (
    .A(u_riscvmcu_digital_mem_addr[23:0]), .Din(u_riscvmcu_digital_mem_wdata),
    .str(u_riscvmcu_digital_mem_write_en), .C(C), .ld(u_riscvmcu_digital_mem_read_en), .D(mem_data));
  LED led_1 (.in(u_riscvmcu_gpio_values[0]));
  LED led_2 (.in(u_riscvmcu_gpio_values[1]));
  LED led_3 (.in(u_riscvmcu_gpio_values[2]));
  // PolarityAwareLED polarityawareled_1: pin names not known; wires that end beside it: u_riscvmcu_gpio_values[0], 1'b0

  // Other names for the same wires on the sheet: clk = C; clk_timer = timeclk

  // Notes on the sheet:
  //   C: Hz: 50000
  //   contents of eepromdualport_1 (hex, n*v repeats v):
  //   93,2,70,0,37,3,0,c0,23,20,53,0,93,2,70,0,23,22,53,0,13,0,0,0,6f
  //   ,f0,df,ff,1,0,0,0,1,0,0,0,1,0,0,0,1,0,0,0,1,0,0,0,1,0,0,0,1,0,0,0
  //   ,1,0,0,0,1,0,0,0,1
endmodule

/* Code of riscvmcu:
`include "digital_soc.v"
module riscvmcu(
	input  wire        clk,           // 时钟信号
    input  wire        rst,           // 复位信号
    input  wire        clk_timer,

    output wire  [31:0] digital_flash_addr,
    output wire  digital_flash_write_en,
    output wire  digital_flash_read_en,
    output wire  [2:0] digital_flash_byte_size,
    output wire  [7:0] digital_flash_wdata,
    input wire   [7:0] digital_flash_data,
    output wire  [31:0] digital_mem_addr,
    output wire  digital_mem_write_en,
    output wire  digital_mem_read_en,
    output wire  [3:0] digital_mem_byte_size,
    output wire  [31:0] digital_mem_wdata,
    input wire [31:0] digital_mem_data,
    inout wire [31:0] gpio_values
);
digital_soc digital_soc(
    .clk(clk),
    .rst(rst),
    .clk_timer(clk_timer),
    .digital_flash_addr(digital_flash_addr),
    .digital_flash_write_en(digital_flash_write_en),
    .digital_flash_read_en(digital_flash_read_en),
    .digital_flash_byte_size(digital_flash_byte_size),
    .digital_flash_wdata(digital_flash_wdata),
    .digital_flash_data(digital_flash_data),
    .digital_mem_addr(digital_mem_addr),
    .digital_mem_write_en(digital_mem_write_en),
    .digital_mem_read_en(digital_mem_read_en),
    .digital_mem_byte_size(digital_mem_byte_size),
    .digital_mem_wdata(digital_mem_wdata),
    .digital_mem_data(digital_mem_data),
    .gpio_values(gpio_values)
);
endmodule
*/
