// Digital circuit digital_soc1.dig as structural Verilog
module digital_soc1 (
  input  C,
  input  timeclk,
  input  [31:0] in_3
);

  wire rst_n, u_riscvmcu_digital_flash_read_en, u_riscvmcu_digital_flash_write_en,
       u_riscvmcu_digital_mem_read_en, u_riscvmcu_digital_mem_write_en;
  wire [7:0] flash_data, u_riscvmcu_digital_flash_wdata;
  wire [31:0] mem_data, u_riscvmcu_digital_flash_addr, u_riscvmcu_digital_mem_addr,
       u_riscvmcu_digital_mem_wdata, u_riscvmcu_gpio_values_out;

  Reset reset_1 (.out(rst_n));
  Terminal terminal_1 ();  // open: D, C, en
  riscvmcu #(.applicationType("IVERILOG")) u_riscvmcu (
    .digital_flash_data(flash_data), .gpio_values_in(in_3), .digital_mem_data(mem_data),
    .digital_flash_addr(u_riscvmcu_digital_flash_addr),
    .digital_flash_write_en(u_riscvmcu_digital_flash_write_en),
    .digital_flash_read_en(u_riscvmcu_digital_flash_read_en),
    .digital_flash_wdata(u_riscvmcu_digital_flash_wdata), .digital_mem_addr(u_riscvmcu_digital_mem_addr),
    .digital_mem_write_en(u_riscvmcu_digital_mem_write_en),
    .digital_mem_read_en(u_riscvmcu_digital_mem_read_en), .digital_mem_wdata(u_riscvmcu_digital_mem_wdata),
    .gpio_values_out(u_riscvmcu_gpio_values_out));  // open: digital_flash_byte_size, digital_mem_byte_size
  EEPROMDualPort #(.AddrBits(24), .Bits(8)) eepromdualport_1 (
    .A(u_riscvmcu_digital_flash_addr[23:0]), .Din(u_riscvmcu_digital_flash_wdata),
    .str(u_riscvmcu_digital_flash_write_en), .C(C), .ld(u_riscvmcu_digital_flash_read_en), .D(flash_data));
  RAMDualPort #(.AddrBits(24), .Bits(32)) ramdualport_1 (
    .A(u_riscvmcu_digital_mem_addr[23:0]), .Din(u_riscvmcu_digital_mem_wdata),
    .str(u_riscvmcu_digital_mem_write_en), .C(C), .ld(u_riscvmcu_digital_mem_read_en), .D(mem_data));
  LED led_1 (.in(u_riscvmcu_gpio_values_out[0]));
  LED led_2 (.in(u_riscvmcu_gpio_values_out[1]));
  LED led_3 (.in(u_riscvmcu_gpio_values_out[2]));
  LED led_4 (.in(u_riscvmcu_gpio_values_out[3]));
  LED led_5 (.in(u_riscvmcu_gpio_values_out[4]));
  LED led_6 (.in(u_riscvmcu_gpio_values_out[5]));
  LED led_7 (.in(u_riscvmcu_gpio_values_out[6]));

  // Other names for the same wires on the sheet: clk = C; clk_timer = timeclk

  // Notes on the sheet:
  //   C: Hz: 50000
  //   contents of eepromdualport_1 (hex, n*v repeats v):
  //   0,7,0,2,93,87,17,0,f3,93,57,30,37,2e,0,0,13,e,8e,80,f3,13,e,30
  //   ,37,1,0,1,ef,0,90,1c,ef,0,40,9,73,0,20,30,20*0,ef,0,40,45,73,0
  //   ,20,30,8*0,ef,0,80,1,ef,0,40,45,ef,0,0,3,73,0,20,30,f3,13,45,30
  //   ,67,80,0,0,13,1,81,fe,23,20,c1,0,23,22,d1,0,23,24,e1,0,23,26,f1
  //   ,0,23,28,1,1,23,2a,11,1,67,80,0,0,3,26,1,0,83,26,41,0,3,27,81
  //   ,0,83,27,c1,0,3,28,1,1,83,28,41,1,13,1,81,1,67,80,0,0,ef,f0,1f
  //   ,fc,ef,0,80,3e,ef,f0,9f,fd,67,80,0,0,ef,f0,1f,fb,ef,0,40,3d,ef
  //   ,f0,9f,fc,73,0,20,30,67,80,0,0,13,1,1,ff,13,5,f0,7,23,26,11,0
  //   ,ef,0,c0,2c,b7,7,0,10,83,a7,7,7,63,84,7,6,23,24,81,0,37,4,0,10
  //   ,83,27,84,6,63,90,7,4,ef,0,40,30,13,65,f5,7,ef,0,0,2f,93,7,10
  //   ,0,23,24,f4,6,3,24,81,0,37,15,0,0,13,5,5,9f,ef,0,0,4f,83,20,c1
  //   ,0,13,6,80,c,13,5,40,1f,93,5,0,0,13,1,1,1,6f,0,80,7b,ef,0,80,2c
  //   ,13,75,5,f8,ef,0,40,2b,23,24,4,6,3,24,81,0,6f,f0,9f,fc,ef,0,0
  //   ,2b,13,75,5,f8,ef,0,c0,29,b7,7,0,10,3,a5,c7,6,13,5,15,0,13,7,70
  //   ,0,63,4c,a7,0,13,7,5,0,93,5,10,0,23,a6,e7,6,ef,0,80,23,6f,f0,5f
  //   ,f9,13,7,10,0,13,5,7,0,6f,f0,9f,fe,13,1,1,ff,13,5,a0,0,23,26,11
  //   ,0,ef,0,0,27,b7,7,0,10,23,a8,a7,6,ef,0,0,28,37,15,0,0,83,20,c1
  //   ,0,13,5,45,a0,13,1,1,1,6f,0,0,45,13,1,1,ff,13,5,f0,7,23,22,91
  //   ,0,23,20,21,1,23,26,11,0,23,24,81,0,b7,4,0,10,ef,0,c0,1c,13,9
  //   ,80,0,13,5,a0,0,ef,0,40,22,23,a8,a4,6,13,4,10,0,63,a,5,4,ef,0
  //   ,80,20,13,65,f5,7,ef,0,40,1f,93,5,0,0,13,5,40,1f,ef,0,40,79,ef
  //   ,0,0,1f,13,75,5,f8,ef,0,c0,1d,13,5,40,1f,93,5,0,0,ef,0,c0,77,13
  //   ,5,a0,0,ef,0,0,1e,23,a8,a4,6,13,4,10,0,e3,10,5,fc,6f,0,c0,0,83
  //   ,a7,4,7,e3,90,7,fa,13,5,4,0,93,5,10,0,ef,0,40,16,13,5,40,1f,93
  //   ,5,0,0,ef,0,40,74,13,5,4,0,93,5,0,0,13,4,14,0,ef,0,80,14,e3,18
  //   ,24,fd,6f,f0,1f,f7,13,1,1,ff,23,26,11,0,ef,0,40,6d,93,5,0,0,13
  //   ,6,80,c,13,5,40,1f,ef,0,c0,65,93,5,80,18,13,5,10,0,ef,0,80,19
  //   ,6f,0,0,0,13,1,1,ff,23,24,81,0,23,26,11,0,13,4,5,0,63,4,6,0,ef
  //   ,f0,df,fe,13,5,4,0,83,20,c1,0,3,24,81,0,13,1,1,1,67,80,0,0,83
  //   ,47,5,0,13,7,5,0,13,5,0,0,63,86,7,2,93,16,25,0,33,5,d5,0,93,87
  //   ,7,fd,13,7,17,0,13,15,15,0,33,5,f5,0,83,47,7,0,13,75,f5,f,e3,90
  //   ,7,fe,67,80,0,0,67,80,0,0,b7,17,0,0,93,87,c7,a1,3,d6,87,0,13,1,1
  //   ,ff,83,a6,7,0,3,a7,47,0,83,c7,a7,0,23,22,d1,0,23,24,e1,0,a3,81
  //   ,5,0,23,16,c1,0,23,7,f1,0,13,7,90,0,93,86,25,0,63,56,a7,2,93,7
  //   ,5,0,13,5,0,0,93,87,67,ff,13,5,15,0,e3,4c,f7,fe,b3,87,27,0,83
  //   ,c7,47,0,23,80,f6,0,93,86,f6,ff,e3,4e,a7,fc,33,5,25,0,83,47,45
  //   ,0,23,80,f6,0,13,85,5,0,13,1,1,1,67,80,0,0,63,8e,5,0,b7,7,0,c0
  //   ,13,5,f5,ff,3,a7,7,0,b3,95,a5,0,b3,e5,e5,0,23,a0,b7,0,67,80,0,0
  //   ,b7,7,0,c0,23,a0,a7,0,67,80,0,0,37,7,0,c0,13,5,f5,ff,93,7,10,0
  //   ,13,7,87,0,b3,97,a7,0,3,27,7,0,63,8a,5,0,33,67,f7,0,b7,7,0,c0
  //   ,23,a2,e7,0,67,80,0,0,93,c7,f7,ff,33,f7,e7,0,b7,7,0,c0,23,a2,e7
  //   ,0,67,80,0,0,b7,7,0,c0,23,a2,a7,0,67,80,0,0,b7,7,0,c0,3,a5,87
  //   ,0,67,80,0,0,37,7,0,c0,13,5,f5,ff,93,7,10,0,b3,97,a7,0,3,25,87
  //   ,0,33,f5,a7,0,67,80,0,0,b7,7,0,c0,23,a8,7,0,67,80,0,0,b7,7,0,10
  //   ,13,15,25,0,93,87,7,0,b3,87,a7,0,37,7,0,10,23,a0,b7,0,3,25,47
  //   ,7,93,7,f0,7f,63,f4,a7,0,67,80,0,0,b7,17,0,0,93,87,7,80,33,65
  //   ,f5,0,23,2a,a7,6,6f,f0,9f,bf,37,7,0,10,83,27,47,7,93,e7,7,8,13
  //   ,6,5,0,b7,6,0,10,13,85,7,0,23,ac,c6,6,23,2a,f7,6,6f,f0,5f,bd,67
  //   ,80,0,0,b7,7,0,10,83,a7,87,7,63,84,7,0,67,80,7,0,67,80,0,0,b7
  //   ,7,ff,f,3,a7,7,0,b7,7,0,10,13,17,27,0,93,87,7,0,b3,87,e7,0,83
  //   ,a7,7,0,63,84,7,0,67,80,7,0,67,80,0,0,b7,7,0,10,13,7,10,0,23,ae
  //   ,e7,6,67,80,0,0,13,1,1,ff,23,24,81,0,37,4,0,10,23,26,11,0,83,27
  //   ,4,8,63,8e,7,0,b7,7,0,10,83,20,c1,0,3,24,81,0,23,ae,7,6,13,1,1,1
  //   ,67,80,0,0,93,5,c0,4c,13,5,20,0,ef,f0,9f,f1,93,7,10,0,23,20,f4
  //   ,8,b7,7,0,10,83,20,c1,0,3,24,81,0,23,ae,7,6,13,1,1,1,67,80,0,0
  //   ,b7,7,0,a0,23,82,a7,10,13,87,7,11,83,27,7,0,93,f7,17,0,e3,8c,7
  //   ,fe,67,80,0,0,63,8a,5,2,37,6,0,a0,13,7,6,0,b3,6,b5,0,13,6,46,10
  //   ,13,7,7,11,83,47,5,0,23,0,f6,0,83,27,7,0,93,f7,17,0,e3,8c,7,fe
  //   ,13,5,15,0,e3,14,d5,fe,67,80,0,0,13,8,5,0,63,84,5,6,b7,7,0,c0
  //   ,37,3,0,a0,b7,8,0,40,b3,85,f5,0,13,3,c3,10,93,88,f8,ff,13,5,0,0
  //   ,6f,0,80,1,83,c7,7,0,23,0,f7,0,13,5,15,0,63,84,b6,2,93,87,6,0
  //   ,93,86,17,0,33,87,16,1,3,26,3,0,33,7,e8,0,e3,ee,c7,fc,37,7,0,a0
  //   ,23,24,f7,10,67,80,0,0,93,87,5,0,37,7,0,a0,23,24,f7,10,67,80,0,0
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endmodule

/* Code of riscvmcu:
`timescale 1ns/1ns
`include "digital_soc.v"
module riscvmcu(

    output wire  [31:0] digital_flash_addr,
    output wire  digital_flash_write_en,
    output wire  digital_flash_read_en,
    output wire  [2:0] digital_flash_byte_size,
    output wire  [7:0] digital_flash_wdata,
    input wire   [7:0] digital_flash_data,
    input wire  [31:0] gpio_values_in,
    output wire  [31:0] digital_mem_addr,
    output wire  digital_mem_write_en,
    output wire  digital_mem_read_en,
    output wire  [3:0] digital_mem_byte_size,
    output wire  [31:0] digital_mem_wdata,
    input wire [31:0] digital_mem_data,
    output wire [31:0] gpio_values_out
);

reg clk_c;
reg clk_t;
reg rst_n;

initial begin
        clk_c = 0;
        rst_n = 0;
        clk_t = 0;
        #10 rst_n = 1;
end

always #5 clk_c = ~clk_c;
always #1000000 clk_t = ~clk_t;

wire [31:0] gpio_values;

assign gpio_values = gpio_values_in;
assign gpio_values_out = gpio_values;

genvar idx;
    generate
        for (idx = 0; idx < `GPIO_NUMS; idx = idx + 1) begin
            pulldown(gpio_values[idx]);
        end
    endgenerate

digital_soc digital_soc(
    .clk(clk_c),
    .rst_n(rst_n),
    .clk_timer(clk_t),
    .digital_flash_addr(digital_flash_addr),
    .digital_flash_write_en(digital_flash_write_en),
    .digital_flash_read_en(digital_flash_read_en),
    .digital_flash_byte_size(digital_flash_byte_size),
    .digital_flash_wdata(digital_flash_wdata),
    .digital_flash_data(digital_flash_data),
    .digital_mem_addr(digital_mem_addr),
    .digital_mem_write_en(digital_mem_write_en),
    .digital_mem_read_en(digital_mem_read_en),
    .digital_mem_byte_size(digital_mem_byte_size),
    .digital_mem_wdata(digital_mem_wdata),
    .digital_mem_data(digital_mem_data),
    .gpio_values(gpio_values)
);
endmodule
*/
