// Digital circuit tt.dig as structural Verilog
module tt (
  input  C,
  input  timeclk,
  input  in_3,
  input  in_4,
  input  [7:0] in_5,
  input  [31:0] in_6,
  output [31:0] out_7,
  output out_8,
  output out_9,
  output [2:0] out_10,
  output [7:0] out_11,
  output [31:0] out_12,
  output out_13,
  output out_14,
  output [3:0] out_15,
  output [31:0] out_16,
  output [31:0] out_17
);

  wire rst;

  Reset reset_1 (.out(rst));
  riscvmcu #(.applicationType("Socket")) u_riscvmcu (
    .clk(in_3), .rst(rst), .clk_timer(in_4), .digital_flash_data(in_5), .digital_mem_data(in_6),
    .digital_flash_addr(out_7), .digital_flash_write_en(out_8), .digital_flash_read_en(out_9),
    .digital_flash_byte_size(out_10), .digital_flash_wdata(out_11), .digital_mem_addr(out_12),
    .digital_mem_write_en(out_13), .digital_mem_read_en(out_14), .digital_mem_byte_size(out_15),
    .digital_mem_wdata(out_16), .gpio_values_out(out_17));

  // Other names for the same wires on the sheet: clk = C; clk_timer = timeclk

  // Notes on the sheet:
  //   C: Hz: 50000
  //   timeclk: Hz: 100
endmodule

/* Code of riscvmcu:
127.0.0.1:8009
*/
