// Digital circuit memory.dig as structural Verilog
module memory (
  input  [31:0] Addr,
  input  [31:0] Data_in,
  input  WE,
  input  OE,
  input  [3:0] ByteSize_in,
  input  Clock,
  output [31:0] Data_out
);

  wire and_1_out, and_2_out, and_3_out, and_4_out, and_5_out, and_6_out, and_7_out, and_8_out, and_9_out,
       and_10_out, and_11_out, and_12_out, cs0, cs1, cs2, cs3, we0, we1, we2, we3;
  wire [7:0] byte0, byte1, byte2, byte3, data0, data1, data2, data3;

  assign {byte3, byte2, byte1, byte0} = WE ? Data_in : 32'bz;  // Driver driver_1
  assign Data_in = OE ? {byte3, byte2, byte1, byte0} : 32'bz;  // Driver driver_2
  Decoder #(.Selector_Bits(2)) decoder_1 (.sel(Addr[1:0]), .out_0(cs0), .out_1(cs1), .out_2(cs2), .out_3(cs3));
  and and_1 (and_1_out, WE, cs0);
  and and_2 (and_2_out, OE, cs0);
  and and_3 (and_3_out, WE, cs0);
  RAMSinglePort #(.AddrBits(24), .Bits(8)) ramsingleport_1 (.A(Addr[25:2]), .str(we0), .C(Clock), .ld(OE), .D(data0));
  assign data0 = and_1_out ? byte0 : 8'bz;  // Driver driver_3
  assign data1 = and_1_out ? byte1 : 8'bz;  // Driver driver_4
  assign data2 = and_1_out ? byte2 : 8'bz;  // Driver driver_5
  assign data3 = and_1_out ? byte3 : 8'bz;  // Driver driver_6
  assign byte0 = and_2_out ? data0 : 8'bz;  // Driver driver_7
  assign byte1 = and_2_out ? data1 : 8'bz;  // Driver driver_8
  assign byte2 = and_2_out ? data2 : 8'bz;  // Driver driver_9
  assign byte3 = and_2_out ? data3 : 8'bz;  // Driver driver_10
  assign we0 = and_3_out ? ByteSize_in[0] : 1'bz;  // Driver driver_11
  assign we1 = and_3_out ? ByteSize_in[1] : 1'bz;  // Driver driver_12
  assign we2 = and_3_out ? ByteSize_in[2] : 1'bz;  // Driver driver_13
  assign we3 = and_3_out ? ByteSize_in[3] : 1'bz;  // Driver driver_14
  RAMSinglePort #(.AddrBits(24), .Bits(8)) ramsingleport_2 (.A(Addr[25:2]), .str(we1), .C(Clock), .ld(OE), .D(data1));
  and and_4 (and_4_out, WE, cs1);
  and and_5 (and_5_out, OE, cs1);
  and and_6 (and_6_out, WE, cs1);
  assign data1 = and_4_out ? byte0 : 8'bz;  // Driver driver_15
  assign data2 = and_4_out ? byte1 : 8'bz;  // Driver driver_16
  assign data3 = and_4_out ? byte2 : 8'bz;  // Driver driver_17
  assign data0 = and_4_out ? byte3 : 8'bz;  // Driver driver_18
  assign byte0 = and_5_out ? data1 : 8'bz;  // Driver driver_19
  assign byte1 = and_5_out ? data2 : 8'bz;  // Driver driver_20
  assign byte2 = and_5_out ? data3 : 8'bz;  // Driver driver_21
  assign byte3 = and_5_out ? data0 : 8'bz;  // Driver driver_22
  assign we1 = and_6_out ? ByteSize_in[0] : 1'bz;  // Driver driver_23
  assign we2 = and_6_out ? ByteSize_in[1] : 1'bz;  // Driver driver_24
  assign we3 = and_6_out ? ByteSize_in[2] : 1'bz;  // Driver driver_25
  assign we0 = and_6_out ? ByteSize_in[3] : 1'bz;  // Driver driver_26
  RAMSinglePort #(.AddrBits(24), .Bits(8)) ramsingleport_3 (.A(Addr[25:2]), .str(we2), .C(Clock), .ld(OE), .D(data2));
  and and_7 (and_7_out, WE, cs2);
  and and_8 (and_8_out, OE, cs2);
  and and_9 (and_9_out, WE, cs2);
  assign data2 = and_7_out ? byte0 : 8'bz;  // Driver driver_27
  assign data3 = and_7_out ? byte1 : 8'bz;  // Driver driver_28
  assign data0 = and_7_out ? byte2 : 8'bz;  // Driver driver_29
  assign data1 = and_7_out ? byte3 : 8'bz;  // Driver driver_30
  assign byte0 = and_8_out ? data2 : 8'bz;  // Driver driver_31
  assign byte1 = and_8_out ? data3 : 8'bz;  // Driver driver_32
  assign byte2 = and_8_out ? data0 : 8'bz;  // Driver driver_33
  assign byte3 = and_8_out ? data1 : 8'bz;  // Driver driver_34
  assign we2 = and_9_out ? ByteSize_in[0] : 1'bz;  // Driver driver_35
  assign we3 = and_9_out ? ByteSize_in[1] : 1'bz;  // Driver driver_36
  assign we0 = and_9_out ? ByteSize_in[2] : 1'bz;  // Driver driver_37
  assign we1 = and_9_out ? ByteSize_in[3] : 1'bz;  // Driver driver_38
  RAMSinglePort #(.AddrBits(24), .Bits(8)) ramsingleport_4 (.A(Addr[25:2]), .str(we3), .C(Clock), .ld(OE), .D(data3));
  and and_10 (and_10_out, WE, cs3);
  and and_11 (and_11_out, OE, cs3);
  and and_12 (and_12_out, WE, cs3);
  assign data3 = and_10_out ? byte0 : 8'bz;  // Driver driver_39
  assign data0 = and_10_out ? byte1 : 8'bz;  // Driver driver_40
  assign data1 = and_10_out ? byte2 : 8'bz;  // Driver driver_41
  assign data2 = and_10_out ? byte3 : 8'bz;  // Driver driver_42
  assign byte0 = and_11_out ? data3 : 8'bz;  // Driver driver_43
  assign byte1 = and_11_out ? data0 : 8'bz;  // Driver driver_44
  assign byte2 = and_11_out ? data1 : 8'bz;  // Driver driver_45
  assign byte3 = and_11_out ? data2 : 8'bz;  // Driver driver_46
  assign we3 = and_12_out ? ByteSize_in[0] : 1'bz;  // Driver driver_47
  assign we0 = and_12_out ? ByteSize_in[1] : 1'bz;  // Driver driver_48
  assign we1 = and_12_out ? ByteSize_in[2] : 1'bz;  // Driver driver_49
  assign we2 = and_12_out ? ByteSize_in[3] : 1'bz;  // Driver driver_50

  assign Data_out = Data_in;

  // Other names for the same wires on the sheet: addr_sub[23:0] = Addr[25:2]; _1byte = ByteSize_in[0];
  //   _2byte = ByteSize_in[1]; _3byte = ByteSize_in[2]; _4byte = ByteSize_in[3]; c = Clock; data[31:0] = Data_in
endmodule
