// Digital circuit 3bit-decoder.dig as structural Verilog
module _3bit_decoder (
  input  EN,
  input  [2:0] Din,
  output _0,
  output _1,
  output _2,
  output _3,
  output _4,
  output _5,
  output _6,
  output _7
);

  wire decoder_1_out_0, decoder_1_out_1, decoder_1_out_2, decoder_1_out_3, decoder_1_out_4, decoder_1_out_5,
       decoder_1_out_6, decoder_1_out_7;

  Decoder #(.Selector_Bits(3)) decoder_1 (
    .sel(Din), .out_0(decoder_1_out_0), .out_1(decoder_1_out_1), .out_2(decoder_1_out_2),
    .out_3(decoder_1_out_3), .out_4(decoder_1_out_4), .out_5(decoder_1_out_5), .out_6(decoder_1_out_6),
    .out_7(decoder_1_out_7));
  assign _0 = EN ? decoder_1_out_0 : 1'bz;  // Driver driver_1
  assign _1 = EN ? decoder_1_out_1 : 1'bz;  // Driver driver_2
  assign _2 = EN ? decoder_1_out_2 : 1'bz;  // Driver driver_3
  assign _3 = EN ? decoder_1_out_3 : 1'bz;  // Driver driver_4
  assign _4 = EN ? decoder_1_out_4 : 1'bz;  // Driver driver_5
  assign _5 = EN ? decoder_1_out_5 : 1'bz;  // Driver driver_6
  assign _6 = EN ? decoder_1_out_6 : 1'bz;  // Driver driver_7
  assign _7 = EN ? decoder_1_out_7 : 1'bz;  // Driver driver_8
endmodule
