// Digital circuit addr-compare.dig as structural Verilog
module addr_compare (
  input  [31:0] Addr_in1,
  input  [31:0] Addr_in2,
  output Eq_out
);

  wire [31:0] xor_1_out;

  assign xor_1_out = Addr_in1 ^ Addr_in2;  // XOr xor_1, 32 bits wide
  Comparator #(.Bits(32)) comparator_1 (.a(xor_1_out), .b({32{1'b0}}), .eq(Eq_out));  // open: gt, lt
endmodule
