// Digital circuit csr-addr-spliter.dig as structural Verilog
module csr_addr_spliter (
  input  [11:0] Addr_csr,
  output Out_0,
  output Out_1,
  output Out_2,
  output Out_3,
  output Out_4,
  output Out_5,
  output Out_6,
  output Out_7
);

  wire [3:0] lookuptable_1_out;

  LookUpTable #(.Bits(4)) lookuptable_1 (
    .in0(Addr_csr[0]), .in1(Addr_csr[1]), .in2(Addr_csr[2]), .in3(Addr_csr[3]), .in4(Addr_csr[4]),
    .in5(Addr_csr[5]), .in6(Addr_csr[6]), .in7(Addr_csr[7]), .in8(Addr_csr[8]), .in9(Addr_csr[9]),
    .in10(Addr_csr[10]), .in11(Addr_csr[11]), .out(lookuptable_1_out));
  Decoder #(.Selector_Bits(4)) decoder_1 (
    .sel(lookuptable_1_out), .out_0(Out_0), .out_1(Out_1), .out_2(Out_2), .out_3(Out_3), .out_4(Out_4),
    .out_5(Out_5), .out_6(Out_6), .out_7(Out_7));  // open: out_8, out_9, out_10, out_11, out_12, out_13, out_14, out_15

  // Other names for the same wires on the sheet: w0 = Addr_csr[0]; w1 = Addr_csr[1]; w2 = Addr_csr[2];
  //   w3 = Addr_csr[3]; w4 = Addr_csr[4]; w5 = Addr_csr[5]; w6 = Addr_csr[6]; w7 = Addr_csr[7]; w8 = Addr_csr[8];
  //   w9 = Addr_csr[9]; w10 = Addr_csr[10]; w11 = Addr_csr[11]; wen0 = Out_0; wen1 = Out_1; wen2 = Out_2;
  //   wen3 = Out_3; wen4 = Out_4; wen5 = Out_5; wen6 = Out_6; wen7 = Out_7

  // Notes on the sheet:
  //   contents of lookuptable_1 (hex, n*v repeats v):
  //   768*0,1,0,0,0,2,3,59*0,4,5,6,7
endmodule
