// Digital circuit csr.dig as structural Verilog
module csr (
  input  [5:0] CSRCode_in,
  input  [31:0] Data_in,
  input  [11:0] Csr_Addr,
  input  [4:0] Imm5_in,
  input  Clock,
  input  [31:0] Data_temp,
  output En,
  output [11:0] Addr_csr,
  output [31:0] Out_rd,
  output [31:0] Out_csr
);

  wire [31:0] and_1_out, and_2_out, not_1_out, not_2_out, or_2_out, or_3_out, out_temp_q;

  or or_1 (En, CSRCode_in[0], CSRCode_in[1], CSRCode_in[2], CSRCode_in[3], CSRCode_in[4], CSRCode_in[5]);
  assign Out_csr = CSRCode_in[0] ? Data_in : 32'bz;  // Driver driver_1
  assign or_2_out = Data_in | Out_rd;  // Or or_2, 32 bits wide
  assign not_1_out = ~Data_in;  // Not not_1, 32 bits wide
  assign and_1_out = not_1_out & Out_rd;  // And and_1, 32 bits wide
  assign Out_csr = CSRCode_in[1] ? or_2_out : 32'bz;  // Driver driver_2
  assign Out_csr = CSRCode_in[2] ? and_1_out : 32'bz;  // Driver driver_3
  assign Out_csr = CSRCode_in[3] ? {{27{1'b0}}, Imm5_in} : 32'bz;  // Driver driver_4
  assign or_3_out = {{27{1'b0}}, Imm5_in} | Out_rd;  // Or or_3, 32 bits wide
  assign and_2_out = not_2_out & Out_rd;  // And and_2, 32 bits wide
  assign not_2_out = ~{{27{1'b0}}, Imm5_in};  // Not not_2, 32 bits wide
  assign Out_csr = CSRCode_in[4] ? or_3_out : 32'bz;  // Driver driver_5
  assign Out_csr = CSRCode_in[5] ? and_2_out : 32'bz;  // Driver driver_6
  assign Addr_csr = En ? Csr_Addr : 12'bz;  // Driver driver_7
  Register #(.Bits(32)) out_temp (.D(Data_temp), .C(Clock), .en(1'b1), .Q(out_temp_q));
  PullDown pulldown_1 (.out(En));
  assign Out_rd = En ? out_temp_q : 32'bz;  // Driver driver_8
  PullDown #(.Bits(32)) pulldown_2 (.out(Out_rd));

  // Other names for the same wires on the sheet: addr[11:0] = Csr_Addr; c = Clock; csr_en = En; csrrw = CSRCode_in[0];
  //   csrrs = CSRCode_in[1]; csrrc = CSRCode_in[2]; csrrwi = CSRCode_in[3]; csrrsi = CSRCode_in[4];
  //   csrrci = CSRCode_in[5]; data_out[31:0] = Out_rd; data_w[31:0] = Out_csr; imm_in[4:0] = Imm5_in
endmodule
