// Digital circuit cust_ctrl.dig as structural Verilog
module cust_ctrl (
  input  [31:0] op_code,
  input  cust_code,
  input  Clock,
  output PC_init
);

  wire [10:0] register_1_q;
  wire [31:0] driver_1_out;

  assign driver_1_out = cust_code ? op_code : 32'bz;  // Driver driver_1
  Register #(.Bits(12)) register_1 (.D(driver_1_out[31:20]), .C(Clock), .en(cust_code), .Q({PC_init, register_1_q}));
endmodule
