// Digital circuit i2c-master-readdata.dig as structural Verilog
module i2c_master_readdata (
  input  en,
  input  Clock,
  input  SDA_in,
  output SDA,
  output status,
  output [7:0] Data_out
);

  wire bit0, bit1, bit2, bit3, bit4, bit5, bit6, bit7, counter_1_ovf, d_statusen, first, master_s0,
       master_s1, master_s3, or_1_out, s_ack, s_end;
  wire [1:0] m_status;
  wire [2:0] bit_pos;
  wire [7:0] byte_in, multiplexer_1_out;

  assign byte_in = first ? {8{1'b0}} : 8'bz;  // Driver driver_1
  Decoder #(.Selector_Bits(3)) decoder_1 (
    .sel(bit_pos), .out_0(bit7), .out_1(bit6), .out_2(bit5), .out_3(bit4), .out_4(bit3), .out_5(bit2),
    .out_6(bit1), .out_7(bit0));
  Multiplexer multiplexer_1 (.sel(bit0), .in_0(Data_out[0]), .in_1(SDA_in), .out(multiplexer_1_out[0]));
  Multiplexer multiplexer_2 (.sel(bit1), .in_0(Data_out[1]), .in_1(SDA_in), .out(multiplexer_1_out[1]));
  Multiplexer multiplexer_3 (.sel(bit2), .in_0(Data_out[2]), .in_1(SDA_in), .out(multiplexer_1_out[2]));
  Multiplexer multiplexer_4 (.sel(bit3), .in_0(Data_out[3]), .in_1(SDA_in), .out(multiplexer_1_out[3]));
  Multiplexer multiplexer_5 (.sel(bit4), .in_0(Data_out[4]), .in_1(SDA_in), .out(multiplexer_1_out[4]));
  Multiplexer multiplexer_6 (.sel(bit5), .in_0(Data_out[5]), .in_1(SDA_in), .out(multiplexer_1_out[5]));
  Multiplexer multiplexer_7 (.sel(bit6), .in_0(Data_out[6]), .in_1(SDA_in), .out(multiplexer_1_out[6]));
  Multiplexer multiplexer_8 (.sel(bit7), .in_0(Data_out[7]), .in_1(SDA_in), .out(multiplexer_1_out[7]));
  _4_status_mechine _4_status_mechine_1 (
    .Clock(Clock), .nexten_0(en), .nexten_1(s_end), .nexten_2(1'b1), .nexten_3(1'b1),
    .direct_statusen(d_statusen), .direct_status(2'b00), .falling_edge_status(4'b0001), .Status_cur(m_status));
  assign byte_in = master_s1 ? multiplexer_1_out : 8'bz;  // Driver driver_2
  Counter counter_1 (.en(status), .C(Clock), .clr(first), .ovf(counter_1_ovf));  // open: out
  Decoder #(.Selector_Bits(2)) decoder_2 (
    .sel(m_status), .out_0(master_s0), .out_1(master_s1), .out_2(d_statusen), .out_3(master_s3));
  assign SDA = s_ack ? 1'b0 : 1'bz;  // Driver driver_3
  or or_1 (or_1_out, master_s1, first);
  RS_FF_AS rs_ff_as_1 (.S(master_s1), .R(counter_1_ovf), .nQ(first));  // open: Q
  Counter #(.Bits(3)) counter_2 (.en(1'b1), .C(~Clock), .clr(~master_s1), .out(bit_pos), .ovf(s_end));
  Register #(.Bits(8)) register_1 (.D(byte_in), .C(Clock), .en(or_1_out), .Q(Data_out));
  assign status = ~first ? master_s0 : 1'bz;  // DriverInvSel driverinvsel_1
  D_FF d_ff_1 (.D(s_end), .C(~Clock), .Q(s_ack));  // open: nQ
  PullDown pulldown_1 (.out(status));

  // Other names for the same wires on the sheet: byte_out[7:0] = Data_out; end = status; master_s2 = d_statusen;
  //   on_off = en; scl = Clock

  // Notes on the sheet:
  //   s0: wait start
  //   s1: readdata
  //   s2: send ack
endmodule
