// Digital circuit i2c-master-senddata.dig as structural Verilog
module i2c_master_senddata (
  input  [7:0] Data_in,
  input  en,
  input  Clock,
  input  SDA_in,
  output SDA,
  output status,
  output ack
);

  wire and_1_out, and_2_out, bitselector_1_out, counter_2_ovf, d_statusen, first, master_s0, master_s1,
       master_s3, or_1_out, or_2_out, or_3_out, register_1_q, s_end, s_endtmp;
  wire [1:0] m_status;
  wire [2:0] bit_pos, d_ff_1_q, sub_1_s;

  _4_status_mechine _4_status_mechine_1 (
    .Clock(Clock), .nexten_0(en), .nexten_1(s_end), .nexten_2(1'b1), .nexten_3(1'b1),
    .direct_statusen(d_statusen), .direct_status(2'b00), .falling_edge_status(4'b0101), .Status_cur(m_status));
  Counter #(.Bits(3)) counter_1 (.en(1'b1), .C(Clock), .clr(~master_s1), .out(bit_pos), .ovf(s_endtmp));
  Register register_1 (.D(s_endtmp), .C(Clock), .en(1'b1), .Q(register_1_q));
  Counter #(.Bits(2)) counter_2 (.en(status), .C(Clock), .clr(first), .ovf(counter_2_ovf));  // open: out
  Decoder #(.Selector_Bits(2)) decoder_1 (
    .sel(m_status), .out_0(master_s0), .out_1(master_s1), .out_2(d_statusen), .out_3(master_s3));
  Register register_2 (.D(register_1_q), .C(~Clock), .en(1'b1), .Q(s_end));
  RS_FF_AS rs_ff_as_1 (.S(master_s1), .R(counter_2_ovf), .nQ(first));  // open: Q
  Sub #(.Bits(3)) sub_1 (.a(3'b111), .b(bit_pos), .c_i(1'b0), .s(sub_1_s));  // open: c_o
  or or_1 (or_1_out, en, first);
  or or_2 (or_2_out, master_s0, ack);
  and and_1 (and_1_out, ~s_end, master_s1);  // And
  D_FF #(.Bits(3)) d_ff_1 (.D(sub_1_s), .C(~Clock), .Q(d_ff_1_q));  // open: nQ
  assign status = ~or_1_out ? or_2_out : 1'bz;  // DriverInvSel driverinvsel_1
  BitSelector #(.Selector_Bits(3)) bitselector_1 (.in(Data_in), .sel(d_ff_1_q), .out(bitselector_1_out));
  assign SDA = and_1_out ? bitselector_1_out : 1'bz;  // Driver driver_1
  PullUp #(.Bits(3)) pullup_1 (.out(d_ff_1_q));
  and and_2 (and_2_out, s_end, ~SDA_in);  // And
  or or_3 (or_3_out, s_end, first);
  Register register_3 (.D(and_2_out), .C(Clock), .en(or_3_out), .Q(ack));
  PullDown pulldown_1 (.out(status));

  // Other names for the same wires on the sheet: end = status; master_s2 = d_statusen; on_off = en; scl = Clock;
  //   send_byte[7:0] = Data_in

  // Notes on the sheet:
  //   s0: wait start
  //   s1: send data
  //   s2: wait ack
endmodule
