// Digital circuit i2c-master.dig as structural Verilog
module i2c_master (
  input  [6:0] Dev_addr,
  input  [7:0] mem_addr,
  input  RW,
  input  on_off,
  input  SDA_in,
  input  [7:0] Data_in,
  input  Clock,
  output SCL,
  output SDA,
  output Out_en,
  output [7:0] Data_out,
  output status,
  output NACK,
  output [1:0] stat
);

  wire ack_1, ack_2, ack_3, and_1_out, and_2_out, and_3_out, and_4_out, and_5_out, and_6_out, and_7_out,
       dstatus_en, slave_s1, slave_s2, slave_s3, to_s0, to_s2, to_s3;
  wire [1:0] dstatus;

  Counter counter_1 (.en(1'b1), .C(Clock), .clr(1'b0), .ovf(SCL));  // open: out
  _4_status_mechine _4_status_mechine_1 (
    .Clock(SCL), .nexten_0(on_off), .nexten_1(to_s2), .nexten_2(to_s3), .nexten_3(to_s0),
    .direct_statusen(dstatus_en), .direct_status(dstatus), .falling_edge_status(4'b0000), .Status_cur(stat));
  and and_1 (and_1_out, status, on_off);
  and and_2 (and_2_out, ~ack_1, to_s2);  // And
  and and_3 (and_3_out, RW, Out_en);
  and and_4 (and_4_out, ~ack_2, to_s3);  // And
  i2c_master_startandaddr S1 (
    .Clock(SCL), .start(and_1_out), .RW(RW), .Dev_addr(Dev_addr), .SDA_in(SDA_in), .Clock_Src(Clock),
    .SDA(SDA), .ack(ack_1), .status(to_s2));
  or or_1 (dstatus_en, and_2_out, and_3_out, and_4_out);
  Decoder #(.Selector_Bits(2)) decoder_1 (
    .sel(stat), .out_0(status), .out_1(slave_s1), .out_2(slave_s2), .out_3(slave_s3));
  assign dstatus = dstatus_en ? 2'b00 : 2'bz;  // Driver driver_1
  assign SDA = dstatus_en ? 1'b0 : 1'bz;  // Driver driver_2
  and and_5 (and_5_out, to_s2, RW);
  and and_6 (and_6_out, to_s2, ~RW);  // And
  and and_7 (and_7_out, to_s3, ~RW);  // And
  i2c_master_readdata S2 (
    .en(and_5_out), .Clock(SCL), .SDA_in(SDA_in), .SDA(SDA), .status(Out_en), .Data_out(Data_out));
  i2c_master_senddata S2_2 (
    .Data_in(mem_addr), .en(and_6_out), .Clock(SCL), .SDA_in(SDA_in), .SDA(SDA), .status(to_s3), .ack(ack_2));
  i2c_master_senddata S3 (
    .Data_in(Data_in), .en(and_7_out), .Clock(SCL), .SDA_in(SDA_in), .SDA(SDA), .status(to_s0), .ack(ack_3));
  not not_1 (NACK, ack_1);

  // Other names for the same wires on the sheet: c = Clock; I2C_status[1:0] = stat; slave_s0 = status

  // Notes on the sheet:
  //   Clock: Hz: 2
  //   s0: wait start
  //   s1: send dev address
  //   s2: send write mem address or read data
  //   s3: send write data
endmodule
