// Digital circuit i2c-random.dig as structural Verilog
module i2c_random (
  input  SDA,
  input  SCL,
  input  [6:0] Dev_address,
  output SDA_out,
  output [7:0] \rand 
);

  wire en_max, en_min, Out_en;
  wire [7:0] Addr_out, area, Data_out, max, min, Out_rand, rand_base, src_rand;

  Register #(.Bits(8)) u_min (.D(Data_out), .C(SCL), .en(en_min), .Q(min));
  Comparator #(.Bits(8)) comparator_1 (.a(Addr_out), .b(8'h1), .eq(en_min));  // open: gt, lt
  Comparator #(.Bits(8)) comparator_2 (.a(Addr_out), .b(8'h2), .eq(en_max));  // open: gt, lt
  Register #(.Bits(8)) u_max (.D(Data_out), .C(SCL), .en(en_max), .Q(max));
  PRNG #(.Bits(8)) prng_1 (.S(8'h1), .se(1'b0), .ne(1'b1), .C(SCL), .R(src_rand));
  Sub #(.Bits(8)) sub_1 (.a(max), .b(min), .c_i(1'b0), .s(area));  // open: c_o
  i2c_slave i2c_slave_1 (
    .SCL(SCL), .SDA(SDA), .Address(Dev_address), .Data_in(Out_rand), .SDA_out(SDA_out), .Out_en(Out_en),
    .Data_out(Data_out), .Addr_out(Addr_out));
  Div #(.Bits(8)) div_1 (.a(src_rand), .b(area), .r(rand_base));  // open: q
  Add #(.Bits(8)) add_1 (.a(min), .b(rand_base), .c_i(1'b0), .s(Out_rand));  // open: c_o
  assign \rand  = ~SDA_out ? Out_rand : 8'bz;  // DriverInvSel driverinvsel_1

  // Other names for the same wires on the sheet: dev_addr[6:0] = Dev_address; sda_in = SDA

  // Notes on the sheet:
  //   SCL: Hz: 50
endmodule
