// Digital circuit led_waiter_ctrl.dig as structural Verilog
module led_waiter_ctrl (
  input  CLK
);

  wire c_r, counter_rst, not_1_out, rst_status;
  wire [2:0] Led_status_in, Led_status_out;
  wire [15:0] Counter_in, Counter_out;

  Reset rst_n (.out(rst_status));
  assign Counter_in = ~rst_status ? {16{1'b0}} : 16'bz;  // DriverInvSel driverinvsel_1
  not not_1 (not_1_out, rst_status);
  or or_1 (c_r, not_1_out, CLK);
  assign Led_status_in = ~rst_status ? 3'b001 : 3'bz;  // DriverInvSel driverinvsel_2
  Register #(.Bits(3)) Led_status (.D(Led_status_in), .C(c_r), .en(1'b1), .Q(Led_status_out));
  Counter #(.Bits(16)) counter_1 (.en(rst_status), .C(CLK), .clr(counter_rst), .out(Counter_in));  // open: ovf
  Comparator #(.Bits(16)) comparator_1 (.a(Counter_out), .b(16'hc34f), .eq(counter_rst));  // open: gt, lt
  assign Led_status_in = counter_rst ? {Led_status_out[1:0], Led_status_out[2]} : 3'bz;  // Driver driver_1
  Register #(.Bits(16)) Counter_2 (.D(Counter_in), .C(c_r), .en(1'b1), .Q(Counter_out));
  assign Led_status_in = ~counter_rst ? Led_status_out : 3'bz;  // DriverInvSel driverinvsel_3
  LED LED1 (.in(Led_status_out[0]));
  LED LED2 (.in(Led_status_out[1]));
  LED LED3 (.in(Led_status_out[2]));

  // Notes on the sheet:
  //   CLK: Hz: 50000
endmodule
