// Digital circuit uart-term.dig as structural Verilog
module uart_term (
  input  RX,
  input  UartClock,
  output TX
);

  wire comparator_1_eq, en_input, en_output, en_send, keyboard_1_av, read_en, read_ready, wait_input,
       writeable;
  wire [7:0] input_byte, read_byte;
  wire [15:8] keyboard_1_d;

  Comparator #(.Bits(8)) comparator_1 (.a(read_byte), .b({8{1'b1}}), .eq(comparator_1_eq));  // open: gt, lt
  assign read_en = UartClock ? read_ready : 1'bz;  // Driver driver_1
  Register register_1 (.D(comparator_1_eq), .C(UartClock), .en(read_ready), .Q(wait_input));
  and and_1 (en_output, read_ready, ~comparator_1_eq);  // And
  and and_2 (en_input, wait_input, ~en_output, writeable);  // And
  Terminal terminal_1 (.D(read_byte), .C(UartClock), .en(en_output));
  Keyboard keyboard_1 (.C(UartClock), .en(1'b1), .D({keyboard_1_d, input_byte}), .av(keyboard_1_av));
  PullUp pullup_1 (.out(read_en));
  and and_3 (en_send, keyboard_1_av, en_input);
  uart_ttl uart_ttl_1 (
    .InnerClock(UartClock), .Clock(UartClock), .read_en(read_en), .Data_in(input_byte), .write_en(en_send),
    .RX(RX), .TX(TX), .Read_out(read_byte), .Read_ready(read_ready), .Writeable(writeable));

  // Other names for the same wires on the sheet: read_bit = RX; uart_clock = UartClock

  // Notes on the sheet:
  //   UartClock: Hz: 50
endmodule
