// Digital circuit zero-register.dig as structural Verilog
module zero_register (
  input  [31:0] D,
  input  OE_p1,
  input  OE_P2,
  input  OE_P3,
  output [31:0] OutPut_P1,
  output [31:0] OutPut_P2,
  output [31:0] OutPut_P3
);

  assign OutPut_P1 = OE_p1 ? {32{1'b0}} : 32'bz;  // Driver driver_1
  assign OutPut_P2 = OE_P2 ? {32{1'b0}} : 32'bz;  // Driver driver_2
  assign OutPut_P3 = OE_P3 ? {32{1'b0}} : 32'bz;  // Driver driver_3
endmodule
