// Digital circuit risc-v-computer - 副本.dig as structural Verilog
module \risc_v_computer___副本  (
  input  in_2,
  output [31:0] out_1,
  output [31:0] out_3,
  output [31:0] out_4
);

  wire and_1_out, and_2_out, c, Invalid_op, rd_en;
  wire [4:0] driver_1_out, rd, rs1, rs2;
  wire [11:0] imm_12;
  wire [18:0] alu_op;
  wire [31:0] instruction_code, rd_out, rs1_data, rs2_data;

  Button button_1 (.out(c));
  // Program_Counter program_counter_1: pin names not known; wires that end beside it: 32'h80000000, 1'b1, c, 32'h1, 1'b0, in_2, out_4
  Instruction_decoder instruction_decoder_1 (
    .Instruction_In(out_1), .rd(rd), .rs1(rs1), .rs2(rs2), .imm_2032(imm_12), .invalid(Invalid_op),
    .alu_op(alu_op));  // open: mechie_op, imm_2531, imm_1231, csr_op, jmp_op, SL_op, Cust_op
  Register #(.Bits(32)) Instrction_Reg (.D(instruction_code), .C(c), .en(1'b1), .Q(out_1));
  LED led_1 (.in(Invalid_op));
  alu alu_1 (
    .Alu_in(alu_op), .rs1_in(rs1_data), .rs2_in(rs2_data), .Imm12_in(imm_12), .rd_out(rd_out),
    .EN_out(rd_en), .InvlidOP_out(Invalid_op));
  ROM #(.AddrBits(8), .Bits(32)) bootloader_rom (.A(out_4[7:0]), .sel(and_1_out), .D(instruction_code));
  and and_1 (and_1_out, out_4[31], 1'b1);
  assign driver_1_out = rd_en ? rd : 5'bz;  // Driver driver_1
  EEPROMDualPort #(.AddrBits(24), .Bits(32)) kernel_rom (
    .A(out_4[23:0]), .Din(32'h1), .str(1'b0), .C(c), .ld(and_2_out), .D(instruction_code));
  risc_v_registers risc_v_registers_1 (
    .OE_P1(rs1), .Din(rd_out), .Clock(c), .WE(driver_1_out), .OE_P2(rs2), .OE_P3(rd), .Output_P1(rs1_data),
    .Output_P2(rs2_data), .Output_P3(out_3));
  and and_2 (and_2_out, out_4[30], 1'b1);
  // also tied to GND on the sheet: in_2

  // Other names for the same wires on the sheet: addr_real[23:0] = out_4[23:0]; PC_addr[31:0] = out_4;
  //   addrflag_eeprom = out_4[30]; addrflag_boot = out_4[31]; PC_code[31:0] = out_1; reset = in_2

  // Notes on the sheet:
  //   contents of bootloader_rom (hex, n*v repeats v):
  //   200001001009
endmodule
