// Digital circuit risc-v-computer.dig as structural Verilog
module risc_v_computer (
  output [31:0] out_1,
  output [31:0] out_2,
  output [31:0] out_3,
  output [31:0] _3,
  output [4:0] out_5,
  output [4:0] out_6,
  output [4:0] out_7,
  output [31:0] out_8,
  output [31:0] out_9,
  output [31:0] out_10,
  output [11:0] out_11
);

  wire and_1_out, and_2_out, c, Cust_op, Invalid_op, nor_1_out, not_1_out, Oe_mem, PC_inited, PC_jmp, rd_en,
       We_mem;
  wire [3:0] storebytes_size;
  wire [4:0] driver_5_out;
  wire [5:0] csr_op;
  wire [6:0] imm_7;
  wire [8:0] jmp_op, mem_op;
  wire [18:0] alu_op;
  wire [19:0] imm_20;
  wire [31:0] Addr_jmp, data_mem, data_memrd, Instrction_Reg_q, mem_addr, program_counter_1_pc_next;

  Button button_1 (.out(c));
  not not_1 (not_1_out, PC_inited);
  assign out_3 = not_1_out ? 32'h80000000 : 32'bz;  // Driver driver_1
  j_alu j_alu_1 (
    .jmp_op(jmp_op), .PC_cur(out_3), .PC_next(out_2), .rs1_in(out_9), .rs2_in(out_10), .Imm12_in(out_11),
    .Imm20_in(imm_20), .Imm7_in(imm_7), .offset_5(out_5), .Addr_jmp(Addr_jmp), .rd_out(out_8),
    .EN_out(rd_en), .En_jmp(PC_jmp));
  Program_Counter program_counter_1 (
    .En(1'b1), .Clock(c), .Addr_set(out_3), .Addr_jmp(Addr_jmp), .En_jmp(PC_jmp),
    .PC_next(program_counter_1_pc_next));
  assign out_2 = not_1_out ? 32'h80000004 : 32'bz;  // Driver driver_2
  assign out_2 = PC_inited ? program_counter_1_pc_next : 32'bz;  // Driver driver_3
  Instruction_decoder instruction_decoder_1 (
    .Instruction_In(_3), .rd(out_5), .rs1(out_6), .rs2(out_7), .imm_2531(imm_7), .imm_1231(imm_20),
    .imm_2032(out_11), .invalid(Invalid_op), .csr_op(csr_op), .jmp_op(jmp_op), .alu_op(alu_op),
    .SL_op(mem_op), .Cust_op(Cust_op));  // open: mechie_op
  LED led_1 (.in(Invalid_op));
  Register #(.Bits(32)) Instrction_Reg (.D(out_2), .C(c), .en(1'b1), .Q(Instrction_Reg_q));
  assign out_3 = PC_inited ? Instrction_Reg_q : 32'bz;  // Driver driver_4
  alu alu_1 (
    .Alu_in(alu_op), .rs1_in(out_9), .rs2_in(out_10), .Imm12_in(out_11), .rd_out(out_8), .EN_out(rd_en),
    .InvlidOP_out(Invalid_op));
  cust_ctrl cust_ctrl_1 (.op_code(_3), .cust_code(Cust_op), .Clock(c), .PC_init(PC_inited));
  assign driver_5_out = rd_en ? out_5 : 5'bz;  // Driver driver_5
  csr_alu csr_alu_1 (
    .CSRCode_in(csr_op), .Data_in(out_9), .Csr_Addr(out_11), .Imm5_in(out_6), .Clock(c), .Out_rd(out_8),
    .En_rd(rd_en));  // open: ddata
  risc_v_registers risc_v_registers_1 (
    .OE_P1(out_6), .Din(out_8), .Clock(c), .WE(driver_5_out), .OE_P2(out_7), .OE_P3(out_5),
    .Output_P1(out_9), .Output_P2(out_10), .Output_P3(out_1));
  ROM #(.AddrBits(8), .Bits(32)) bootloader_rom (.A(out_3[7:0]), .sel(and_1_out), .D(_3));
  and and_1 (and_1_out, out_3[31], 1'b1);
  nor nor_1 (nor_1_out, out_3[30], out_3[31]);
  ls_alu ls_alu_1 (
    .MemOp_in(mem_op), .Data_in(data_memrd), .rs1(out_9), .Offset_12(out_11), .Offset_7(imm_7),
    .Offset_5(out_5), .imm_20(imm_20), .rs2(out_10), .Addr_out(mem_addr), .RegWE_out(rd_en),
    .StoreByteSize_out(storebytes_size), .rd_out(out_8), .oe_out(Oe_mem), .we_out(We_mem), .Mem_out(data_mem));
  EEPROMDualPort #(.AddrBits(24), .Bits(32)) kernel_rom (
    .A(out_3[23:0]), .Din(32'h1), .str(1'b0), .C(c), .ld(and_2_out), .D(_3));
  and and_2 (and_2_out, out_3[30], 1'b1);
  memory memory_1 (
    .Addr(mem_addr), .Data_in(data_mem), .WE(We_mem), .OE(Oe_mem), .ByteSize_in(storebytes_size), .Clock(c),
    .Addr_PC(out_3), .OE_PC(nor_1_out), .Data_out(data_memrd), .DataPC_out(_3));

  // Other names for the same wires on the sheet: imm_12[11:0] = out_11; instruction_code[31:0] = _3;
  //   addr_real[23:0] = out_3[23:0]; PC_exec[31:0] = out_3; addrflag_eeprom = out_3[30]; addrflag_boot = out_3[31];
  //   PC_next[31:0] = out_2; rd[4:0] = out_5; rd_out[31:0] = out_8; rs1[4:0] = out_6; rs1_data[31:0] = out_9;
  //   rs2[4:0] = out_7; rs2_data[31:0] = out_10

  // Notes on the sheet:
  //   contents of bootloader_rom (hex, n*v repeats v):
  //   8000007f,0,0,0,4008113
endmodule
