// Digital circuit risc-v-registers.dig as structural Verilog
module risc_v_registers (
  input  [4:0] OE_P1,
  input  [31:0] Din,
  input  Clock,
  input  [4:0] WE,
  input  [4:0] OE_P2,
  input  [4:0] OE_P3,
  output [31:0] Output_P1,
  output [31:0] Output_P2,
  output [31:0] Output_P3
);

  wire OE0, OE0_P2, OE0_P3, OE1, OE1_P2, OE1_P3, OE2, OE2_P2, OE2_P3, OE3, OE3_P2, OE3_P3, OE4, OE4_P2,
       OE4_P3, OE5, OE5_P2, OE5_P3, OE6, OE6_P2, OE6_P3, OE7, OE7_P2, OE7_P3, OE8, OE8_P2, OE8_P3, OE9,
       OE9_P2, OE9_P3, OE10, OE10_P2, OE10_P3, OE11, OE11_P2, OE11_P3, OE12, OE12_P2, OE12_P3, OE13, OE13_P2,
       OE13_P3, OE14, OE14_P2, OE14_P3, OE15, OE15_P2, OE15_P3, OE16, OE16_P2, OE16_P3, OE17, OE17_P2,
       OE17_P3, OE18, OE18_P2, OE18_P3, OE19, OE19_P2, OE19_P3, OE20, OE20_P2, OE20_P3, OE21, OE21_P2,
       OE21_P3, OE22, OE22_P2, OE22_P3, OE23, OE23_P2, OE23_P3, OE24, OE24_P2, OE24_P3, OE25, OE25_P2,
       OE25_P3, OE26, OE26_P2, OE26_P3, OE27, OE27_P2, OE27_P3, OE28, OE28_P2, OE28_P3, OE29, OE29_P2,
       OE29_P3, OE30, OE30_P2, OE30_P3, WE0, WE1, WE2, WE3, WE4, WE5, WE6, WE7, WE8, WE9, WE10, WE11, WE12,
       WE13, WE14, WE15, WE16, WE17, WE18, WE19, WE20, WE21, WE22, WE23, WE24, WE25, WE26, WE27, WE28, WE29,
       WE30;

  LookUpTable #(.Bits(31)) lookuptable_1 (
    .in0(OE_P3[0]), .in1(OE_P3[1]), .in2(OE_P3[2]), .in3(OE_P3[3]), .in4(OE_P3[4]),
    .out({OE30_P3, OE29_P3, OE28_P3, OE27_P3, OE26_P3, OE25_P3, OE24_P3, OE23_P3, OE22_P3, OE21_P3, OE20_P3, OE19_P3, OE18_P3, OE17_P3, OE16_P3, OE15_P3, OE14_P3, OE13_P3, OE12_P3, OE11_P3, OE10_P3, OE9_P3, OE8_P3, OE7_P3, OE6_P3, OE5_P3, OE4_P3, OE3_P3, OE2_P3, OE1_P3, OE0_P3}));
  LookUpTable #(.Bits(31)) lookuptable_2 (
    .in0(WE[0]), .in1(WE[1]), .in2(WE[2]), .in3(WE[3]), .in4(WE[4]),
    .out({WE30, WE29, WE28, WE27, WE26, WE25, WE24, WE23, WE22, WE21, WE20, WE19, WE18, WE17, WE16, WE15, WE14, WE13, WE12, WE11, WE10, WE9, WE8, WE7, WE6, WE5, WE4, WE3, WE2, WE1, WE0}));
  LookUpTable #(.Bits(31)) lookuptable_3 (
    .in0(OE_P2[0]), .in1(OE_P2[1]), .in2(OE_P2[2]), .in3(OE_P2[3]), .in4(OE_P2[4]),
    .out({OE30_P2, OE29_P2, OE28_P2, OE27_P2, OE26_P2, OE25_P2, OE24_P2, OE23_P2, OE22_P2, OE21_P2, OE20_P2, OE19_P2, OE18_P2, OE17_P2, OE16_P2, OE15_P2, OE14_P2, OE13_P2, OE12_P2, OE11_P2, OE10_P2, OE9_P2, OE8_P2, OE7_P2, OE6_P2, OE5_P2, OE4_P2, OE3_P2, OE2_P2, OE1_P2, OE0_P2}));
  LookUpTable #(.Bits(31)) lookuptable_4 (
    .in0(OE_P1[0]), .in1(OE_P1[1]), .in2(OE_P1[2]), .in3(OE_P1[3]), .in4(OE_P1[4]),
    .out({OE30, OE29, OE28, OE27, OE26, OE25, OE24, OE23, OE22, OE21, OE20, OE19, OE18, OE17, OE16, OE15, OE14, OE13, OE12, OE11, OE10, OE9, OE8, OE7, OE6, OE5, OE4, OE3, OE2, OE1, OE0}));
  _32_bit_register x1___ra (
    .Din(Din), .clock(Clock), .WE(WE1), .OE1(OE1), .OE2(OE1_P2), .OE3(OE1_P3), .Output1(Output_P1),
    .Output2(Output_P2), .Output3(Output_P3));  // open: data
  _32_bit_register x2___sp (
    .Din(Din), .clock(Clock), .WE(WE2), .OE1(OE2), .OE2(OE2_P2), .OE3(OE2_P3), .Output1(Output_P1),
    .Output2(Output_P2), .Output3(Output_P3));  // open: data
  _32_bit_register x3___gp (
    .Din(Din), .clock(Clock), .WE(WE3), .OE1(OE3), .OE2(OE3_P2), .OE3(OE3_P3), .Output1(Output_P1),
    .Output2(Output_P2), .Output3(Output_P3));  // open: data
  _32_bit_register x4___tp (
    .Din(Din), .clock(Clock), .WE(WE4), .OE1(OE4), .OE2(OE4_P2), .OE3(OE4_P3), .Output1(Output_P1),
    .Output2(Output_P2), .Output3(Output_P3));  // open: data
  _32_bit_register x5___t0 (
    .Din(Din), .clock(Clock), .WE(WE5), .OE1(OE5), .OE2(OE5_P2), .OE3(OE5_P3), .Output1(Output_P1),
    .Output2(Output_P2), .Output3(Output_P3));  // open: data
  _32_bit_register x6___t1 (
    .Din(Din), .clock(Clock), .WE(WE6), .OE1(OE6), .OE2(OE6_P2), .OE3(OE6_P3), .Output1(Output_P1),
    .Output2(Output_P2), .Output3(Output_P3));  // open: data
  _32_bit_register x7___t2 (
    .Din(Din), .clock(Clock), .WE(WE7), .OE1(OE7), .OE2(OE7_P2), .OE3(OE7_P3), .Output1(Output_P1),
    .Output2(Output_P2), .Output3(Output_P3));  // open: data
  _32_bit_register x8___s0___fp (
    .Din(Din), .clock(Clock), .WE(WE8), .OE1(OE8), .OE2(OE8_P2), .OE3(OE8_P3), .Output1(Output_P1),
    .Output2(Output_P2), .Output3(Output_P3));  // open: data
  _32_bit_register x9___s1 (
    .Din(Din), .clock(Clock), .WE(WE9), .OE1(OE9), .OE2(OE9_P2), .OE3(OE9_P3), .Output1(Output_P1),
    .Output3(Output_P3));  // open: data, Output2
  _32_bit_register x10___a0 (
    .Din(Din), .clock(Clock), .WE(WE10), .OE1(OE10), .OE2(OE10_P2), .OE3(OE10_P3), .Output1(Output_P1),
    .Output2(Output_P2), .Output3(Output_P3));  // open: data
  _32_bit_register x11___a1 (
    .Din(Din), .clock(Clock), .WE(WE11), .OE1(OE11), .OE2(OE11_P2), .OE3(OE11_P3), .Output1(Output_P1),
    .Output2(Output_P2), .Output3(Output_P3));  // open: data
  _32_bit_register x12___a2 (
    .Din(Din), .clock(Clock), .WE(WE12), .OE1(OE12), .OE2(OE12_P2), .OE3(OE12_P3), .Output1(Output_P1),
    .Output2(Output_P2), .Output3(Output_P3));  // open: data
  zero_register zero_register_1 (
    .D(Din), .OE_p1(OE0), .OE_P2(OE0_P2), .OE_P3(OE0_P3), .OutPut_P1(Output_P1), .OutPut_P2(Output_P2),
    .OutPut_P3(Output_P3));
  _32_bit_register x13___a3 (
    .Din(Din), .clock(Clock), .WE(WE13), .OE1(OE13), .OE2(OE13_P2), .OE3(OE13_P3), .Output1(Output_P1),
    .Output2(Output_P2), .Output3(Output_P3));  // open: data
  _32_bit_register x14___a4 (
    .Din(Din), .clock(Clock), .WE(WE14), .OE1(OE14), .OE2(OE14_P2), .OE3(OE14_P3), .Output1(Output_P1),
    .Output2(Output_P2), .Output3(Output_P3));  // open: data
  _32_bit_register x15___a5 (
    .Din(Din), .clock(Clock), .WE(WE15), .OE1(OE15), .OE2(OE15_P2), .OE3(OE15_P3), .Output1(Output_P1),
    .Output2(Output_P2), .Output3(Output_P3));  // open: data
  _32_bit_register x16___a6 (
    .Din(Din), .clock(Clock), .WE(WE16), .OE1(OE16), .OE2(OE16_P2), .OE3(OE16_P3), .Output1(Output_P1),
    .Output2(Output_P2), .Output3(Output_P3));  // open: data
  _32_bit_register x17___a7 (
    .Din(Din), .clock(Clock), .WE(WE17), .OE1(OE17), .OE2(OE17_P2), .OE3(OE17_P3), .Output1(Output_P1),
    .Output2(Output_P2), .Output3(Output_P3));  // open: data
  _32_bit_register x18___s2 (
    .Din(Din), .clock(Clock), .WE(WE18), .OE1(OE18), .OE2(OE18_P2), .OE3(OE18_P3), .Output1(Output_P1),
    .Output2(Output_P2), .Output3(Output_P3));  // open: data
  _32_bit_register x19___s3 (
    .Din(Din), .clock(Clock), .WE(WE19), .OE1(OE19), .OE2(OE19_P2), .OE3(OE19_P3), .Output1(Output_P1),
    .Output2(Output_P2), .Output3(Output_P3));  // open: data
  _32_bit_register x20___s4 (
    .Din(Din), .clock(Clock), .WE(WE20), .OE1(OE20), .OE2(OE20_P2), .OE3(OE20_P3), .Output1(Output_P1),
    .Output2(Output_P2), .Output3(Output_P3));  // open: data
  _32_bit_register x21___s5 (
    .Din(Din), .clock(Clock), .WE(WE21), .OE1(OE21), .OE2(OE21_P2), .OE3(OE21_P3), .Output1(Output_P1),
    .Output2(Output_P2), .Output3(Output_P3));  // open: data
  _32_bit_register x22___s6 (
    .Din(Din), .clock(Clock), .WE(WE22), .OE1(OE22), .OE2(OE22_P2), .OE3(OE22_P3), .Output1(Output_P1),
    .Output2(Output_P2), .Output3(Output_P3));  // open: data
  _32_bit_register x23___s7 (
    .Din(Din), .clock(Clock), .WE(WE23), .OE1(OE23), .OE2(OE23_P2), .OE3(OE23_P3), .Output1(Output_P1),
    .Output2(Output_P2), .Output3(Output_P3));  // open: data
  _32_bit_register x24___s8 (
    .Din(Din), .clock(Clock), .WE(WE24), .OE1(OE24), .OE2(OE24_P2), .OE3(OE24_P3), .Output1(Output_P1),
    .Output2(Output_P2), .Output3(Output_P3));  // open: data
  _32_bit_register x25___s9 (
    .Din(Din), .clock(Clock), .WE(WE25), .OE1(OE25), .OE2(OE25_P2), .OE3(OE25_P3), .Output1(Output_P1),
    .Output2(Output_P2), .Output3(Output_P3));  // open: data
  _32_bit_register x26___s10 (
    .Din(Din), .clock(Clock), .WE(WE26), .OE1(OE26), .OE2(OE26_P2), .OE3(OE26_P3), .Output1(Output_P1),
    .Output2(Output_P2), .Output3(Output_P3));  // open: data
  _32_bit_register x27___s11 (
    .Din(Din), .clock(Clock), .WE(WE27), .OE1(OE27), .OE2(OE27_P2), .OE3(OE27_P3), .Output1(Output_P1),
    .Output2(Output_P2), .Output3(Output_P3));  // open: data
  _32_bit_register x28___t3 (
    .Din(Din), .clock(Clock), .WE(WE28), .OE1(OE28), .OE2(OE28_P2), .OE3(OE28_P3), .Output1(Output_P1),
    .Output2(Output_P2), .Output3(Output_P3));  // open: data
  _32_bit_register x30___t5 (
    .Din(Din), .clock(Clock), .WE(WE29), .OE1(OE29), .OE2(OE29_P2), .OE3(OE30_P2), .Output1(Output_P1),
    .Output2(Output_P2), .Output3(Output_P3));  // open: data
  _32_bit_register x31___t6 (
    .Din(Din), .clock(Clock), .WE(WE30), .OE1(OE30), .OE2(OE30_P2), .OE3(OE30_P3), .Output1(Output_P1),
    .Output2(Output_P2), .Output3(Output_P3));  // open: data

  // Notes on the sheet:
  //   contents of lookuptable_1 (hex, n*v repeats v):
  //   1,2,4,8,10,20,40,40,100,200,400,800,1000,2000,4000,8000,10000
  //   ,20000,40000,80000,100000,200000,400000,800000,1000000,2000000
  //   ,4000000,8000000,10000000,20000000,40000000,80000000
  //   contents of lookuptable_2 (hex, n*v repeats v):
  //   0,2,4,8,10,20,40,40,100,200,400,800,1000,2000,4000,8000,10000
  //   ,20000,40000,80000,100000,200000,400000,800000,1000000,2000000
  //   ,4000000,8000000,10000000,20000000,40000000,80000000
  //   contents of lookuptable_3 (hex, n*v repeats v):
  //   1,2,4,8,10,20,40,40,100,200,400,800,1000,2000,4000,8000,10000
  //   ,20000,40000,80000,100000,200000,400000,800000,1000000,2000000
  //   ,4000000,8000000,10000000,20000000,40000000,80000000
  //   contents of lookuptable_4 (hex, n*v repeats v):
  //   1,2,4,8,10,20,40,40,100,200,400,800,1000,2000,4000,8000,10000
  //   ,20000,40000,80000,100000,200000,400000,800000,1000000,2000000
  //   ,4000000,8000000,10000000,20000000,40000000,80000000
endmodule
