// Digital circuit 计算机架构.dig as structural Verilog
module \计算机架构  (
  input  clk,
  output [7:0] out_1,
  output [7:0] out_2,
  output [7:0] out_3,
  output [7:0] out_4,
  output [7:0] out_5,
  output [3:0] addr,
  output [7:0] addr_2,
  output [1:0] out_8,
  output [3:0] out_9
);

  wire Addr_OE, Addr_WE, IR_OE, IR_WE, MBR_OE, MBR_WE, Memory_OE, Memory_WE, Output_OE, Output_WE, PC_EN,
       PC_OE, RegA_OE, RegA_WE, RegB_OE, RegB_WE, Sum_OE;
  wire [2:0] counter_1_out;
  wire [3:0] \IR_指令寄存器_output , \地址寄存器_output ;
  wire [7:0] \_8位加法器_1_sum , RegA_output, RegB_output, RegSumOut_output;

  Counter #(.Bits(3)) counter_1 (.en(1'b1), .C(clk), .clr(1'b0), .out(counter_1_out));  // open: ovf
  LookUpTable #(.Bits(17)) lookuptable_1 (
    .in0(counter_1_out[0]), .in1(counter_1_out[1]), .in2(counter_1_out[2]), .in3(addr_2[4]), .in4(addr_2[5]),
    .out({PC_EN, PC_OE, Addr_WE, Addr_OE, IR_WE, IR_OE, Memory_WE, Memory_OE, MBR_WE, MBR_OE, Output_WE, Output_OE, Sum_OE, RegB_WE, RegB_OE, RegA_WE, RegA_OE}));
  Counter #(.Bits(2)) \PC计数器  (.en(PC_EN), .C(clk), .clr(1'b0), .out(out_8));  // open: ovf
  \_8位寄存器  \IR_指令寄存器  (
    .Din(RegSumOut_output), .clock(clk), .WE(IR_WE), .OE(IR_OE), .data(addr_2),
    .Output({out_9, \IR_指令寄存器_output }));
  \_8位寄存器  RegA (.Din(RegSumOut_output), .clock(clk), .WE(RegA_WE), .OE(RegA_OE), .data(out_1), .Output(RegA_output));
  \_8位寄存器  RegB (.Din(RegSumOut_output), .clock(clk), .WE(RegB_WE), .OE(RegB_OE), .data(out_2), .Output(RegB_output));
  assign \IR_指令寄存器_output  = PC_OE ? {2'b00, out_8} : 4'bz;  // Driver driver_1
  \_8位加法器  \_8位加法器_1  (
    .A(RegA_output), .B(RegB_output), .OE(Sum_OE), .C(1'b0), .Sum(\_8位加法器_1_sum ), .data(out_4));  // open: carray
  \_4位寄存器  \u_地址寄存器  (
    .Din(\IR_指令寄存器_output ), .clock(clk), .WE(Addr_WE), .OE(Addr_OE), .data(addr), .Output(\地址寄存器_output ));
  \_8位寄存器  RegSumOut (
    .Din(\_8位加法器_1_sum ), .clock(clk), .WE(Output_WE), .OE(Output_OE), .data(out_5), .Output(RegSumOut_output));
  \_8位寄存器  MBR_RegCache (
    .Din(RegSumOut_output), .clock(clk), .WE(MBR_WE), .OE(MBR_OE), .data(out_3), .Output(RegSumOut_output));
  EEPROMDualPort #(.AddrBits(4), .Bits(8)) \u_模拟内存1  (
    .A(\地址寄存器_output ), .Din(RegSumOut_output), .str(Memory_WE), .C(clk), .ld(Memory_OE), .D(RegSumOut_output));

  // Other names for the same wires on the sheet: clock = clk

  // Notes on the sheet:
  //   clk: Hz: 50
  //   contents of lookuptable_1 (hex, n*v repeats v):
  //   1c000,3200,4800,2300,82,0,0,0,1c000,3200,4800,2300,88,0,0,0,1c000
  //   ,3200,4800,55,120,0,0,0,1c000,3200,4800,2480
  //   内部数据总线
  //   外部数据总线
  //   contents of 模拟内存1 (hex, n*v repeats v):
  //   f,1e,20,3f,10*0,5,92
endmodule
